// Logisim project 1选4数据选择器.circ as structural Verilog: 1 circuit, main circuit main
module main (
  input  D,
  input  A0,
  input  A1,
  output Y0,
  output Y1,
  output Y2,
  output Y3
);

  wire and_1_out, and_2_out, and_3_out, and_4_out, not_1_out, not_2_out, not_3_out, not_4_out;

  not not_1 (not_1_out, A1);
  not not_2 (not_2_out, A0);
  not not_3 (not_3_out, A1);
  not not_4 (not_4_out, A0);
  and and_1 (and_1_out, A1, A0);
  and and_2 (and_2_out, not_1_out, not_2_out);
  and and_3 (and_3_out, not_3_out, A0);
  and and_4 (and_4_out, A1, not_4_out);
  and and_5 (Y3, and_1_out, D);
  and and_6 (Y0, and_2_out, D);
  and and_7 (Y1, and_3_out, D);
  and and_8 (Y2, and_4_out, D);
endmodule
