// Logisim project 2031加密电路.circ as structural Verilog: 1 circuit, main circuit main
module main (
  input  D3,
  input  D2,
  input  D1,
  input  D0,
  output D3_2,
  output D2_2,
  output D1_2,
  output D0_2
);


  assign D0_2 = D1;
  assign D1_2 = D3;
  assign D2_2 = D0;
  assign D3_2 = D2;
endmodule
