// Logisim project 4选1数据选择器.circ as structural Verilog: 1 circuit, main circuit main
module main (
  input  D0,
  input  D1,
  input  D2,
  input  D3,
  input  A1,
  input  A0,
  output Y
);

  wire and_1_out, and_2_out, and_3_out, and_4_out, and_5_out, and_6_out, and_7_out, and_8_out, not_1_out,
       not_2_out, not_3_out, not_4_out, or_1_out, or_2_out;

  not not_1 (not_1_out, A1);
  not not_2 (not_2_out, A0);
  not not_3 (not_3_out, A1);
  not not_4 (not_4_out, A0);
  and and_1 (and_1_out, not_1_out, not_2_out);
  and and_2 (and_2_out, not_3_out, A0);
  and and_3 (and_3_out, A1, not_4_out);
  and and_4 (and_4_out, A1, A0);
  and and_5 (and_5_out, and_1_out, D0);
  and and_6 (and_6_out, and_2_out, D1);
  and and_7 (and_7_out, and_3_out, D2);
  and and_8 (and_8_out, and_4_out, D3);
  or or_1 (or_1_out, and_5_out, and_6_out);
  or or_2 (or_2_out, and_7_out, and_8_out);
  or or_3 (Y, or_1_out, or_2_out);
endmodule
