// Logisim project _alu_benchmarkV4.0.circ as structural Verilog: 4 circuits, main circuit main
module main (
  output [7:0] Test_num,
  output Equal
);

  wire ADD, AND, and_1_out, CF, CF_S, CLK, comparator_2_eq, comparator_3_eq, DIV, \EQ__标志 , EQ_OK, EQ_S,
       Halt, MUL, multiplexer_1_out, NEQ, nHalt, NOR, OF, OF_OK, OR, priority_encoder_1_gs, ROK, SAR, SCMP,
       SLL, SLR, SUB, tunnel, UCMP, UOF_OK, XOR, \与 , \乘法 , \减法 , \加法 , \异或 , \悬空检测 , \或 , \或非 , \无符号比较 ,
       \无符号溢出标志 , \有符号比较 , \有符号溢出标志 , \算术右移 , \逻辑右移 , \逻辑左移 , \除法 ;
  wire [2:2] FLAG_Standard;
  wire [3:0] ALUOP, High, Low, Mid;
  wire [7:0] adder_1_out, \单项评分_1_total , \单项评分_1_扣分 , \单项评分_1_正确条数 , \单项评分_2_total , \单项评分_2_扣分 ,
       \单项评分_2_正确条数 , \单项评分_3_total , \单项评分_3_扣分 , \单项评分_3_正确条数 , \单项评分_4_total , \单项评分_4_扣分 , \单项评分_4_正确条数 ,
       \单项评分_5_total , \单项评分_5_扣分 , \单项评分_5_正确条数 , \单项评分_6_total , \单项评分_6_扣分 , \单项评分_6_正确条数 ,
       \单项评分_7_total , \单项评分_7_扣分 , \单项评分_7_正确条数 , \单项评分_8_total , \单项评分_8_扣分 , \单项评分_8_正确条数 ,
       \单项评分_9_total , \单项评分_9_扣分 , \单项评分_9_正确条数 , \单项评分_10_total , \单项评分_10_扣分 , \单项评分_10_正确条数 ,
       \单项评分_11_total , \单项评分_11_扣分 , \单项评分_11_正确条数 , \单项评分_12_total , \单项评分_12_扣分 , \单项评分_12_正确条数 ,
       \单项评分_13_total , \单项评分_13_扣分 , \单项评分_13_正确条数 , \单项评分_14_total , \单项评分_14_扣分 , \单项评分_14_正确条数 ,
       \单项评分_15_total , \单项评分_15_扣分 , \单项评分_15_正确条数 , \单项评分_16_total , \单项评分_16_扣分 , \单项评分_16_正确条数 ,
       \总评分_1_result ;
  wire [9:0] counter_1_q;
  wire [31:0] bit_extender_1_out, R, R2, R2_Standard, R_Standard, X, Y;

  Clock clock_1 (.out(CLK));
  Register register_1 (.D(adder_1_out), .en(nHalt), .Q(Test_num), .clk(CLK));  // open: clr
  LED \u_测试完成  (.in(Halt));
  Counter #(.width(10), .max('h3ff)) counter_1 (
    .count(NEQ), .Q(counter_1_q), .clk(CLK), .clr(Halt));  // open: load, D, carry
  LED #(.active("false")) led_1 (.in(\逻辑左移 ));
  LED #(.active("false")) led_2 (.in(\逻辑右移 ));
  LED #(.active("false")) led_3 (.in(\EQ__标志 ));
  \单项评分  \u_单项评分_1  (
    .EQ(ROK), .CLK(CLK), .\分值 (5'b00101), .\正确条数 (\单项评分_1_正确条数 ), .\扣分 (\单项评分_1_扣分 ), .ALU_SWITCH(SLL),
    .Total(\单项评分_1_total ), .Right(\逻辑左移 ), .EN(nHalt));
  // Probe on \单项评分_2_total 
  // Probe on \单项评分_1_total 
  // Probe on \单项评分_1_正确条数 
  // Probe on \单项评分_1_扣分 
  Adder adder_1 (.a(8'h1), .b(Test_num), .out(adder_1_out));  // open: cin, cout
  not not_1 (nHalt, Halt);
  Comparator #(.width(4)) comparator_1 (.a(ALUOP), .b(4'b1111), .eq(Halt));  // open: gt, lt
  and and_1 (and_1_out, ~Halt, NEQ);  // AND_Gate
  LED #(.active("false")) led_4 (.in(\算术右移 ));
  LED led_5 (.in(\悬空检测 ));
  \单项评分  \u_单项评分_2  (
    .EQ(ROK), .CLK(CLK), .\分值 (5'b00101), .\正确条数 (\单项评分_2_正确条数 ), .\扣分 (\单项评分_2_扣分 ), .ALU_SWITCH(SAR),
    .Total(\单项评分_2_total ), .Right(\算术右移 ), .EN(nHalt));
  // Probe on \单项评分_3_total 
  // Probe on \单项评分_3_正确条数 
  // Probe on \单项评分_2_正确条数 
  // Probe on \单项评分_2_扣分 
  trace trace_1 (
    .in_1(Test_num), .X(X), .Y(Y), .AluOP(ALUOP), .R(R_Standard), .R2(R2_Standard),
    .FLAGS({FLAG_Standard[2], CF_S, EQ_S}));
  RAM #(.addrWidth(10), .dataWidth(32), .bus("separate")) ram_1 (
    .addr(counter_1_q), .din(X), .str(and_1_out), .clk(CLK));  // open: data, sel, ld, clr
  LED #(.active("false")) led_6 (.in(\与 ));
  LED #(.active("false")) led_7 (.in(\或 ));
  LED #(.active("false")) led_8 (.in(\有符号溢出标志 ));
  \单项评分  \u_单项评分_3  (
    .EQ(ROK), .CLK(CLK), .\分值 (5'b00101), .\正确条数 (\单项评分_3_正确条数 ), .\扣分 (\单项评分_3_扣分 ), .ALU_SWITCH(SLR),
    .Total(\单项评分_3_total ), .Right(\逻辑右移 ), .EN(nHalt));
  // Probe on \单项评分_4_正确条数 
  // Probe on \单项评分_4_正确条数 
  // Probe on \单项评分_3_扣分 
  \单项评分  \u_单项评分_4  (
    .EQ(ROK), .CLK(CLK), .\分值 (5'b00101), .\正确条数 (\单项评分_4_正确条数 ), .\扣分 (\单项评分_4_扣分 ), .ALU_SWITCH(MUL),
    .Total(\单项评分_4_total ), .Right(\乘法 ), .EN(nHalt));
  // Probe on \单项评分_5_total 
  // Probe on \单项评分_5_正确条数 
  // Probe on \单项评分_4_扣分 
  // Probe on \单项评分_5_扣分 
  RAM #(.addrWidth(10), .dataWidth(32), .bus("separate")) ram_2 (
    .addr(counter_1_q), .din(Y), .str(and_1_out), .clk(CLK));  // open: data, sel, ld, clr
  assign bit_extender_1_out = {{28{1'b0}}, ALUOP};  // Bit_Extender bit_extender_1
  LED #(.active("false")) led_9 (.in(\或非 ));
  LED #(.active("false")) led_10 (.in(\异或 ));
  \单项评分  \u_单项评分_5  (
    .EQ(ROK), .CLK(CLK), .\分值 (5'b00101), .\正确条数 (\单项评分_5_正确条数 ), .\扣分 (\单项评分_5_扣分 ), .ALU_SWITCH(DIV),
    .Total(\单项评分_5_total ), .Right(\除法 ), .EN(nHalt));
  \单项评分  \u_单项评分_6  (
    .EQ(ROK), .CLK(CLK), .\分值 (5'b00101), .\正确条数 (\单项评分_6_正确条数 ), .\扣分 (\单项评分_6_扣分 ), .ALU_SWITCH(ADD),
    .Total(\单项评分_6_total ), .Right(\加法 ), .EN(nHalt));
  // Probe on \单项评分_6_total 
  // Probe on \单项评分_6_正确条数 
  // Probe on \单项评分_6_扣分 
  ALU alu_1 (
    .AluOP(ALUOP), .X(X), .Equal(Equal), .Result(R), .Signed_Overflow(OF), .Y(Y), .Result_2(R2),
    .UnSigned_Overflow(CF));
  LED #(.active("false")) led_11 (.in(\乘法 ));
  LED #(.active("false")) led_12 (.in(\除法 ));
  LED #(.active("false")) led_13 (.in(\无符号溢出标志 ));
  \单项评分  \u_单项评分_7  (
    .EQ(ROK), .CLK(CLK), .\分值 (5'b00101), .\正确条数 (\单项评分_7_正确条数 ), .\扣分 (\单项评分_7_扣分 ), .ALU_SWITCH(SUB),
    .Total(\单项评分_7_total ), .Right(\减法 ), .EN(nHalt));
  // Probe on \单项评分_7_total 
  // Probe on \单项评分_7_正确条数 
  // Probe on \单项评分_7_扣分 
  // Probe on \总评分_1_result 
  RAM #(.addrWidth(10), .dataWidth(32), .bus("separate")) ram_3 (
    .addr(counter_1_q), .din(bit_extender_1_out), .str(and_1_out), .clk(CLK));  // open: data, sel, ld, clr
  LED #(.active("false")) led_14 (.in(\加法 ));
  LED #(.active("false")) led_15 (.in(\减法 ));
  \单项评分  \u_单项评分_8  (
    .EQ(ROK), .CLK(CLK), .\分值 (5'b00101), .\正确条数 (\单项评分_8_正确条数 ), .\扣分 (\单项评分_8_扣分 ), .ALU_SWITCH(AND),
    .Total(\单项评分_8_total ), .Right(\与 ), .EN(nHalt));
  // Probe on \单项评分_9_total 
  // Probe on \单项评分_8_total 
  // Probe on \单项评分_8_正确条数 
  // Probe on \单项评分_8_扣分 
  \总评分  \u_总评分_1  (
    .in_1(\单项评分_1_扣分 ), .in_2(\单项评分_16_扣分 ), .in_3(\单项评分_2_扣分 ), .in_4(\单项评分_3_扣分 ), .in_5(\单项评分_6_扣分 ),
    .in_6(\单项评分_7_扣分 ), .in_7(\单项评分_8_扣分 ), .in_8(\单项评分_9_扣分 ), .in_9(\单项评分_10_扣分 ), .in_10(\单项评分_11_扣分 ),
    .in_11(\单项评分_13_扣分 ), .in_12(\单项评分_12_扣分 ), .in_13(\单项评分_15_扣分 ), .in_14(\单项评分_5_扣分 ),
    .in_15(\单项评分_4_扣分 ), .in_16(\单项评分_14_扣分 ), .Result(\总评分_1_result ), .High(High), .Low(Low), .Mid(Mid),
    .\悬空扣分 (\悬空检测 ));
  Hex_Digit_Display hex_digit_display_1 (.value(High));  // open: dp
  Hex_Digit_Display hex_digit_display_2 (.value(Mid));  // open: dp
  \单项评分  \u_单项评分_9  (
    .EQ(ROK), .CLK(CLK), .\分值 (5'b00101), .\正确条数 (\单项评分_9_正确条数 ), .\扣分 (\单项评分_9_扣分 ), .ALU_SWITCH(OR),
    .Total(\单项评分_9_total ), .Right(\或 ), .EN(nHalt));
  // Probe on \单项评分_10_total 
  // Probe on \单项评分_10_正确条数 
  // Probe on \单项评分_9_正确条数 
  // Probe on \单项评分_9_扣分 
  Hex_Digit_Display hex_digit_display_3 (.value(Low));  // open: dp
  LED #(.active("false")) led_16 (.in(\有符号比较 ));
  LED #(.active("false")) led_17 (.in(\无符号比较 ));
  \单项评分  \u_单项评分_10  (
    .EQ(ROK), .CLK(CLK), .\分值 (5'b00101), .\正确条数 (\单项评分_10_正确条数 ), .\扣分 (\单项评分_10_扣分 ), .ALU_SWITCH(XOR),
    .Total(\单项评分_10_total ), .Right(\异或 ), .EN(nHalt));
  // Probe on \单项评分_11_total 
  // Probe on \单项评分_11_正确条数 
  // Probe on \单项评分_11_扣分 
  // Probe on \单项评分_10_扣分 
  \单项评分  \u_单项评分_11  (
    .EQ(ROK), .CLK(CLK), .\分值 (5'b00101), .\正确条数 (\单项评分_11_正确条数 ), .\扣分 (\单项评分_11_扣分 ), .ALU_SWITCH(NOR),
    .Total(\单项评分_11_total ), .Right(\或非 ), .EN(nHalt));
  // Probe on \单项评分_13_total 
  // Probe on \单项评分_13_正确条数 
  // Probe on \单项评分_13_扣分 
  \单项评分  \u_单项评分_12  (
    .EQ(ROK), .CLK(CLK), .\分值 (5'b00101), .\正确条数 (\单项评分_12_正确条数 ), .\扣分 (\单项评分_12_扣分 ), .ALU_SWITCH(UCMP),
    .Total(\单项评分_12_total ), .Right(\无符号比较 ), .EN(nHalt));
  \单项评分  \u_单项评分_13  (
    .EQ(ROK), .CLK(CLK), .\分值 (5'b00101), .\正确条数 (\单项评分_13_正确条数 ), .\扣分 (\单项评分_13_扣分 ), .ALU_SWITCH(SCMP),
    .Total(\单项评分_13_total ), .Right(\有符号比较 ), .EN(nHalt));
  // Probe on \单项评分_12_total 
  // Probe on \单项评分_12_正确条数 
  // Probe on \单项评分_12_扣分 
  \单项评分  \u_单项评分_14  (
    .EQ(EQ_OK), .CLK(CLK), .\分值 (5'b01000), .\正确条数 (\单项评分_14_正确条数 ), .\扣分 (\单项评分_14_扣分 ), .ALU_SWITCH(EQ_OK),
    .Total(\单项评分_14_total ), .Right(\EQ__标志 ), .EN(nHalt));
  // Probe on \单项评分_15_total 
  // Probe on \单项评分_14_total 
  // Probe on \单项评分_14_正确条数 
  // Probe on \单项评分_14_扣分 
  \单项评分  \u_单项评分_15  (
    .EQ(OF_OK), .CLK(CLK), .\分值 (5'b01000), .\正确条数 (\单项评分_15_正确条数 ), .\扣分 (\单项评分_15_扣分 ), .ALU_SWITCH(1'b1),
    .Total(\单项评分_15_total ), .Right(\有符号溢出标志 ), .EN(nHalt));
  // Probe on \单项评分_16_total 
  // Probe on \单项评分_16_正确条数 
  // Probe on \单项评分_15_正确条数 
  // Probe on \单项评分_16_扣分 
  // Probe on \单项评分_15_扣分 
  \单项评分  \u_单项评分_16  (
    .EQ(UOF_OK), .CLK(CLK), .\分值 (5'b01000), .\正确条数 (\单项评分_16_正确条数 ), .\扣分 (\单项评分_16_扣分 ), .ALU_SWITCH(1'b1),
    .Total(\单项评分_16_total ), .Right(\无符号溢出标志 ), .EN(nHalt));
  // Probe on ALUOP
  Decoder #(.select(4), .enable("false")) decoder_1 (
    .out0(SLL), .out1(SAR), .out2(SLR), .out3(MUL), .out4(DIV), .out5(ADD), .out6(SUB), .out7(AND),
    .out8(OR), .out9(XOR), .out10(NOR), .out11(SCMP), .out12(UCMP), .sel(ALUOP));  // open: out13, out14, out15
  xnor xnor_1 (EQ_OK, EQ_S, Equal);
  xnor xnor_2 (OF_OK, FLAG_Standard[2], OF);
  xnor xnor_3 (UOF_OK, CF_S, CF);
  Comparator #(.width(32)) comparator_2 (.a(R_Standard), .b(R), .eq(comparator_2_eq));  // open: gt, lt
  Comparator #(.width(32)) comparator_3 (.a(R2_Standard), .b(R2), .eq(comparator_3_eq));  // open: gt, lt
  Multiplexer #(.disabled(0), .enable("false")) multiplexer_1 (
    .in0(1'b1), .in1(1'b1), .out(multiplexer_1_out), .sel(CF));
  and and_2 (ROK, comparator_2_eq, comparator_3_eq);
  or or_1 (tunnel, ADD, SUB);
  Priority_Encoder #(.select(1)) priority_encoder_1 (
    .in0(multiplexer_1_out), .in1(multiplexer_1_out), .gs(priority_encoder_1_gs));  // open: out, en_out, en_in
  not not_2 (\悬空检测 , priority_encoder_1_gs);
  nand nand_1 (NEQ, EQ_OK, OF_OK, UOF_OK, ROK);

  // Other names for the same wires on the sheet: EQ = Equal; FLAG_Standard[1:0] = {CF_S, EQ_S};
  //   OF_S = FLAG_Standard[2]

  // Notes on the sheet:
  //   操作码为F停止
  //   错误记录X
  //   错误记录Y
  //   运算故障指示灯，红色异常
  //   错误记录ALUOP
  //   错误扣分值
  //   3个存储器存储的是所有错误的测试用例
  //   成绩
  //   华中科技大学：计算机组成课程组
  //   悬空扣5分
  //   错误扣分值
  //   各部分分值
  //   各部分扣分
  //   悬空检测
endmodule

// Trace
module trace (
  input  [7:0] in_1,
  output [31:0] X,
  output [31:0] Y,
  output [3:0] AluOP,
  output [31:0] R,
  output [31:0] R2,
  output [2:0] FLAGS
);

  ROM #(.dataWidth(32)) rom_1 (.addr(in_1), .data(X));  // open: sel
  ROM #(.dataWidth(32)) rom_2 (.addr(in_1), .data(Y));  // open: sel
  ROM #(.dataWidth(4)) rom_3 (.addr(in_1), .data(AluOP));  // open: sel
  ROM #(.dataWidth(32)) rom_4 (.addr(in_1), .data(R));  // open: sel
  ROM #(.dataWidth(32)) rom_5 (.addr(in_1), .data(R2));  // open: sel
  ROM #(.dataWidth(3)) rom_6 (.addr(in_1), .data(FLAGS));  // open: sel

  // Notes on the sheet:
  //   X trace
  //   Y trace
  //   ALU OP Trace
  //   Result Benchmark
  //   Result2 Benchmark
  //   FLAGS Benchmark
  //   contents of rom_1 (hex, n*v repeats v):
  //   ff00ffff ff00ffff ff000000 ff00ffff 7fffffff fffffffe ffff ffffffff 7fffffff 80000000 7ff00000 7c
  //   80000000 7fffffff ff00ffff 7fffffff 18*fffffffe
  //   contents of rom_2 (hex, n*v repeats v):
  //   7 ff00ffff 18 18 10 10 80 ffffffff c 80000000 7c 7ff00000 1 fffffffe 18 74 fffffffe 88 10 ffffffff
  //   10 ffffffff 12*10
  //   contents of rom_3 (hex, n*v repeats v):
  //   0 0 1 2 3 4 4*5 4*6 7 8 9 a b b c c f 11*9 f
  //   contents of rom_4 (hex, n*v repeats v):
  //   807fff80 80000000 ffffffff ff fffffff0 fffffff 1007f fffffffe 8000000b 0 7fefff84 8010007c 7fffffff
  //   80000001 18 7fffffff 0 1 1 1 0 1 300000 11*ffffffee 1
  //   contents of rom_5 (hex, n*v repeats v):
  //   4*0 7 e
  //   contents of rom_6 (hex, n*v repeats v):
  //   0 1 5*0 3 4 7 0 2 4 6 0 0 1 17*0 66*1
endmodule

// 统计评分
module \单项评分  (
  input  ALU_SWITCH,
  input  EQ,
  input  EN,
  input  [4:0] \分值 ,
  input  CLK,
  output [7:0] \正确条数 ,
  output [7:0] \扣分 ,
  output Right,
  output [7:0] Total
);

  wire and_1_out, and_2_out, not_1_out, priority_encoder_1_gs, priority_encoder_1_out;
  wire [7:0] bit_extender_1_out;

  and and_1 (and_1_out, ALU_SWITCH, EN);
  Priority_Encoder #(.select(1)) priority_encoder_1 (
    .in0(EQ), .in1(EQ), .out(priority_encoder_1_out), .gs(priority_encoder_1_gs));  // open: en_out, en_in
  Counter counter_1 (.count(and_1_out), .Q(Total), .clk(CLK));  // open: load, D, carry, clr
  and and_2 (and_2_out, ALU_SWITCH, priority_encoder_1_out, priority_encoder_1_gs, EN);
  Counter counter_2 (.count(and_2_out), .Q(\正确条数 ), .clk(CLK));  // open: load, D, carry, clr
  Comparator comparator_1 (.a(\正确条数 ), .b(Total), .eq(Right));  // open: gt, lt
  assign bit_extender_1_out = {{3{1'b0}}, \分值 };  // Bit_Extender bit_extender_1
  Multiplexer #(.width(8), .enable("false")) multiplexer_1 (
    .in0({8{1'b0}}), .in1(bit_extender_1_out), .out(\扣分 ), .sel(not_1_out));
  not not_1 (not_1_out, Right);

  // Notes on the sheet:
  //   只有使用优先编码器才能屏蔽掉位置状态
endmodule

// 分数汇总计算
module \总评分  (
  input  [7:0] in_1,
  input  [7:0] in_2,
  input  [7:0] in_3,
  input  [7:0] in_4,
  input  [7:0] in_5,
  input  [7:0] in_6,
  input  [7:0] in_7,
  input  [7:0] in_8,
  input  [7:0] in_9,
  input  [7:0] in_10,
  input  [7:0] in_11,
  input  [7:0] in_12,
  input  [7:0] in_13,
  input  [7:0] in_14,
  input  [7:0] in_15,
  input  [7:0] in_16,
  input  \悬空扣分 ,
  output [7:0] Result,
  output [3:0] High,
  output [3:0] Low,
  output [3:0] Mid
);

  wire [7:0] adder_1_out, adder_2_out, adder_3_out, adder_4_out, adder_5_out, adder_6_out, adder_7_out,
       adder_8_out, adder_9_out, adder_10_out, adder_11_out, adder_12_out, adder_13_out, adder_14_out,
       adder_15_out, divider_1_out, subtractor_1_out, subtractor_2_out;
  wire [7:4] divider_1_rem, divider_2_out, divider_2_rem;

  Adder adder_1 (.a(in_1), .b(in_2), .out(adder_1_out));  // open: cin, cout
  Adder adder_2 (.a(in_3), .b(in_4), .out(adder_2_out));  // open: cin, cout
  Adder adder_3 (.a(in_5), .b(in_6), .out(adder_3_out));  // open: cin, cout
  Adder adder_4 (.a(in_7), .b(in_8), .out(adder_4_out));  // open: cin, cout
  Adder adder_5 (.a(in_9), .b(in_10), .out(adder_5_out));  // open: cin, cout
  Adder adder_6 (.a(in_11), .b(in_12), .out(adder_6_out));  // open: cin, cout
  Adder adder_7 (.a(in_13), .b(in_14), .out(adder_7_out));  // open: cin, cout
  Adder adder_8 (.a(in_15), .b(in_16), .out(adder_8_out));  // open: cin, cout
  Adder adder_9 (.a(adder_1_out), .b(adder_2_out), .out(adder_9_out));  // open: cin, cout
  Adder adder_10 (.a(adder_3_out), .b(adder_4_out), .out(adder_10_out));  // open: cin, cout
  Adder adder_11 (.a(adder_5_out), .b(adder_6_out), .out(adder_11_out));  // open: cin, cout
  Adder adder_12 (.a(adder_7_out), .b(adder_8_out), .out(adder_12_out));  // open: cin, cout
  Adder adder_13 (.a(adder_9_out), .b(adder_10_out), .out(adder_13_out));  // open: cin, cout
  Adder adder_14 (.a(adder_11_out), .b(adder_12_out), .out(adder_14_out));  // open: cin, cout
  Adder adder_15 (.a(adder_13_out), .b(adder_14_out), .out(adder_15_out));  // open: cin, cout
  Subtractor subtractor_1 (.a(8'h64), .b(adder_15_out), .out(subtractor_1_out));  // open: bin, bout
  Subtractor subtractor_2 (.a(subtractor_1_out), .b(8'h5), .out(subtractor_2_out));  // open: bin, bout
  Multiplexer #(.width(8), .enable("false")) multiplexer_1 (
    .in0(subtractor_1_out), .in1(subtractor_2_out), .out(Result), .sel(\悬空扣分 ));
  Divider divider_1 (.a(Result), .b(8'ha), .out(divider_1_out), .rem({divider_1_rem, Low}));  // open: upper
  Divider divider_2 (
    .a(divider_1_out), .b(8'ha), .out({divider_2_out, High}), .rem({divider_2_rem, Mid}));  // open: upper
endmodule
