// Logisim project alu.circ as structural Verilog
// FA
module \一位全加器FA封装1  (
  input  Cin,
  input  Xi,
  input  Yi,
  output Cout,
  output Si
);

  wire AND_2_out, AND_out, XOR_2_out;

  or OR (Cout, AND_out, AND_2_out);
  and AND (AND_out, Xi, Yi);
  and AND_2 (AND_2_out, Cin, XOR_2_out);
  xor XOR (Si, Cin, XOR_2_out);
  xor XOR_2 (XOR_2_out, Xi, Yi);

  // Notes on the sheet:
  //   Si = Xi ^ Yi ^ Cin
  //   Cout = Xi Yi + Cin (Xi ^ Yi)
endmodule

module \一位全加器FA封装2  (
  input  Cin,
  input  Xi,
  input  Yi,
  output Cout,
  output Si
);

  wire AND_2_out, AND_out, XOR_2_out;

  or OR (Cout, AND_out, AND_2_out);
  and AND (AND_out, Xi, Yi);
  and AND_2 (AND_2_out, Cin, XOR_2_out);
  xor XOR (Si, Cin, XOR_2_out);
  xor XOR_2 (XOR_2_out, Xi, Yi);

  // Notes on the sheet:
  //   Si = Xi ^ Yi ^ Cin
  //   Cout = Xi Yi + Cin (Xi ^ Yi)
endmodule

module \一位全加器FA封装3  (
  input  Cin,
  input  Xi,
  input  Yi,
  output Cout,
  output Si
);

  wire AND_2_out, AND_out, XOR_2_out;

  or OR (Cout, AND_out, AND_2_out);
  and AND (AND_out, Xi, Yi);
  and AND_2 (AND_2_out, Cin, XOR_2_out);
  xor XOR (Si, Cin, XOR_2_out);
  xor XOR_2 (XOR_2_out, Xi, Yi);

  // Notes on the sheet:
  //   Si = Xi ^ Yi ^ Cin
  //   Cout = Xi Yi + Cin (Xi ^ Yi)
endmodule

// ADD
module \_8位串行加法器  (
  input  [7:0] X,
  input  [7:0] Y,
  input  Cin,
  output [7:0] S,
  output Cout,
  output Overflow
);

  wire \一位全加器fa封装1_2_cout , \一位全加器fa封装1_3_cout , \一位全加器fa封装1_4_cout , \一位全加器fa封装1_5_cout ,
       \一位全加器fa封装1_6_cout , \一位全加器fa封装1_7_cout , \一位全加器fa封装1_8_cout ;

  xor xor_1 (Overflow, Cout, \一位全加器fa封装1_2_cout );
  \一位全加器FA封装1  \u_一位全加器fa封装1_1  (.Cout(Cout), .Si(S[7]), .Cin(\一位全加器fa封装1_2_cout ), .Xi(X[7]), .Yi(Y[7]));
  \一位全加器FA封装1  \u_一位全加器fa封装1_2  (
    .Cout(\一位全加器fa封装1_2_cout ), .Si(S[6]), .Cin(\一位全加器fa封装1_3_cout ), .Xi(X[6]), .Yi(Y[6]));
  \一位全加器FA封装1  \u_一位全加器fa封装1_3  (
    .Cout(\一位全加器fa封装1_3_cout ), .Si(S[5]), .Cin(\一位全加器fa封装1_4_cout ), .Xi(X[5]), .Yi(Y[5]));
  \一位全加器FA封装1  \u_一位全加器fa封装1_4  (
    .Cout(\一位全加器fa封装1_4_cout ), .Si(S[4]), .Cin(\一位全加器fa封装1_5_cout ), .Xi(X[4]), .Yi(Y[4]));
  \一位全加器FA封装1  \u_一位全加器fa封装1_5  (
    .Cout(\一位全加器fa封装1_5_cout ), .Si(S[3]), .Cin(\一位全加器fa封装1_6_cout ), .Xi(X[3]), .Yi(Y[3]));
  \一位全加器FA封装1  \u_一位全加器fa封装1_6  (
    .Cout(\一位全加器fa封装1_6_cout ), .Si(S[2]), .Cin(\一位全加器fa封装1_7_cout ), .Xi(X[2]), .Yi(Y[2]));
  // Probe on X
  // Probe on Y
  // Probe on S
  \一位全加器FA封装1  \u_一位全加器fa封装1_7  (
    .Cout(\一位全加器fa封装1_7_cout ), .Si(S[1]), .Cin(\一位全加器fa封装1_8_cout ), .Xi(X[1]), .Yi(Y[1]));
  // Probe on X
  // Probe on Y
  // Probe on S
  \一位全加器FA封装1  \u_一位全加器fa封装1_8  (.Cout(\一位全加器fa封装1_8_cout ), .Si(S[0]), .Cin(Cin), .Xi(X[0]), .Yi(Y[0]));

  // Other names for the same wires on the sheet: OF = Overflow

  // Notes on the sheet:
  //   输入引脚区
  //   符号位
  //   输出引脚区
  //   +
  //   =
  //   有符号加法
  //   +
  //   =
  //   无符号加法
endmodule

// CAS
module \_8位可控加减法器  (
  input  [7:0] X,
  input  [7:0] Y,
  input  Sub,
  output [7:0] S,
  output Cout,
  output Overflow
);

  wire xor_2_out, xor_3_out, xor_4_out, xor_5_out, xor_6_out, xor_7_out, xor_8_out, xor_9_out,
       \一位全加器fa封装1_2_cout , \一位全加器fa封装1_3_cout , \一位全加器fa封装1_4_cout , \一位全加器fa封装1_5_cout ,
       \一位全加器fa封装1_6_cout , \一位全加器fa封装1_7_cout , \一位全加器fa封装1_8_cout ;
  wire [8:0] \运算指示 ;

  xor xor_1 (Overflow, Cout, \一位全加器fa封装1_2_cout );
  \一位全加器FA封装1  \u_一位全加器fa封装1_1  (.Cout(Cout), .Si(S[7]), .Cin(\一位全加器fa封装1_2_cout ), .Xi(X[7]), .Yi(xor_2_out));
  xor xor_2 (xor_2_out, Y[7], Sub);
  \一位全加器FA封装1  \u_一位全加器fa封装1_2  (
    .Cout(\一位全加器fa封装1_2_cout ), .Si(S[6]), .Cin(\一位全加器fa封装1_3_cout ), .Xi(X[6]), .Yi(xor_3_out));
  xor xor_3 (xor_3_out, Y[6], Sub);
  \一位全加器FA封装1  \u_一位全加器fa封装1_3  (
    .Cout(\一位全加器fa封装1_3_cout ), .Si(S[5]), .Cin(\一位全加器fa封装1_4_cout ), .Xi(X[5]), .Yi(xor_4_out));
  xor xor_4 (xor_4_out, Y[5], Sub);
  \一位全加器FA封装1  \u_一位全加器fa封装1_4  (
    .Cout(\一位全加器fa封装1_4_cout ), .Si(S[4]), .Cin(\一位全加器fa封装1_5_cout ), .Xi(X[4]), .Yi(xor_5_out));
  xor xor_5 (xor_5_out, Y[4], Sub);
  \一位全加器FA封装1  \u_一位全加器fa封装1_5  (
    .Cout(\一位全加器fa封装1_5_cout ), .Si(S[3]), .Cin(\一位全加器fa封装1_6_cout ), .Xi(X[3]), .Yi(xor_6_out));
  xor xor_6 (xor_6_out, Y[3], Sub);
  \一位全加器FA封装1  \u_一位全加器fa封装1_6  (
    .Cout(\一位全加器fa封装1_6_cout ), .Si(S[2]), .Cin(\一位全加器fa封装1_7_cout ), .Xi(X[2]), .Yi(xor_7_out));
  xor xor_7 (xor_7_out, Y[2], Sub);
  // Probe on X
  // Probe on Y
  // Probe on S
  \一位全加器FA封装1  \u_一位全加器fa封装1_7  (
    .Cout(\一位全加器fa封装1_7_cout ), .Si(S[1]), .Cin(\一位全加器fa封装1_8_cout ), .Xi(X[1]), .Yi(xor_8_out));
  xor xor_8 (xor_8_out, Y[1], Sub);
  DotMatrix #(.matrixcols(3), .matrixrows(3)) dotmatrix_1 (.col0(\运算指示 [8:6]), .col1(\运算指示 [5:3]), .col2(\运算指示 [2:0]));
  \一位全加器FA封装1  \u_一位全加器fa封装1_8  (.Cout(\一位全加器fa封装1_8_cout ), .Si(S[0]), .Cin(Sub), .Xi(X[0]), .Yi(xor_9_out));
  xor xor_9 (xor_9_out, Y[0], Sub);
  // Probe on X
  // Probe on Y
  // Probe on S
  Multiplexer #(.width(9), .enable("false")) multiplexer_1 (.in0(9'hba), .in1(9'h92), .out(\运算指示 ), .sel(Sub));

  // Other names for the same wires on the sheet: OF = Overflow

  // Notes on the sheet:
  //   输入引脚区
  //   符号位
  //   输出引脚区
  //   =
  //   有符号
  //   =
  //   无符号
endmodule

// CLA74182
module CLA74182 (
  input  G4,
  input  P4,
  input  G3,
  input  P3,
  input  G2,
  input  P2,
  input  G1,
  input  P1,
  input  Cin,
  output C4,
  output C3,
  output C2,
  output C1,
  output G_star,
  output P_star
);

  wire and_1_out, and_2_out, and_3_out, and_5_out, and_6_out, and_7_out, and_8_out, and_9_out, and_10_out,
       and_11_out, and_12_out, and_13_out, and_14_out;

  or or_1 (G_star, G4, and_1_out, and_3_out, and_2_out);
  and and_1 (and_1_out, P4, G3);
  and and_2 (and_2_out, P4, P3, P2, G1);
  and and_3 (and_3_out, P4, P3, G2);
  and and_4 (P_star, P4, P3, P2, P1);
  and and_5 (and_5_out, P4, G3);
  or or_2 (C4, G4, and_5_out, and_6_out, and_7_out, and_8_out);
  and and_6 (and_6_out, P4, P3, G2);
  and and_7 (and_7_out, P4, P3, P2, G1);
  and and_8 (and_8_out, P4, P3, P2, P1, Cin);
  or or_3 (C3, G3, and_9_out, and_10_out, and_11_out);
  and and_9 (and_9_out, P3, G2);
  and and_10 (and_10_out, P3, P2, G1);
  or or_4 (C2, G2, and_12_out, and_13_out);
  and and_11 (and_11_out, P3, P2, P1, Cin);
  and and_12 (and_12_out, P2, G1);
  and and_13 (and_13_out, P2, P1, Cin);
  or or_5 (C1, G1, and_14_out);
  and and_14 (and_14_out, P1, Cin);

  // Notes on the sheet:
  //   输入引脚区
  //   请根据以上引脚以及隧道信号设计完成74LS182先行进位电路
  //   输出引脚区
  //   请勿增改引脚定义
endmodule

// 4位快速加法器
module \_4位快速加法器  (
  input  [3:0] X,
  input  [3:0] Y,
  input  Cin,
  output [3:0] S,
  output Cout,
  output G_star,
  output P_star
);

  wire and_5_out, and_6_out, and_8_out, and_9_out, and_10_out, and_11_out, and_12_out, and_13_out,
       and_14_out, and_15_out, and_16_out, and_17_out, and_18_out, C1, C2, C3, G1, G2, G3, G4, P1, P2, P3, P4;

  and and_1 (G4, X[3], Y[3]);
  xor xor_1 (P4, X[3], Y[3]);
  xor xor_2 (S[3], P4, C3);
  and and_2 (G3, X[2], Y[2]);
  xor xor_3 (S[2], P3, C2);
  xor xor_4 (P3, X[2], Y[2]);
  and and_3 (G2, X[1], Y[1]);
  xor xor_5 (S[1], P2, C1);
  xor xor_6 (P2, X[1], Y[1]);
  xor xor_7 (S[0], P1, Cin);
  and and_4 (G1, X[0], Y[0]);
  and and_5 (and_5_out, P4, G3);
  xor xor_8 (P1, X[0], Y[0]);
  or or_1 (G_star, G4, and_5_out, and_6_out, and_8_out);
  and and_6 (and_6_out, P4, P3, G2);
  // Probe on X
  // Probe on Y
  // Probe on S
  and and_7 (P_star, P4, P3, P2, P1);
  and and_8 (and_8_out, P4, P3, P2, G1);
  // Probe on X
  // Probe on Y
  // Probe on S
  and and_9 (and_9_out, P4, G3);
  or or_2 (Cout, G4, and_9_out, and_10_out, and_11_out, and_12_out);
  and and_10 (and_10_out, P4, P3, G2);
  and and_11 (and_11_out, P4, P3, P2, G1);
  and and_12 (and_12_out, P4, P3, P2, P1, Cin);
  or or_3 (C3, G3, and_13_out, and_14_out, and_15_out);
  and and_13 (and_13_out, P3, G2);
  and and_14 (and_14_out, P3, P2, G1);
  and and_15 (and_15_out, P3, P2, P1, Cin);
  or or_4 (C2, G2, and_16_out, and_17_out);
  and and_16 (and_16_out, P2, G1);
  and and_17 (and_17_out, P2, P1, Cin);
  or or_5 (C1, G1, and_18_out);
  and and_18 (and_18_out, P1, Cin);

  // Other names for the same wires on the sheet: C4 = Cout

  // Notes on the sheet:
  //   输入引脚区
  //   输出引脚区
  //   +
  //   =
  //   有符号加法
  //   +
  //   =
  //   无符号加法
endmodule

// 16位快速加法器
module \_16位快速加法器  (
  input  [15:0] X,
  input  [15:0] Y,
  input  Cin,
  output Cout,
  output G_star,
  output P_star,
  output [15:0] S
);

  wire cla74182_1_c1, cla74182_1_c2, cla74182_1_c3, \n4位快速加法器_1_g_star , \n4位快速加法器_1_p_star ,
       \n4位快速加法器_2_g_star , \n4位快速加法器_2_p_star , \n4位快速加法器_3_g_star , \n4位快速加法器_3_p_star ,
       \n4位快速加法器_4_g_star , \n4位快速加法器_4_p_star ;

  CLA74182 cla74182_1 (
    .G4(\n4位快速加法器_1_g_star ), .P4(\n4位快速加法器_1_p_star ), .G3(\n4位快速加法器_2_g_star ), .P3(\n4位快速加法器_2_p_star ),
    .G2(\n4位快速加法器_3_g_star ), .P2(\n4位快速加法器_3_p_star ), .G1(\n4位快速加法器_4_g_star ), .P1(\n4位快速加法器_4_p_star ),
    .Cin(Cin), .C4(Cout), .C3(cla74182_1_c3), .C2(cla74182_1_c2), .C1(cla74182_1_c1), .G_star(G_star),
    .P_star(P_star));
  \_4位快速加法器  \u_4位快速加法器_1  (
    .X(X[15:12]), .Y(Y[15:12]), .Cin(cla74182_1_c3), .S(S[15:12]), .G_star(\n4位快速加法器_1_g_star ),
    .P_star(\n4位快速加法器_1_p_star ));  // open: Cout
  \_4位快速加法器  \u_4位快速加法器_2  (
    .X(X[11:8]), .Y(Y[11:8]), .Cin(cla74182_1_c2), .S(S[11:8]), .G_star(\n4位快速加法器_2_g_star ),
    .P_star(\n4位快速加法器_2_p_star ));  // open: Cout
  \_4位快速加法器  \u_4位快速加法器_3  (
    .X(X[7:4]), .Y(Y[7:4]), .Cin(cla74182_1_c1), .S(S[7:4]), .G_star(\n4位快速加法器_3_g_star ),
    .P_star(\n4位快速加法器_3_p_star ));  // open: Cout
  // Probe on X
  // Probe on Y
  // Probe on S
  // Probe on X
  // Probe on Y
  // Probe on S
  \_4位快速加法器  \u_4位快速加法器_4  (
    .X(X[3:0]), .Y(Y[3:0]), .Cin(Cin), .S(S[3:0]), .G_star(\n4位快速加法器_4_g_star ), .P_star(\n4位快速加法器_4_p_star ));  // open: Cout

  // Other names for the same wires on the sheet: S0[3:0] = S[3:0]; S1[3:0] = S[7:4]; S2[3:0] = S[11:8];
  //   S3[3:0] = S[15:12]; X0[3:0] = X[3:0]; X1[3:0] = X[7:4]; X2[3:0] = X[11:8]; X3[3:0] = X[15:12]; Y0[3:0] = Y[3:0];
  //   Y1[3:0] = Y[7:4]; Y2[3:0] = Y[11:8]; Y3[3:0] = Y[15:12]

  // Notes on the sheet:
  //   输入引脚区
  //   输出引脚区
  //   +
  //   =
  //   有符号加法
  //   +
  //   =
  //   无符号加法
endmodule

// 32位加法器
module \_32位快速加法器  (
  input  Cin,
  input  [31:0] X,
  input  [31:0] Y,
  output Cout,
  output [31:0] S,
  output Overflow
);

  wire and_1_out, and_2_out, and_3_out, and_5_out, and_6_out, and_7_out, C1, G1, G2, G_star, not_1_out,
       not_2_out, not_3_out, P1, P2, P_star;

  or or_1 (G_star, G2, and_1_out);
  and and_1 (and_1_out, P2, G1);
  and and_2 (and_2_out, not_1_out, not_2_out, S[31]);
  or or_2 (Overflow, and_2_out, and_3_out);
  and and_3 (and_3_out, X[31], Y[31], not_3_out);
  and and_4 (P_star, P2, P1);
  not not_1 (not_1_out, X[31]);
  not not_2 (not_2_out, Y[31]);
  not not_3 (not_3_out, S[31]);
  or or_3 (Cout, G2, and_5_out, and_6_out);
  and and_5 (and_5_out, P2, G1);
  and and_6 (and_6_out, P2, P1, Cin);
  or or_4 (C1, G1, and_7_out);
  and and_7 (and_7_out, P1, Cin);
  \_16位快速加法器  \u_16位快速加法器_1  (
    .X(X[31:16]), .Y(Y[31:16]), .Cin(C1), .S(S[31:16]), .G_star(G2), .P_star(P2));  // open: Cout
  \_16位快速加法器  \u_16位快速加法器_2  (
    .X(X[15:0]), .Y(Y[15:0]), .Cin(Cin), .S(S[15:0]), .G_star(G1), .P_star(P1));  // open: Cout
  // Probe on X
  // Probe on Y
  // Probe on S
  // Probe on X
  // Probe on Y
  // Probe on S

  // Other names for the same wires on the sheet: S0[15:0] = S[15:0]; S1[15:0] = S[31:16]; fs = S[31];
  //   X0[15:0] = X[15:0]; X1[15:0] = X[31:16]; f0 = X[31]; Y0[15:0] = Y[15:0]; Y1[15:0] = Y[31:16]; f1 = Y[31]

  // Notes on the sheet:
  //   输入引脚区
  //   输出引脚区
  //   +
  //   =
  //   有符号加法
  //   +
  //   =
  //   无符号加法
endmodule

module \补码一位乘法器  (
  input  [7:0] X,
  input  [7:0] Y,
  output [15:0] \乘积 
);

  wire Yn_1_2_q, \时钟_out ;

  Clock \u_时钟  (.out(\时钟_out ));
  Register register_1 (.Q(\乘积 [15:8]), .clk(\时钟_out ));  // open: D, en, clr
  // Probe on X
  // Probe on \乘积 [15:8]
  // Probe on Y
  // Probe on \乘积 [7:0]
  Register Y_2 (.Q(\乘积 [7:0]), .clk(\时钟_out ));  // open: D, en, clr
  // Probe on \乘积 
  // Probe on Yn_1_2_q
  Register #(.width(1)) Yn_1_2 (.Q(Yn_1_2_q), .clk(\时钟_out ));  // open: D, en, clr
  \_8位串行加法器  \u_8位串行加法器_1  ();  // open: X, Y, Cin, S, Cout, Overflow

  // Notes on the sheet:
  //   ∑
endmodule

// 与门阵列
module \_5位乘法与门阵列  (
  input  [4:0] X,
  input  [4:0] Y,
  output [4:0] XY0,
  output [4:0] XY1,
  output [4:0] XY2,
  output [4:0] XY3,
  output [4:0] XY4
);

  and and_1 (XY0[4], X[4], Y[0]);
  and and_2 (XY1[4], X[4], Y[1]);
  and and_3 (XY2[4], X[4], Y[2]);
  and and_4 (XY3[4], X[4], Y[3]);
  and and_5 (XY4[4], X[4], Y[4]);
  and and_6 (XY0[3], X[3], Y[0]);
  and and_7 (XY1[3], X[3], Y[1]);
  and and_8 (XY2[3], X[3], Y[2]);
  and and_9 (XY3[3], X[3], Y[3]);
  and and_10 (XY4[3], X[3], Y[4]);
  and and_11 (XY0[2], X[2], Y[0]);
  and and_12 (XY1[2], X[2], Y[1]);
  and and_13 (XY2[2], X[2], Y[2]);
  and and_14 (XY3[2], X[2], Y[3]);
  and and_15 (XY4[2], X[2], Y[4]);
  and and_16 (XY0[0], X[0], Y[0]);
  and and_17 (XY0[1], X[1], Y[0]);
  and and_18 (XY1[0], X[0], Y[1]);
  and and_19 (XY1[1], X[1], Y[1]);
  and and_20 (XY2[1], X[1], Y[2]);
  and and_21 (XY2[0], X[0], Y[2]);
  and and_22 (XY3[0], X[0], Y[3]);
  and and_23 (XY3[1], X[1], Y[3]);
  and and_24 (XY4[1], X[1], Y[4]);
  and and_25 (XY4[0], X[0], Y[4]);

  // Other names for the same wires on the sheet: X0Y0 = XY0[0]; X1Y0 = XY0[1]; X2Y0 = XY0[2]; X3Y0 = XY0[3];
  //   X4Y0 = XY0[4]; X0Y1 = XY1[0]; X1Y1 = XY1[1]; X2Y1 = XY1[2]; X3Y1 = XY1[3]; X4Y1 = XY1[4]; X0Y2 = XY2[0];
  //   X1Y2 = XY2[1]; X2Y2 = XY2[2]; X3Y2 = XY2[3]; X4Y2 = XY2[4]; X0Y3 = XY3[0]; X1Y3 = XY3[1]; X2Y3 = XY3[2];
  //   X3Y3 = XY3[3]; X4Y3 = XY3[4]; X0Y4 = XY4[0]; X1Y4 = XY4[1]; X2Y4 = XY4[2]; X3Y4 = XY4[3]; X4Y4 = XY4[4]
endmodule

module \_5位阵列乘法器  (
  input  [4:0] X,
  input  [4:0] Y,
  output [9:0] \乘积 
);

  wire X0Y1, X0Y2, X0Y3, X0Y4, X1Y0, X1Y1, X1Y2, X1Y3, X1Y4, X2Y0, X2Y1, X2Y2, X2Y3, X2Y4, X3Y0, X3Y1, X3Y2,
       X3Y3, X3Y4, X4Y0, X4Y1, X4Y2, X4Y3, X4Y4, \一位全加器fa封装3_2_cout , \一位全加器fa封装3_2_si , \一位全加器fa封装3_3_cout ,
       \一位全加器fa封装3_4_cout , \一位全加器fa封装3_4_si , \一位全加器fa封装3_5_cout , \一位全加器fa封装3_5_si , \一位全加器fa封装3_6_cout ,
       \一位全加器fa封装3_7_cout , \一位全加器fa封装3_7_si , \一位全加器fa封装3_8_cout , \一位全加器fa封装3_8_si , \一位全加器fa封装3_9_cout ,
       \一位全加器fa封装3_9_si , \一位全加器fa封装3_10_cout , \一位全加器fa封装3_11_cout , \一位全加器fa封装3_11_si ,
       \一位全加器fa封装3_12_cout , \一位全加器fa封装3_12_si , \一位全加器fa封装3_13_cout , \一位全加器fa封装3_13_si ,
       \一位全加器fa封装3_14_cout , \一位全加器fa封装3_15_cout , \一位全加器fa封装3_15_si , \一位全加器fa封装3_16_cout ,
       \一位全加器fa封装3_16_si , \一位全加器fa封装3_17_cout , \一位全加器fa封装3_18_cout , \一位全加器fa封装3_18_si ,
       \一位全加器fa封装3_19_cout , \一位全加器fa封装3_20_cout ;

  \一位全加器FA封装3  \u_一位全加器fa封装3_1  (
    .Cout(\乘积 [9]), .Si(\乘积 [8]), .Cin(\一位全加器fa封装3_2_cout ), .Xi(\一位全加器fa封装3_3_cout ), .Yi(X4Y4));
  // Probe on X
  \一位全加器FA封装3  \u_一位全加器fa封装3_2  (
    .Cout(\一位全加器fa封装3_2_cout ), .Si(\一位全加器fa封装3_2_si ), .Cin(\一位全加器fa封装3_4_cout ), .Xi(X3Y4), .Yi(X4Y3));
  \一位全加器FA封装3  \u_一位全加器fa封装3_3  (
    .Cout(\一位全加器fa封装3_3_cout ), .Si(\乘积 [7]), .Cin(\一位全加器fa封装3_5_cout ), .Xi(\一位全加器fa封装3_6_cout ),
    .Yi(\一位全加器fa封装3_2_si ));
  \一位全加器FA封装3  \u_一位全加器fa封装3_4  (
    .Cout(\一位全加器fa封装3_4_cout ), .Si(\一位全加器fa封装3_4_si ), .Cin(\一位全加器fa封装3_7_cout ), .Xi(X3Y3), .Yi(X4Y2));
  \一位全加器FA封装3  \u_一位全加器fa封装3_5  (
    .Cout(\一位全加器fa封装3_5_cout ), .Si(\一位全加器fa封装3_5_si ), .Cin(\一位全加器fa封装3_8_cout ), .Xi(X2Y4),
    .Yi(\一位全加器fa封装3_4_si ));
  \一位全加器FA封装3  \u_一位全加器fa封装3_6  (
    .Cout(\一位全加器fa封装3_6_cout ), .Si(\乘积 [6]), .Cin(\一位全加器fa封装3_9_cout ), .Xi(\一位全加器fa封装3_10_cout ),
    .Yi(\一位全加器fa封装3_5_si ));
  // Probe on Y
  \一位全加器FA封装3  \u_一位全加器fa封装3_7  (
    .Cout(\一位全加器fa封装3_7_cout ), .Si(\一位全加器fa封装3_7_si ), .Cin(\一位全加器fa封装3_11_cout ), .Xi(X3Y2), .Yi(X4Y1));
  \一位全加器FA封装3  \u_一位全加器fa封装3_8  (
    .Cout(\一位全加器fa封装3_8_cout ), .Si(\一位全加器fa封装3_8_si ), .Cin(\一位全加器fa封装3_12_cout ), .Xi(X2Y3),
    .Yi(\一位全加器fa封装3_7_si ));
  \一位全加器FA封装3  \u_一位全加器fa封装3_9  (
    .Cout(\一位全加器fa封装3_9_cout ), .Si(\一位全加器fa封装3_9_si ), .Cin(\一位全加器fa封装3_13_cout ), .Xi(X1Y4),
    .Yi(\一位全加器fa封装3_8_si ));
  \一位全加器FA封装3  \u_一位全加器fa封装3_10  (
    .Cout(\一位全加器fa封装3_10_cout ), .Si(\乘积 [5]), .Cin(\一位全加器fa封装3_14_cout ), .Xi(1'b0), .Yi(\一位全加器fa封装3_9_si ));
  \一位全加器FA封装3  \u_一位全加器fa封装3_11  (
    .Cout(\一位全加器fa封装3_11_cout ), .Si(\一位全加器fa封装3_11_si ), .Cin(1'b0), .Xi(X3Y1), .Yi(X4Y0));
  \一位全加器FA封装3  \u_一位全加器fa封装3_12  (
    .Cout(\一位全加器fa封装3_12_cout ), .Si(\一位全加器fa封装3_12_si ), .Cin(\一位全加器fa封装3_15_cout ), .Xi(X2Y2),
    .Yi(\一位全加器fa封装3_11_si ));
  \一位全加器FA封装3  \u_一位全加器fa封装3_13  (
    .Cout(\一位全加器fa封装3_13_cout ), .Si(\一位全加器fa封装3_13_si ), .Cin(\一位全加器fa封装3_16_cout ), .Xi(X1Y3),
    .Yi(\一位全加器fa封装3_12_si ));
  \一位全加器FA封装3  \u_一位全加器fa封装3_14  (
    .Cout(\一位全加器fa封装3_14_cout ), .Si(\乘积 [4]), .Cin(\一位全加器fa封装3_17_cout ), .Xi(X0Y4), .Yi(\一位全加器fa封装3_13_si ));
  // Probe on \乘积 
  \一位全加器FA封装3  \u_一位全加器fa封装3_15  (
    .Cout(\一位全加器fa封装3_15_cout ), .Si(\一位全加器fa封装3_15_si ), .Cin(1'b0), .Xi(X2Y1), .Yi(X3Y0));
  \一位全加器FA封装3  \u_一位全加器fa封装3_16  (
    .Cout(\一位全加器fa封装3_16_cout ), .Si(\一位全加器fa封装3_16_si ), .Cin(\一位全加器fa封装3_18_cout ), .Xi(X1Y2),
    .Yi(\一位全加器fa封装3_15_si ));
  \一位全加器FA封装3  \u_一位全加器fa封装3_17  (
    .Cout(\一位全加器fa封装3_17_cout ), .Si(\乘积 [3]), .Cin(\一位全加器fa封装3_19_cout ), .Xi(X0Y3), .Yi(\一位全加器fa封装3_16_si ));
  \一位全加器FA封装3  \u_一位全加器fa封装3_18  (
    .Cout(\一位全加器fa封装3_18_cout ), .Si(\一位全加器fa封装3_18_si ), .Cin(1'b0), .Xi(X1Y1), .Yi(X2Y0));
  \一位全加器FA封装3  \u_一位全加器fa封装3_19  (
    .Cout(\一位全加器fa封装3_19_cout ), .Si(\乘积 [2]), .Cin(\一位全加器fa封装3_20_cout ), .Xi(X0Y2), .Yi(\一位全加器fa封装3_18_si ));
  \一位全加器FA封装3  \u_一位全加器fa封装3_20  (.Cout(\一位全加器fa封装3_20_cout ), .Si(\乘积 [1]), .Cin(1'b0), .Xi(X0Y1), .Yi(X1Y0));
  and and_1 (X4Y0, X[4], Y[0]);
  and and_2 (X4Y1, X[4], Y[1]);
  and and_3 (X4Y2, X[4], Y[2]);
  and and_4 (X4Y3, X[4], Y[3]);
  and and_5 (X4Y4, X[4], Y[4]);
  and and_6 (X3Y0, X[3], Y[0]);
  and and_7 (X3Y1, X[3], Y[1]);
  and and_8 (X3Y2, X[3], Y[2]);
  and and_9 (X3Y3, X[3], Y[3]);
  and and_10 (X3Y4, X[3], Y[4]);
  and and_11 (X2Y0, X[2], Y[0]);
  and and_12 (X1Y0, X[1], Y[0]);
  and and_13 (X2Y1, X[2], Y[1]);
  and and_14 (X1Y1, X[1], Y[1]);
  and and_15 (X1Y2, X[1], Y[2]);
  and and_16 (X2Y2, X[2], Y[2]);
  and and_17 (X1Y3, X[1], Y[3]);
  and and_18 (X2Y2, X[2], Y[3]);
  and and_19 (X1Y4, X[1], Y[4]);
  and and_20 (X2Y4, X[2], Y[4]);
  and and_21 (\乘积 [0], X[0], Y[0]);
  and and_22 (X0Y1, X[0], Y[1]);
  and and_23 (X0Y2, X[0], Y[2]);
  and and_24 (X0Y3, X[0], Y[3]);
  and and_25 (X0Y4, X[0], Y[4]);
  // _5位乘法与门阵列 5位乘法与门阵列_1: pin names not known; wires that end beside it: X, {X4Y4, X3Y4, X2Y4, X1Y4, X0Y4}, {X4Y3, X3Y3, X2Y3, X1Y3, X0Y3}, {X4Y2, X3Y2, X2Y2, X1Y2, X0Y2}, {X4Y1, X3Y1, X2Y1, X1Y1, X0Y1}, Y, {X4Y0, X3Y0, X2Y0, X1Y0, \乘积 [0]}

  // Other names for the same wires on the sheet: P[9:0] = \乘积 ; P0 = \乘积 [0]; X0Y0 = \乘积 [0];
  //   XY0[4:0] = {X4Y0, X3Y0, X2Y0, X1Y0, \乘积 [0]}; P1 = \乘积 [1]; P2 = \乘积 [2]; P3 = \乘积 [3]; P4 = \乘积 [4];
  //   P5 = \乘积 [5]; P6 = \乘积 [6]; P7 = \乘积 [7]; P8 = \乘积 [8]; P9 = \乘积 [9]; XY1[4:0] = {X4Y1, X3Y1, X2Y1, X1Y1, X0Y1};
  //   XY2[4:0] = {X4Y2, X3Y2, X2Y2, X1Y2, X0Y2}; XY3[4:0] = {X4Y3, X3Y3, X2Y3, X1Y3, X0Y3};
  //   XY4[4:0] = {X4Y4, X3Y4, X2Y4, X1Y4, X0Y4}

  // Notes on the sheet:
  //   输入引脚区
  //   输出引脚区
endmodule

// ALU
module ALU (
  input  [31:0] X,
  input  [31:0] Y,
  input  [3:0] AluOP,
  output Signed_Overflow,
  output UnSigned_Overflow,
  output Equal,
  output [31:0] Result,
  output [31:0] Result_2
);

  wire func5_1_of, func5_1_out, func6_1_of, func6_1_out;
  wire [31:0] func0_1_out, func1_1_out, func2_1_out, func3_1_out, func3_1_out_2, func4_1_out, func4_1_out_2,
       func5_1_s, func6_1_s, func7_1_out, func8_1_out, func9_1_out, func10_1_out, func11_1_out, func12_1_out;

  // Probe on X
  // Probe on X
  // Probe on Y
  // Probe on Y
  Multiplexer #(.select(4)) multiplexer_1 (
    .in0(1'b0), .in1(1'b0), .in2(1'b0), .in3(1'b0), .in4(1'b0), .in5(func5_1_out), .in6(func6_1_out),
    .in7(1'b0), .in8(1'b0), .in9(1'b0), .in10(1'b0), .in11(1'b0), .in12(1'b0), .in13(1'b0), .in14(1'b0),
    .in15(1'b0), .out(UnSigned_Overflow), .sel(AluOP));  // open: en
  Multiplexer #(.select(4)) multiplexer_2 (
    .in0(1'b0), .in1(1'b0), .in2(1'b0), .in3(1'b0), .in4(1'b0), .in5(func5_1_of), .in6(func6_1_of),
    .in7(1'b0), .in8(1'b0), .in9(1'b0), .in10(1'b0), .in11(1'b0), .in12(1'b0), .in13(1'b0), .in14(1'b0),
    .in15(1'b0), .out(Signed_Overflow), .sel(AluOP));  // open: en
  // Probe on AluOP
  Func0 func0_1 (.X(X), .Y(Y), .out(func0_1_out));
  Func1 func1_1 (.X(X), .Y(Y), .out(func1_1_out));
  Func2 func2_1 (.X(X), .Y(Y), .out(func2_1_out));
  Func3 func3_1 (.X(X), .Y(Y), .out(func3_1_out), .out_2(func3_1_out_2));
  Func4 func4_1 (.X(X), .Y(Y), .out(func4_1_out), .out_2(func4_1_out_2));
  Func5 func5_1 (.X(X), .Y(Y), .out(func5_1_out), .of(func5_1_of), .s(func5_1_s));
  Func6 func6_1 (.X(X), .Y(Y), .out(func6_1_out), .of(func6_1_of), .s(func6_1_s));
  Func7 func7_1 (.X(X), .Y(Y), .out(func7_1_out));
  Func8 func8_1 (.X(X), .Y(Y), .out(func8_1_out));
  Func9 func9_1 (.X(X), .Y(Y), .out(func9_1_out));
  Func10 func10_1 (.X(X), .Y(Y), .out(func10_1_out));
  Func11 func11_1 (.X(X), .Y(Y), .out(func11_1_out));
  Func12 func12_1 (.X(X), .Y(Y), .out(func12_1_out));
  // Probe on Result
  // Probe on Result
  Multiplexer #(.select(4), .width(32)) multiplexer_3 (
    .in0(func0_1_out), .in1(func1_1_out), .in2(func2_1_out), .in3(func3_1_out), .in4(func4_1_out),
    .in5(func5_1_s), .in6(func6_1_s), .in7(func7_1_out), .in8(func8_1_out), .in9(func9_1_out),
    .in10(func10_1_out), .in11(func11_1_out), .in12(func12_1_out), .out(Result), .sel(AluOP));  // open: in13, in14, in15, en
  Multiplexer #(.select(4), .width(32)) multiplexer_4 (
    .in0({32{1'b0}}), .in1({32{1'b0}}), .in2({32{1'b0}}), .in3(func3_1_out_2), .in4(func4_1_out_2),
    .in5({32{1'b0}}), .in6({32{1'b0}}), .in7({32{1'b0}}), .in8({32{1'b0}}), .in9({32{1'b0}}),
    .in10({32{1'b0}}), .in11({32{1'b0}}), .in12({32{1'b0}}), .out(Result_2), .sel(AluOP));  // open: in13, in14, in15, en
  // Probe on Result_2
  Comparator #(.width(32)) comparator_1 (.a(X), .b(Y), .eq(Equal));  // open: gt, lt

  // Other names for the same wires on the sheet: OF = Signed_Overflow; Result2[31:0] = Result_2; S[3:0] = AluOP;
  //   UOF = UnSigned_Overflow

  // Notes on the sheet:
  //   不要改变此引脚区域内容，也不要改变ALU封装形式
  //   输入引脚
  //   请在下方利用上方输入输出引脚的隧道信号构建ALU电路，ctrl+d复制选择部件
  //   华中科技大学计算机学院 计算机组成原理，鸣谢加州大学伯克利CS61C课程
  //   输出引脚
  //   探测区域
endmodule

module \运算器测试电路  (
  input  [31:0] X,
  input  [31:0] Y,
  input  [3:0] ALU_OP,
  output Signed_Overflow,
  output Unsigned_overflow,
  output [31:0] Result,
  output [31:0] Result_2,
  output Equal
);

  // Probe on X
  // Probe on X
  ALU alu_1 (
    .AluOP(ALU_OP), .X(X), .Equal(Equal), .Result(Result), .Signed_Overflow(Signed_Overflow), .Y(Y),
    .Result_2(Result_2), .UnSigned_Overflow(Unsigned_overflow));
  // Probe on ALU_OP
  // Probe on Y
  // Probe on Y
  // Probe on Result
  // Probe on Result
  // Probe on Result_2

  // Notes on the sheet:
  //   ALu电路无需调整位置即可连接在该电路中，并且不能出现蓝色线缆和三态输出
endmodule

module \华莱士树  (
);

  wire undriven, undriven_2, undriven_3, undriven_4, undriven_5, undriven_6, undriven_7, undriven_8,
       undriven_9, undriven_10, undriven_11, undriven_12, undriven_13, undriven_14, undriven_15, undriven_16,
       undriven_17, undriven_18, undriven_19, undriven_20, undriven_21, undriven_22, undriven_23,
       undriven_24, undriven_25, undriven_26, undriven_27, undriven_28, undriven_29, undriven_30,
       undriven_31, undriven_32, undriven_33, undriven_34, undriven_35, undriven_36, undriven_37,
       undriven_38, undriven_39, undriven_40, undriven_41, undriven_42, undriven_43, undriven_44,
       undriven_45, undriven_46, undriven_47, undriven_48, undriven_49, undriven_50, undriven_51,
       undriven_52, undriven_53, undriven_54, undriven_55, undriven_56, undriven_57, undriven_58,
       undriven_59, undriven_60, undriven_61, undriven_62, undriven_63, undriven_64, undriven_65,
       undriven_66, undriven_67, undriven_68, undriven_69, undriven_70, undriven_71, undriven_72,
       undriven_73, undriven_74, undriven_75, undriven_76, undriven_77, undriven_78, undriven_79,
       undriven_80, undriven_81, undriven_82, undriven_83, undriven_84, undriven_85, undriven_86,
       undriven_87, undriven_88, undriven_89, undriven_90, undriven_91, undriven_92, undriven_93,
       undriven_94, undriven_95, undriven_96, undriven_97, undriven_98, undriven_99, undriven_100,
       undriven_101, undriven_102, undriven_103, undriven_104, undriven_105, undriven_106, undriven_107,
       undriven_108, undriven_109, undriven_110, undriven_111, undriven_112, undriven_113, undriven_114,
       undriven_115, undriven_116, undriven_117, undriven_118, undriven_119, undriven_120, undriven_121,
       undriven_122, undriven_123, undriven_124, undriven_125, undriven_126, undriven_127, undriven_128,
       undriven_130, \一位全加器fa封装2_1_cout , \一位全加器fa封装2_1_si , \一位全加器fa封装2_2_si , \一位全加器fa封装2_3_cout ,
       \一位全加器fa封装2_3_si , \一位全加器fa封装2_4_si , \一位全加器fa封装2_5_si , \一位全加器fa封装2_6_si , \一位全加器fa封装2_7_si ,
       \一位全加器fa封装2_8_si , \一位全加器fa封装2_9_cout , \一位全加器fa封装2_9_si , \一位全加器fa封装2_10_si , \一位全加器fa封装2_11_cout ,
       \一位全加器fa封装2_11_si , \一位全加器fa封装2_12_si , \一位全加器fa封装2_13_si , \一位全加器fa封装2_14_si , \一位全加器fa封装2_15_cout ,
       \一位全加器fa封装2_15_si , \一位全加器fa封装2_16_si , \一位全加器fa封装2_17_cout , \一位全加器fa封装2_17_si , \一位全加器fa封装2_18_si ,
       \一位全加器fa封装2_19_si , \一位全加器fa封装2_20_si , \一位全加器fa封装2_21_si , \一位全加器fa封装2_22_si , \一位全加器fa封装2_23_cout ,
       \一位全加器fa封装2_23_si , \一位全加器fa封装2_24_si , \一位全加器fa封装2_25_cout , \一位全加器fa封装2_25_si , \一位全加器fa封装2_26_si ,
       \一位全加器fa封装2_27_si , \一位全加器fa封装2_28_si , \一位全加器fa封装2_29_cout , \一位全加器fa封装2_29_si , \一位全加器fa封装2_30_si ,
       \一位全加器fa封装2_31_cout , \一位全加器fa封装2_31_si , \一位全加器fa封装2_32_si , \一位全加器fa封装2_33_si , \一位全加器fa封装2_34_si ,
       \一位全加器fa封装2_35_si , \一位全加器fa封装2_36_si , \一位全加器fa封装2_37_cout , \一位全加器fa封装2_37_si , \一位全加器fa封装2_38_si ,
       \一位全加器fa封装2_39_si , \一位全加器fa封装2_40_cout , \一位全加器fa封装2_40_si , \一位全加器fa封装2_41_si , \一位全加器fa封装2_42_si ,
       \一位全加器fa封装2_43_cout , \一位全加器fa封装2_43_si , \一位全加器fa封装2_44_si , \一位全加器fa封装2_45_cout ,
       \一位全加器fa封装2_45_si , \一位全加器fa封装2_46_si , \一位全加器fa封装2_47_si , \一位全加器fa封装2_48_si , \一位全加器fa封装2_49_si ,
       \一位全加器fa封装2_50_si , \一位全加器fa封装2_51_cout , \一位全加器fa封装2_51_si , \一位全加器fa封装2_52_si ,
       \一位全加器fa封装2_53_cout , \一位全加器fa封装2_53_si , \一位全加器fa封装2_54_si , \一位全加器fa封装2_55_si , \一位全加器fa封装2_56_si ,
       \一位全加器fa封装2_57_cout , \一位全加器fa封装2_57_si , \一位全加器fa封装2_58_si , \一位全加器fa封装2_59_cout ,
       \一位全加器fa封装2_59_si , \一位全加器fa封装2_60_si , \一位全加器fa封装2_61_si , \一位全加器fa封装2_62_si , \一位全加器fa封装2_63_si ,
       \一位全加器fa封装2_64_si , \一位全加器fa封装2_65_cout , \一位全加器fa封装2_65_si , \一位全加器fa封装2_66_si ,
       \一位全加器fa封装2_67_cout , \一位全加器fa封装2_67_si , \一位全加器fa封装2_68_si , \一位全加器fa封装2_69_si , \一位全加器fa封装2_70_si ,
       \一位全加器fa封装2_71_cout , \一位全加器fa封装2_71_si , \一位全加器fa封装2_72_si , \一位全加器fa封装2_73_cout ,
       \一位全加器fa封装2_73_si , \一位全加器fa封装2_74_si , \一位全加器fa封装2_75_si , \一位全加器fa封装2_76_si , \一位全加器fa封装2_77_si ,
       \一位全加器fa封装2_78_si , \一位全加器fa封装2_79_cout , \一位全加器fa封装2_79_si , \一位全加器fa封装2_80_si ,
       \一位全加器fa封装2_81_cout , \一位全加器fa封装2_81_si , \一位全加器fa封装2_82_si , \一位全加器fa封装2_83_si , \一位全加器fa封装2_84_si ,
       \一位全加器fa封装2_85_cout , \一位全加器fa封装2_85_si , \一位全加器fa封装2_86_si , \一位全加器fa封装2_87_cout ,
       \一位全加器fa封装2_87_si , \一位全加器fa封装2_88_si , \一位全加器fa封装2_89_si , \一位全加器fa封装2_90_si , \一位全加器fa封装2_91_si ,
       \一位全加器fa封装2_92_si , \一位全加器fa封装2_93_cout , \一位全加器fa封装2_93_si , \一位全加器fa封装2_94_si ,
       \一位全加器fa封装2_95_cout , \一位全加器fa封装2_95_si , \一位全加器fa封装2_96_si , \一位全加器fa封装2_97_si , \一位全加器fa封装2_98_si ,
       \一位全加器fa封装2_99_cout , \一位全加器fa封装2_99_si , \一位全加器fa封装2_100_si , \一位全加器fa封装2_101_cout ,
       \一位全加器fa封装2_101_si , \一位全加器fa封装2_102_si , \一位全加器fa封装2_103_si , \一位全加器fa封装2_104_si ,
       \一位全加器fa封装2_105_si , \一位全加器fa封装2_106_si , \一位全加器fa封装2_107_cout , \一位全加器fa封装2_107_si ,
       \一位全加器fa封装2_108_si , \一位全加器fa封装2_109_cout , \一位全加器fa封装2_109_si , \一位全加器fa封装2_110_si ,
       \一位全加器fa封装2_111_si , \一位全加器fa封装2_112_si ;
  wire [1:0] undriven_131, \一位全加器fa封装2_4_cout , \一位全加器fa封装2_10_cout , \一位全加器fa封装2_16_cout ,
       \一位全加器fa封装2_22_cout , \一位全加器fa封装2_32_cout , \一位全加器fa封装2_38_cout , \一位全加器fa封装2_44_cout ,
       \一位全加器fa封装2_50_cout , \一位全加器fa封装2_60_cout , \一位全加器fa封装2_66_cout , \一位全加器fa封装2_72_cout ,
       \一位全加器fa封装2_78_cout , \一位全加器fa封装2_88_cout , \一位全加器fa封装2_94_cout , \一位全加器fa封装2_100_cout ,
       \一位全加器fa封装2_106_cout ;
  wire [2:0] undriven_129, \一位全加器fa封装2_7_cout , \一位全加器fa封装2_14_cout , \一位全加器fa封装2_21_cout ,
       \一位全加器fa封装2_27_cout , \一位全加器fa封装2_34_cout , \一位全加器fa封装2_42_cout , \一位全加器fa封装2_49_cout ,
       \一位全加器fa封装2_55_cout , \一位全加器fa封装2_63_cout , \一位全加器fa封装2_70_cout , \一位全加器fa封装2_77_cout ,
       \一位全加器fa封装2_84_cout , \一位全加器fa封装2_90_cout , \一位全加器fa封装2_98_cout , \一位全加器fa封装2_105_cout ,
       \一位全加器fa封装2_112_cout ;

  shape shape_1 ();
  \一位全加器FA封装2  \u_一位全加器fa封装2_1  (
    .Cout(\一位全加器fa封装2_1_cout ), .Si(\一位全加器fa封装2_1_si ), .Cin(\一位全加器fa封装2_7_si ), .Xi(\一位全加器fa封装2_2_si ),
    .Yi(\一位全加器fa封装2_6_si ));
  \一位全加器FA封装2  \u_一位全加器fa封装2_2  (
    .Cout(\一位全加器fa封装2_7_cout [2]), .Si(\一位全加器fa封装2_2_si ), .Cin(undriven_3), .Xi(undriven), .Yi(undriven_2));
  \一位全加器FA封装2  \u_一位全加器fa封装2_3  (
    .Cout(\一位全加器fa封装2_3_cout ), .Si(\一位全加器fa封装2_3_si ), .Cin(\一位全加器fa封装2_10_cout [0]),
    .Xi(\一位全加器fa封装2_4_si ), .Yi(\一位全加器fa封装2_10_cout [1]));
  \一位全加器FA封装2  \u_一位全加器fa封装2_4  (
    .Cout(\一位全加器fa封装2_4_cout [0]), .Si(\一位全加器fa封装2_4_si ), .Cin(\一位全加器fa封装2_11_cout ),
    .Xi(\一位全加器fa封装2_1_si ), .Yi(\一位全加器fa封装2_5_si ));
  \一位全加器FA封装2  \u_一位全加器fa封装2_5  (
    .Cout(\一位全加器fa封装2_4_cout [1]), .Si(\一位全加器fa封装2_5_si ), .Cin(\一位全加器fa封装2_14_cout [0]),
    .Xi(\一位全加器fa封装2_14_cout [2]), .Yi(\一位全加器fa封装2_14_cout [1]));
  \一位全加器FA封装2  \u_一位全加器fa封装2_6  (
    .Cout(\一位全加器fa封装2_7_cout [1]), .Si(\一位全加器fa封装2_6_si ), .Cin(undriven_6), .Xi(undriven_4), .Yi(undriven_5));
  \一位全加器FA封装2  \u_一位全加器fa封装2_7  (
    .Cout(\一位全加器fa封装2_7_cout [0]), .Si(\一位全加器fa封装2_7_si ), .Cin(1'b0), .Xi(undriven_7), .Yi(undriven_8));
  \一位全加器FA封装2  \u_一位全加器fa封装2_8  (
    .Cout(\一位全加器fa封装2_14_cout [2]), .Si(\一位全加器fa封装2_8_si ), .Cin(undriven_11), .Xi(undriven_9),
    .Yi(undriven_10));
  \一位全加器FA封装2  \u_一位全加器fa封装2_9  (
    .Cout(\一位全加器fa封装2_9_cout ), .Si(\一位全加器fa封装2_9_si ), .Cin(\一位全加器fa封装2_16_cout [0]),
    .Xi(\一位全加器fa封装2_10_si ), .Yi(\一位全加器fa封装2_16_cout [1]));
  \一位全加器FA封装2  \u_一位全加器fa封装2_10  (
    .Cout(\一位全加器fa封装2_10_cout [0]), .Si(\一位全加器fa封装2_10_si ), .Cin(\一位全加器fa封装2_17_cout ),
    .Xi(\一位全加器fa封装2_11_si ), .Yi(\一位全加器fa封装2_12_si ));
  \一位全加器FA封装2  \u_一位全加器fa封装2_11  (
    .Cout(\一位全加器fa封装2_11_cout ), .Si(\一位全加器fa封装2_11_si ), .Cin(\一位全加器fa封装2_14_si ), .Xi(\一位全加器fa封装2_8_si ),
    .Yi(\一位全加器fa封装2_13_si ));
  \一位全加器FA封装2  \u_一位全加器fa封装2_12  (
    .Cout(\一位全加器fa封装2_10_cout [1]), .Si(\一位全加器fa封装2_12_si ), .Cin(\一位全加器fa封装2_21_cout [0]),
    .Xi(\一位全加器fa封装2_21_cout [2]), .Yi(\一位全加器fa封装2_21_cout [1]));
  \一位全加器FA封装2  \u_一位全加器fa封装2_13  (
    .Cout(\一位全加器fa封装2_14_cout [1]), .Si(\一位全加器fa封装2_13_si ), .Cin(undriven_14), .Xi(undriven_12),
    .Yi(undriven_13));
  shape shape_2 ();
  \一位全加器FA封装2  \u_一位全加器fa封装2_14  (
    .Cout(\一位全加器fa封装2_14_cout [0]), .Si(\一位全加器fa封装2_14_si ), .Cin(1'b0), .Xi(undriven_15), .Yi(undriven_16));
  \一位全加器FA封装2  \u_一位全加器fa封装2_15  (
    .Cout(\一位全加器fa封装2_15_cout ), .Si(\一位全加器fa封装2_15_si ), .Cin(\一位全加器fa封装2_22_cout [0]),
    .Xi(\一位全加器fa封装2_16_si ), .Yi(\一位全加器fa封装2_22_cout [1]));
  \一位全加器FA封装2  \u_一位全加器fa封装2_16  (
    .Cout(\一位全加器fa封装2_16_cout [0]), .Si(\一位全加器fa封装2_16_si ), .Cin(\一位全加器fa封装2_23_cout ),
    .Xi(\一位全加器fa封装2_17_si ), .Yi(\一位全加器fa封装2_20_si ));
  \一位全加器FA封装2  \u_一位全加器fa封装2_17  (
    .Cout(\一位全加器fa封装2_17_cout ), .Si(\一位全加器fa封装2_17_si ), .Cin(\一位全加器fa封装2_21_si ), .Xi(\一位全加器fa封装2_18_si ),
    .Yi(\一位全加器fa封装2_19_si ));
  \一位全加器FA封装2  \u_一位全加器fa封装2_18  (
    .Cout(\一位全加器fa封装2_21_cout [2]), .Si(\一位全加器fa封装2_18_si ), .Cin(undriven_19), .Xi(undriven_17),
    .Yi(undriven_18));
  \一位全加器FA封装2  \u_一位全加器fa封装2_19  (
    .Cout(\一位全加器fa封装2_21_cout [1]), .Si(\一位全加器fa封装2_19_si ), .Cin(undriven_22), .Xi(undriven_20),
    .Yi(undriven_21));
  \一位全加器FA封装2  \u_一位全加器fa封装2_20  (
    .Cout(\一位全加器fa封装2_16_cout [1]), .Si(\一位全加器fa封装2_20_si ), .Cin(\一位全加器fa封装2_27_cout [0]),
    .Xi(\一位全加器fa封装2_27_cout [2]), .Yi(\一位全加器fa封装2_27_cout [1]));
  \一位全加器FA封装2  \u_一位全加器fa封装2_21  (
    .Cout(\一位全加器fa封装2_21_cout [0]), .Si(\一位全加器fa封装2_21_si ), .Cin(1'b0), .Xi(undriven_23), .Yi(undriven_24));
  \一位全加器FA封装2  \u_一位全加器fa封装2_22  (
    .Cout(\一位全加器fa封装2_22_cout [0]), .Si(\一位全加器fa封装2_22_si ), .Cin(\一位全加器fa封装2_29_cout ),
    .Xi(\一位全加器fa封装2_23_si ), .Yi(\一位全加器fa封装2_26_si ));
  \一位全加器FA封装2  \u_一位全加器fa封装2_23  (
    .Cout(\一位全加器fa封装2_23_cout ), .Si(\一位全加器fa封装2_23_si ), .Cin(\一位全加器fa封装2_27_si ), .Xi(\一位全加器fa封装2_24_si ),
    .Yi(\一位全加器fa封装2_28_si ));
  \一位全加器FA封装2  \u_一位全加器fa封装2_24  (
    .Cout(\一位全加器fa封装2_27_cout [2]), .Si(\一位全加器fa封装2_24_si ), .Cin(undriven_27), .Xi(undriven_25),
    .Yi(undriven_26));
  shape shape_3 ();
  \一位全加器FA封装2  \u_一位全加器fa封装2_25  (
    .Cout(\一位全加器fa封装2_25_cout ), .Si(\一位全加器fa封装2_25_si ), .Cin(\一位全加器fa封装2_32_cout [0]),
    .Xi(\一位全加器fa封装2_22_si ), .Yi(\一位全加器fa封装2_32_cout [1]));
  \一位全加器FA封装2  \u_一位全加器fa封装2_26  (
    .Cout(\一位全加器fa封装2_22_cout [1]), .Si(\一位全加器fa封装2_26_si ), .Cin(\一位全加器fa封装2_34_cout [0]),
    .Xi(\一位全加器fa封装2_34_cout [2]), .Yi(\一位全加器fa封装2_34_cout [1]));
  \一位全加器FA封装2  \u_一位全加器fa封装2_27  (
    .Cout(\一位全加器fa封装2_27_cout [0]), .Si(\一位全加器fa封装2_27_si ), .Cin(1'b0), .Xi(undriven_31), .Yi(undriven_32));
  \一位全加器FA封装2  \u_一位全加器fa封装2_28  (
    .Cout(\一位全加器fa封装2_27_cout [1]), .Si(\一位全加器fa封装2_28_si ), .Cin(undriven_30), .Xi(undriven_28),
    .Yi(undriven_29));
  \一位全加器FA封装2  \u_一位全加器fa封装2_29  (
    .Cout(\一位全加器fa封装2_29_cout ), .Si(\一位全加器fa封装2_29_si ), .Cin(\一位全加器fa封装2_34_si ), .Xi(\一位全加器fa封装2_30_si ),
    .Yi(\一位全加器fa封装2_35_si ));
  \一位全加器FA封装2  \u_一位全加器fa封装2_30  (
    .Cout(\一位全加器fa封装2_34_cout [2]), .Si(\一位全加器fa封装2_30_si ), .Cin(undriven_35), .Xi(undriven_33),
    .Yi(undriven_34));
  \一位全加器FA封装2  \u_一位全加器fa封装2_31  (
    .Cout(\一位全加器fa封装2_31_cout ), .Si(\一位全加器fa封装2_31_si ), .Cin(\一位全加器fa封装2_38_cout [0]),
    .Xi(\一位全加器fa封装2_32_si ), .Yi(\一位全加器fa封装2_38_cout [1]));
  \一位全加器FA封装2  \u_一位全加器fa封装2_32  (
    .Cout(\一位全加器fa封装2_32_cout [0]), .Si(\一位全加器fa封装2_32_si ), .Cin(\一位全加器fa封装2_40_cout ),
    .Xi(\一位全加器fa封装2_29_si ), .Yi(\一位全加器fa封装2_33_si ));
  \一位全加器FA封装2  \u_一位全加器fa封装2_33  (
    .Cout(\一位全加器fa封装2_32_cout [1]), .Si(\一位全加器fa封装2_33_si ), .Cin(\一位全加器fa封装2_42_cout [0]),
    .Xi(\一位全加器fa封装2_42_cout [2]), .Yi(\一位全加器fa封装2_42_cout [1]));
  \一位全加器FA封装2  \u_一位全加器fa封装2_34  (
    .Cout(\一位全加器fa封装2_34_cout [0]), .Si(\一位全加器fa封装2_34_si ), .Cin(1'b0), .Xi(undriven_39), .Yi(undriven_40));
  \一位全加器FA封装2  \u_一位全加器fa封装2_35  (
    .Cout(\一位全加器fa封装2_34_cout [1]), .Si(\一位全加器fa封装2_35_si ), .Cin(undriven_38), .Xi(undriven_36),
    .Yi(undriven_37));
  \一位全加器FA封装2  \u_一位全加器fa封装2_36  (
    .Cout(\一位全加器fa封装2_42_cout [2]), .Si(\一位全加器fa封装2_36_si ), .Cin(undriven_43), .Xi(undriven_41),
    .Yi(undriven_42));
  \一位全加器FA封装2  \u_一位全加器fa封装2_37  (
    .Cout(\一位全加器fa封装2_37_cout ), .Si(\一位全加器fa封装2_37_si ), .Cin(\一位全加器fa封装2_44_cout [0]),
    .Xi(\一位全加器fa封装2_38_si ), .Yi(\一位全加器fa封装2_44_cout [1]));
  \一位全加器FA封装2  \u_一位全加器fa封装2_38  (
    .Cout(\一位全加器fa封装2_38_cout [0]), .Si(\一位全加器fa封装2_38_si ), .Cin(\一位全加器fa封装2_45_cout ),
    .Xi(\一位全加器fa封装2_40_si ), .Yi(\一位全加器fa封装2_39_si ));
  \一位全加器FA封装2  \u_一位全加器fa封装2_39  (
    .Cout(\一位全加器fa封装2_38_cout [1]), .Si(\一位全加器fa封装2_39_si ), .Cin(\一位全加器fa封装2_49_cout [0]),
    .Xi(\一位全加器fa封装2_49_cout [2]), .Yi(\一位全加器fa封装2_49_cout [1]));
  \一位全加器FA封装2  \u_一位全加器fa封装2_40  (
    .Cout(\一位全加器fa封装2_40_cout ), .Si(\一位全加器fa封装2_40_si ), .Cin(\一位全加器fa封装2_42_si ), .Xi(\一位全加器fa封装2_36_si ),
    .Yi(\一位全加器fa封装2_41_si ));
  \一位全加器FA封装2  \u_一位全加器fa封装2_41  (
    .Cout(\一位全加器fa封装2_42_cout [1]), .Si(\一位全加器fa封装2_41_si ), .Cin(undriven_46), .Xi(undriven_44),
    .Yi(undriven_45));
  shape shape_4 ();
  \一位全加器FA封装2  \u_一位全加器fa封装2_42  (
    .Cout(\一位全加器fa封装2_42_cout [0]), .Si(\一位全加器fa封装2_42_si ), .Cin(1'b0), .Xi(undriven_47), .Yi(undriven_48));
  \一位全加器FA封装2  \u_一位全加器fa封装2_43  (
    .Cout(\一位全加器fa封装2_43_cout ), .Si(\一位全加器fa封装2_43_si ), .Cin(\一位全加器fa封装2_50_cout [0]),
    .Xi(\一位全加器fa封装2_44_si ), .Yi(\一位全加器fa封装2_50_cout [1]));
  \一位全加器FA封装2  \u_一位全加器fa封装2_44  (
    .Cout(\一位全加器fa封装2_44_cout [0]), .Si(\一位全加器fa封装2_44_si ), .Cin(\一位全加器fa封装2_51_cout ),
    .Xi(\一位全加器fa封装2_45_si ), .Yi(\一位全加器fa封装2_48_si ));
  \一位全加器FA封装2  \u_一位全加器fa封装2_45  (
    .Cout(\一位全加器fa封装2_45_cout ), .Si(\一位全加器fa封装2_45_si ), .Cin(\一位全加器fa封装2_49_si ), .Xi(\一位全加器fa封装2_47_si ),
    .Yi(\一位全加器fa封装2_46_si ));
  \一位全加器FA封装2  \u_一位全加器fa封装2_46  (
    .Cout(\一位全加器fa封装2_49_cout [1]), .Si(\一位全加器fa封装2_46_si ), .Cin(undriven_54), .Xi(undriven_52),
    .Yi(undriven_53));
  \一位全加器FA封装2  \u_一位全加器fa封装2_47  (
    .Cout(\一位全加器fa封装2_49_cout [2]), .Si(\一位全加器fa封装2_47_si ), .Cin(undriven_51), .Xi(undriven_49),
    .Yi(undriven_50));
  \一位全加器FA封装2  \u_一位全加器fa封装2_48  (
    .Cout(\一位全加器fa封装2_44_cout [1]), .Si(\一位全加器fa封装2_48_si ), .Cin(\一位全加器fa封装2_55_cout [0]),
    .Xi(\一位全加器fa封装2_55_cout [2]), .Yi(\一位全加器fa封装2_55_cout [1]));
  \一位全加器FA封装2  \u_一位全加器fa封装2_49  (
    .Cout(\一位全加器fa封装2_49_cout [0]), .Si(\一位全加器fa封装2_49_si ), .Cin(1'b0), .Xi(undriven_55), .Yi(undriven_56));
  \一位全加器FA封装2  \u_一位全加器fa封装2_50  (
    .Cout(\一位全加器fa封装2_50_cout [0]), .Si(\一位全加器fa封装2_50_si ), .Cin(\一位全加器fa封装2_57_cout ),
    .Xi(\一位全加器fa封装2_51_si ), .Yi(\一位全加器fa封装2_54_si ));
  \一位全加器FA封装2  \u_一位全加器fa封装2_51  (
    .Cout(\一位全加器fa封装2_51_cout ), .Si(\一位全加器fa封装2_51_si ), .Cin(\一位全加器fa封装2_55_si ), .Xi(\一位全加器fa封装2_52_si ),
    .Yi(\一位全加器fa封装2_56_si ));
  \一位全加器FA封装2  \u_一位全加器fa封装2_52  (
    .Cout(\一位全加器fa封装2_55_cout [2]), .Si(\一位全加器fa封装2_52_si ), .Cin(undriven_59), .Xi(undriven_57),
    .Yi(undriven_58));
  shape shape_5 ();
  \一位全加器FA封装2  \u_一位全加器fa封装2_53  (
    .Cout(\一位全加器fa封装2_53_cout ), .Si(\一位全加器fa封装2_53_si ), .Cin(\一位全加器fa封装2_60_cout [0]),
    .Xi(\一位全加器fa封装2_50_si ), .Yi(\一位全加器fa封装2_60_cout [1]));
  \一位全加器FA封装2  \u_一位全加器fa封装2_54  (
    .Cout(\一位全加器fa封装2_50_cout [1]), .Si(\一位全加器fa封装2_54_si ), .Cin(\一位全加器fa封装2_63_cout [0]),
    .Xi(\一位全加器fa封装2_63_cout [2]), .Yi(\一位全加器fa封装2_63_cout [1]));
  \一位全加器FA封装2  \u_一位全加器fa封装2_55  (
    .Cout(\一位全加器fa封装2_55_cout [0]), .Si(\一位全加器fa封装2_55_si ), .Cin(1'b0), .Xi(undriven_63), .Yi(undriven_64));
  \一位全加器FA封装2  \u_一位全加器fa封装2_56  (
    .Cout(\一位全加器fa封装2_55_cout [1]), .Si(\一位全加器fa封装2_56_si ), .Cin(undriven_62), .Xi(undriven_60),
    .Yi(undriven_61));
  \一位全加器FA封装2  \u_一位全加器fa封装2_57  (
    .Cout(\一位全加器fa封装2_57_cout ), .Si(\一位全加器fa封装2_57_si ), .Cin(\一位全加器fa封装2_63_si ), .Xi(\一位全加器fa封装2_58_si ),
    .Yi(\一位全加器fa封装2_62_si ));
  \一位全加器FA封装2  \u_一位全加器fa封装2_58  (
    .Cout(\一位全加器fa封装2_63_cout [2]), .Si(\一位全加器fa封装2_58_si ), .Cin(undriven_67), .Xi(undriven_65),
    .Yi(undriven_66));
  \一位全加器FA封装2  \u_一位全加器fa封装2_59  (
    .Cout(\一位全加器fa封装2_59_cout ), .Si(\一位全加器fa封装2_59_si ), .Cin(\一位全加器fa封装2_66_cout [0]),
    .Xi(\一位全加器fa封装2_60_si ), .Yi(\一位全加器fa封装2_66_cout [1]));
  \一位全加器FA封装2  \u_一位全加器fa封装2_60  (
    .Cout(\一位全加器fa封装2_60_cout [0]), .Si(\一位全加器fa封装2_60_si ), .Cin(\一位全加器fa封装2_67_cout ),
    .Xi(\一位全加器fa封装2_57_si ), .Yi(\一位全加器fa封装2_61_si ));
  \一位全加器FA封装2  \u_一位全加器fa封装2_61  (
    .Cout(\一位全加器fa封装2_60_cout [1]), .Si(\一位全加器fa封装2_61_si ), .Cin(\一位全加器fa封装2_70_cout [0]),
    .Xi(\一位全加器fa封装2_70_cout [2]), .Yi(\一位全加器fa封装2_70_cout [1]));
  \一位全加器FA封装2  \u_一位全加器fa封装2_62  (
    .Cout(\一位全加器fa封装2_63_cout [1]), .Si(\一位全加器fa封装2_62_si ), .Cin(undriven_70), .Xi(undriven_68),
    .Yi(undriven_69));
  \一位全加器FA封装2  \u_一位全加器fa封装2_63  (
    .Cout(\一位全加器fa封装2_63_cout [0]), .Si(\一位全加器fa封装2_63_si ), .Cin(1'b0), .Xi(undriven_71), .Yi(undriven_72));
  \一位全加器FA封装2  \u_一位全加器fa封装2_64  (
    .Cout(\一位全加器fa封装2_70_cout [2]), .Si(\一位全加器fa封装2_64_si ), .Cin(undriven_75), .Xi(undriven_73),
    .Yi(undriven_74));
  \一位全加器FA封装2  \u_一位全加器fa封装2_65  (
    .Cout(\一位全加器fa封装2_65_cout ), .Si(\一位全加器fa封装2_65_si ), .Cin(\一位全加器fa封装2_72_cout [0]),
    .Xi(\一位全加器fa封装2_66_si ), .Yi(\一位全加器fa封装2_72_cout [1]));
  \一位全加器FA封装2  \u_一位全加器fa封装2_66  (
    .Cout(\一位全加器fa封装2_66_cout [0]), .Si(\一位全加器fa封装2_66_si ), .Cin(\一位全加器fa封装2_73_cout ),
    .Xi(\一位全加器fa封装2_67_si ), .Yi(\一位全加器fa封装2_68_si ));
  \一位全加器FA封装2  \u_一位全加器fa封装2_67  (
    .Cout(\一位全加器fa封装2_67_cout ), .Si(\一位全加器fa封装2_67_si ), .Cin(\一位全加器fa封装2_70_si ), .Xi(\一位全加器fa封装2_64_si ),
    .Yi(\一位全加器fa封装2_69_si ));
  \一位全加器FA封装2  \u_一位全加器fa封装2_68  (
    .Cout(\一位全加器fa封装2_66_cout [1]), .Si(\一位全加器fa封装2_68_si ), .Cin(\一位全加器fa封装2_77_cout [0]),
    .Xi(\一位全加器fa封装2_77_cout [2]), .Yi(\一位全加器fa封装2_77_cout [1]));
  \一位全加器FA封装2  \u_一位全加器fa封装2_69  (
    .Cout(\一位全加器fa封装2_70_cout [1]), .Si(\一位全加器fa封装2_69_si ), .Cin(undriven_78), .Xi(undriven_76),
    .Yi(undriven_77));
  shape shape_6 ();
  \一位全加器FA封装2  \u_一位全加器fa封装2_70  (
    .Cout(\一位全加器fa封装2_70_cout [0]), .Si(\一位全加器fa封装2_70_si ), .Cin(1'b0), .Xi(undriven_79), .Yi(undriven_80));
  \一位全加器FA封装2  \u_一位全加器fa封装2_71  (
    .Cout(\一位全加器fa封装2_71_cout ), .Si(\一位全加器fa封装2_71_si ), .Cin(\一位全加器fa封装2_78_cout [0]),
    .Xi(\一位全加器fa封装2_72_si ), .Yi(\一位全加器fa封装2_78_cout [1]));
  \一位全加器FA封装2  \u_一位全加器fa封装2_72  (
    .Cout(\一位全加器fa封装2_72_cout [0]), .Si(\一位全加器fa封装2_72_si ), .Cin(\一位全加器fa封装2_79_cout ),
    .Xi(\一位全加器fa封装2_73_si ), .Yi(\一位全加器fa封装2_76_si ));
  \一位全加器FA封装2  \u_一位全加器fa封装2_73  (
    .Cout(\一位全加器fa封装2_73_cout ), .Si(\一位全加器fa封装2_73_si ), .Cin(\一位全加器fa封装2_77_si ), .Xi(\一位全加器fa封装2_75_si ),
    .Yi(\一位全加器fa封装2_74_si ));
  \一位全加器FA封装2  \u_一位全加器fa封装2_74  (
    .Cout(\一位全加器fa封装2_77_cout [1]), .Si(\一位全加器fa封装2_74_si ), .Cin(undriven_86), .Xi(undriven_84),
    .Yi(undriven_85));
  \一位全加器FA封装2  \u_一位全加器fa封装2_75  (
    .Cout(\一位全加器fa封装2_77_cout [2]), .Si(\一位全加器fa封装2_75_si ), .Cin(undriven_83), .Xi(undriven_81),
    .Yi(undriven_82));
  \一位全加器FA封装2  \u_一位全加器fa封装2_76  (
    .Cout(\一位全加器fa封装2_72_cout [1]), .Si(\一位全加器fa封装2_76_si ), .Cin(\一位全加器fa封装2_84_cout [0]),
    .Xi(\一位全加器fa封装2_84_cout [2]), .Yi(\一位全加器fa封装2_84_cout [1]));
  \一位全加器FA封装2  \u_一位全加器fa封装2_77  (
    .Cout(\一位全加器fa封装2_77_cout [0]), .Si(\一位全加器fa封装2_77_si ), .Cin(1'b0), .Xi(undriven_87), .Yi(undriven_88));
  \一位全加器FA封装2  \u_一位全加器fa封装2_78  (
    .Cout(\一位全加器fa封装2_78_cout [0]), .Si(\一位全加器fa封装2_78_si ), .Cin(\一位全加器fa封装2_85_cout ),
    .Xi(\一位全加器fa封装2_79_si ), .Yi(\一位全加器fa封装2_82_si ));
  \一位全加器FA封装2  \u_一位全加器fa封装2_79  (
    .Cout(\一位全加器fa封装2_79_cout ), .Si(\一位全加器fa封装2_79_si ), .Cin(\一位全加器fa封装2_84_si ), .Xi(\一位全加器fa封装2_80_si ),
    .Yi(\一位全加器fa封装2_83_si ));
  \一位全加器FA封装2  \u_一位全加器fa封装2_80  (
    .Cout(\一位全加器fa封装2_84_cout [2]), .Si(\一位全加器fa封装2_80_si ), .Cin(undriven_91), .Xi(undriven_89),
    .Yi(undriven_90));
  shape shape_7 ();
  \一位全加器FA封装2  \u_一位全加器fa封装2_81  (
    .Cout(\一位全加器fa封装2_81_cout ), .Si(\一位全加器fa封装2_81_si ), .Cin(\一位全加器fa封装2_88_cout [0]),
    .Xi(\一位全加器fa封装2_78_si ), .Yi(\一位全加器fa封装2_88_cout [1]));
  \一位全加器FA封装2  \u_一位全加器fa封装2_82  (
    .Cout(\一位全加器fa封装2_78_cout [1]), .Si(\一位全加器fa封装2_82_si ), .Cin(\一位全加器fa封装2_90_cout [0]),
    .Xi(\一位全加器fa封装2_90_cout [2]), .Yi(\一位全加器fa封装2_90_cout [1]));
  \一位全加器FA封装2  \u_一位全加器fa封装2_83  (
    .Cout(\一位全加器fa封装2_84_cout [1]), .Si(\一位全加器fa封装2_83_si ), .Cin(undriven_94), .Xi(undriven_92),
    .Yi(undriven_93));
  \一位全加器FA封装2  \u_一位全加器fa封装2_84  (
    .Cout(\一位全加器fa封装2_84_cout [0]), .Si(\一位全加器fa封装2_84_si ), .Cin(1'b0), .Xi(undriven_95), .Yi(undriven_96));
  \一位全加器FA封装2  \u_一位全加器fa封装2_85  (
    .Cout(\一位全加器fa封装2_85_cout ), .Si(\一位全加器fa封装2_85_si ), .Cin(\一位全加器fa封装2_90_si ), .Xi(\一位全加器fa封装2_86_si ),
    .Yi(\一位全加器fa封装2_91_si ));
  \一位全加器FA封装2  \u_一位全加器fa封装2_86  (
    .Cout(\一位全加器fa封装2_90_cout [2]), .Si(\一位全加器fa封装2_86_si ), .Cin(undriven_99), .Xi(undriven_97),
    .Yi(undriven_98));
  \一位全加器FA封装2  \u_一位全加器fa封装2_87  (
    .Cout(\一位全加器fa封装2_87_cout ), .Si(\一位全加器fa封装2_87_si ), .Cin(\一位全加器fa封装2_94_cout [0]),
    .Xi(\一位全加器fa封装2_88_si ), .Yi(\一位全加器fa封装2_94_cout [1]));
  \一位全加器FA封装2  \u_一位全加器fa封装2_88  (
    .Cout(\一位全加器fa封装2_88_cout [0]), .Si(\一位全加器fa封装2_88_si ), .Cin(\一位全加器fa封装2_95_cout ),
    .Xi(\一位全加器fa封装2_85_si ), .Yi(\一位全加器fa封装2_89_si ));
  \一位全加器FA封装2  \u_一位全加器fa封装2_89  (
    .Cout(\一位全加器fa封装2_88_cout [1]), .Si(\一位全加器fa封装2_89_si ), .Cin(\一位全加器fa封装2_98_cout [0]),
    .Xi(\一位全加器fa封装2_98_cout [2]), .Yi(\一位全加器fa封装2_98_cout [1]));
  \一位全加器FA封装2  \u_一位全加器fa封装2_90  (
    .Cout(\一位全加器fa封装2_90_cout [0]), .Si(\一位全加器fa封装2_90_si ), .Cin(1'b0), .Xi(undriven_103), .Yi(undriven_104));
  \一位全加器FA封装2  \u_一位全加器fa封装2_91  (
    .Cout(\一位全加器fa封装2_90_cout [1]), .Si(\一位全加器fa封装2_91_si ), .Cin(undriven_102), .Xi(undriven_100),
    .Yi(undriven_101));
  \一位全加器FA封装2  \u_一位全加器fa封装2_92  (
    .Cout(\一位全加器fa封装2_98_cout [2]), .Si(\一位全加器fa封装2_92_si ), .Cin(undriven_107), .Xi(undriven_105),
    .Yi(undriven_106));
  \一位全加器FA封装2  \u_一位全加器fa封装2_93  (
    .Cout(\一位全加器fa封装2_93_cout ), .Si(\一位全加器fa封装2_93_si ), .Cin(\一位全加器fa封装2_100_cout [0]),
    .Xi(\一位全加器fa封装2_94_si ), .Yi(\一位全加器fa封装2_100_cout [1]));
  \一位全加器FA封装2  \u_一位全加器fa封装2_94  (
    .Cout(\一位全加器fa封装2_94_cout [0]), .Si(\一位全加器fa封装2_94_si ), .Cin(\一位全加器fa封装2_101_cout ),
    .Xi(\一位全加器fa封装2_95_si ), .Yi(\一位全加器fa封装2_96_si ));
  \一位全加器FA封装2  \u_一位全加器fa封装2_95  (
    .Cout(\一位全加器fa封装2_95_cout ), .Si(\一位全加器fa封装2_95_si ), .Cin(\一位全加器fa封装2_98_si ), .Xi(\一位全加器fa封装2_92_si ),
    .Yi(\一位全加器fa封装2_97_si ));
  \一位全加器FA封装2  \u_一位全加器fa封装2_96  (
    .Cout(\一位全加器fa封装2_94_cout [1]), .Si(\一位全加器fa封装2_96_si ), .Cin(\一位全加器fa封装2_105_cout [0]),
    .Xi(\一位全加器fa封装2_105_cout [2]), .Yi(\一位全加器fa封装2_105_cout [1]));
  \一位全加器FA封装2  \u_一位全加器fa封装2_97  (
    .Cout(\一位全加器fa封装2_98_cout [1]), .Si(\一位全加器fa封装2_97_si ), .Cin(undriven_110), .Xi(undriven_108),
    .Yi(undriven_109));
  shape shape_8 ();
  \一位全加器FA封装2  \u_一位全加器fa封装2_98  (
    .Cout(\一位全加器fa封装2_98_cout [0]), .Si(\一位全加器fa封装2_98_si ), .Cin(1'b0), .Xi(undriven_111), .Yi(undriven_112));
  \一位全加器FA封装2  \u_一位全加器fa封装2_99  (
    .Cout(\一位全加器fa封装2_99_cout ), .Si(\一位全加器fa封装2_99_si ), .Cin(\一位全加器fa封装2_106_cout [0]),
    .Xi(\一位全加器fa封装2_100_si ), .Yi(\一位全加器fa封装2_106_cout [1]));
  \一位全加器FA封装2  \u_一位全加器fa封装2_100  (
    .Cout(\一位全加器fa封装2_100_cout [0]), .Si(\一位全加器fa封装2_100_si ), .Cin(\一位全加器fa封装2_107_cout ),
    .Xi(\一位全加器fa封装2_101_si ), .Yi(\一位全加器fa封装2_104_si ));
  \一位全加器FA封装2  \u_一位全加器fa封装2_101  (
    .Cout(\一位全加器fa封装2_101_cout ), .Si(\一位全加器fa封装2_101_si ), .Cin(\一位全加器fa封装2_105_si ),
    .Xi(\一位全加器fa封装2_102_si ), .Yi(\一位全加器fa封装2_103_si ));
  \一位全加器FA封装2  \u_一位全加器fa封装2_102  (
    .Cout(\一位全加器fa封装2_105_cout [2]), .Si(\一位全加器fa封装2_102_si ), .Cin(undriven_115), .Xi(undriven_113),
    .Yi(undriven_114));
  \一位全加器FA封装2  \u_一位全加器fa封装2_103  (
    .Cout(\一位全加器fa封装2_105_cout [1]), .Si(\一位全加器fa封装2_103_si ), .Cin(undriven_118), .Xi(undriven_116),
    .Yi(undriven_117));
  \一位全加器FA封装2  \u_一位全加器fa封装2_104  (
    .Cout(\一位全加器fa封装2_100_cout [1]), .Si(\一位全加器fa封装2_104_si ), .Cin(\一位全加器fa封装2_112_cout [0]),
    .Xi(\一位全加器fa封装2_112_cout [2]), .Yi(\一位全加器fa封装2_112_cout [1]));
  \一位全加器FA封装2  \u_一位全加器fa封装2_105  (
    .Cout(\一位全加器fa封装2_105_cout [0]), .Si(\一位全加器fa封装2_105_si ), .Cin(1'b0), .Xi(undriven_119),
    .Yi(undriven_120));
  \一位全加器FA封装2  \u_一位全加器fa封装2_106  (
    .Cout(\一位全加器fa封装2_106_cout [0]), .Si(\一位全加器fa封装2_106_si ), .Cin(undriven_125), .Xi(\一位全加器fa封装2_107_si ),
    .Yi(\一位全加器fa封装2_110_si ));
  \一位全加器FA封装2  \u_一位全加器fa封装2_107  (
    .Cout(\一位全加器fa封装2_107_cout ), .Si(\一位全加器fa封装2_107_si ), .Cin(\一位全加器fa封装2_112_si ),
    .Xi(\一位全加器fa封装2_108_si ), .Yi(\一位全加器fa封装2_111_si ));
  \一位全加器FA封装2  \u_一位全加器fa封装2_108  (
    .Cout(\一位全加器fa封装2_112_cout [2]), .Si(\一位全加器fa封装2_108_si ), .Cin(undriven_123), .Xi(undriven_121),
    .Yi(undriven_122));
  \一位全加器FA封装2  \u_一位全加器fa封装2_109  (
    .Cout(\一位全加器fa封装2_109_cout ), .Si(\一位全加器fa封装2_109_si ), .Cin(undriven_131[0]), .Xi(\一位全加器fa封装2_106_si ),
    .Yi(undriven_131[1]));
  \一位全加器FA封装2  \u_一位全加器fa封装2_110  (
    .Cout(\一位全加器fa封装2_106_cout [1]), .Si(\一位全加器fa封装2_110_si ), .Cin(undriven_129[0]), .Xi(undriven_129[2]),
    .Yi(undriven_129[1]));
  \一位全加器FA封装2  \u_一位全加器fa封装2_111  (
    .Cout(\一位全加器fa封装2_112_cout [1]), .Si(\一位全加器fa封装2_111_si ), .Cin(undriven_127), .Xi(undriven_124),
    .Yi(undriven_126));
  \一位全加器FA封装2  \u_一位全加器fa封装2_112  (
    .Cout(\一位全加器fa封装2_112_cout [0]), .Si(\一位全加器fa封装2_112_si ), .Cin(1'b0), .Xi(undriven_128),
    .Yi(undriven_130));
endmodule

module \原码一位乘法  (
  input  [7:0] X,
  input  [7:0] Y,
  output [15:0] \乘积 
);

  wire comparator_1_eq, counter_1_carry, not_1_out, S7, \时钟_out , \清零_out ;
  wire [0:0] SUM_star;
  wire [3:0] Q;
  wire [6:0] SUM1;
  wire [7:0] bitselector_1_out, Yn_1;

  Clock \u_时钟  (.out(\时钟_out ));
  Button \u_清零  (.out(\清零_out ));
  Counter #(.width(4), .max('h9), .ongoal("stay")) counter_1 (
    .Q(Q), .carry(counter_1_carry), .clk(\时钟_out ), .clr(\清零_out ));  // open: load, D, count
  \_8位串行加法器  \u_8位串行加法器_1  (
    .X(\乘积 [15:8]), .Y(bitselector_1_out), .Cin(1'b0), .S({SUM1, SUM_star[0]}), .Cout(S7));  // open: Overflow
  BitSelector #(.width(16), .group(8)) bitselector_1 (.in({X, {8{1'b0}}}), .out(bitselector_1_out), .sel(\乘积 [0]));
  not not_1 (not_1_out, counter_1_carry);
  // Probe on X
  // Probe on Y
  // Probe on \乘积 [15:8]
  Register register_1 (.D({S7, SUM1}), .en(not_1_out), .Q(\乘积 [15:8]), .clk(\时钟_out ), .clr(\清零_out ));
  // Probe on \乘积 
  // Probe on \乘积 [7:0]
  Register Y_2 (.D(Yn_1), .en(not_1_out), .Q(\乘积 [7:0]), .clk(\时钟_out ), .clr(\清零_out ));
  BitSelector #(.width(16), .group(8)) bitselector_2 (
    .in({Y, SUM_star[0], \乘积 [7:1]}), .out(Yn_1), .sel(comparator_1_eq));
  Comparator #(.width(4)) comparator_1 (.a(4'b0000), .b(Q), .eq(comparator_1_eq));  // open: gt, lt

  // Other names for the same wires on the sheet: Yn[7:0] = \乘积 [7:0]; Yn_1_star[7:0] = {SUM_star[0], \乘积 [7:1]};
  //   SUM_star[7:1] = SUM1; SUM1[7] = S7; Y0 = \乘积 [0]; SUM[7:0] = \乘积 [15:8]

  // Notes on the sheet:
  //   ∑
endmodule

module test (
);

  wire X0Y1, X0Y2, X0Y3, X0Y4, X1Y1, X1Y2, X1Y3, X1Y4, X2Y1, X2Y2, X2Y3, X2Y4, X3Y1, X3Y2, X3Y3, X3Y4;

  \一位全加器FA封装3  \u_一位全加器fa封装3_1  ();  // open: Cout, Si, Cin, Xi, Yi
  // 一位全加器FA封装3 一位全加器fa封装3_2: pin names not known; wires that end beside it: X3Y4
  \一位全加器FA封装3  \u_一位全加器fa封装3_3  ();  // open: Cout, Si, Cin, Xi, Yi
  // 一位全加器FA封装3 一位全加器fa封装3_4: pin names not known; wires that end beside it: X3Y3
  // 一位全加器FA封装3 一位全加器fa封装3_5: pin names not known; wires that end beside it: X2Y4
  \一位全加器FA封装3  \u_一位全加器fa封装3_6  ();  // open: Cout, Si, Cin, Xi, Yi
  // 一位全加器FA封装3 一位全加器fa封装3_7: pin names not known; wires that end beside it: X3Y2
  // 一位全加器FA封装3 一位全加器fa封装3_8: pin names not known; wires that end beside it: X2Y3
  // 一位全加器FA封装3 一位全加器fa封装3_9: pin names not known; wires that end beside it: X1Y4
  \一位全加器FA封装3  \u_一位全加器fa封装3_10  ();  // open: Cout, Si, Cin, Xi, Yi
  // 一位全加器FA封装3 一位全加器fa封装3_11: pin names not known; wires that end beside it: X3Y1
  // 一位全加器FA封装3 一位全加器fa封装3_12: pin names not known; wires that end beside it: X2Y2
  // 一位全加器FA封装3 一位全加器fa封装3_13: pin names not known; wires that end beside it: X1Y3
  // 一位全加器FA封装3 一位全加器fa封装3_14: pin names not known; wires that end beside it: X0Y4
  // 一位全加器FA封装3 一位全加器fa封装3_15: pin names not known; wires that end beside it: X2Y1
  // 一位全加器FA封装3 一位全加器fa封装3_16: pin names not known; wires that end beside it: X1Y2
  // 一位全加器FA封装3 一位全加器fa封装3_17: pin names not known; wires that end beside it: X0Y3
  // 一位全加器FA封装3 一位全加器fa封装3_18: pin names not known; wires that end beside it: X1Y1
  // 一位全加器FA封装3 一位全加器fa封装3_19: pin names not known; wires that end beside it: X0Y2
  // 一位全加器FA封装3 一位全加器fa封装3_20: pin names not known; wires that end beside it: X0Y1
endmodule

module \_32位可控加减法器  (
  input  Sub,
  input  [31:0] X,
  input  [31:0] Y,
  output Cout,
  output [31:0] S,
  output Overflow
);

  wire and_1_out, and_2_out, and_3_out, and_4_out, and_5_out, C1, f1, G1, G2, not_1_out, not_2_out,
       not_3_out, P1, P2;
  wire [14:0] xor_1_out;
  wire [15:0] xor_2_out;

  and and_1 (and_1_out, not_1_out, not_2_out, S[31]);
  or or_1 (Overflow, and_1_out, and_2_out);
  and and_2 (and_2_out, X[31], f1, not_3_out);
  or or_2 (Cout, G2, and_4_out, and_3_out);
  and and_3 (and_3_out, P2, P1, Sub);
  and and_4 (and_4_out, P2, G1);
  not not_1 (not_1_out, X[31]);
  not not_2 (not_2_out, f1);
  not not_3 (not_3_out, S[31]);
  or or_3 (C1, G1, and_5_out);
  and and_5 (and_5_out, P1, Sub);
  \_16位快速加法器  \u_16位快速加法器_1  (
    .X(X[31:16]), .Y({f1, xor_1_out}), .Cin(C1), .S(S[31:16]), .G_star(G2), .P_star(P2));  // open: Cout
  \_16位快速加法器  \u_16位快速加法器_2  (
    .X(X[15:0]), .Y(xor_2_out), .Cin(Sub), .S(S[15:0]), .G_star(G1), .P_star(P1));  // open: Cout
  assign {f1, xor_1_out} = Y[31:16] ^ {16{Sub}};  // XOR_Gate xor_1, 16 bits wide
  assign xor_2_out = Y[15:0] ^ {16{Sub}};  // XOR_Gate xor_2, 16 bits wide
  // Probe on X
  // Probe on Y
  // Probe on S
  // Probe on X
  // Probe on Y
  // Probe on S

  // Other names for the same wires on the sheet: in = Sub; S0[15:0] = S[15:0]; S1[15:0] = S[31:16]; fs = S[31];
  //   X0[15:0] = X[15:0]; X1[15:0] = X[31:16]; f0 = X[31]; Y0[15:0] = Y[15:0]; Y1[15:0] = Y[31:16]

  // Notes on the sheet:
  //   输入引脚区
  //   输出引脚区
  //   +
  //   =
  //   有符号加法
  //   +
  //   =
  //   无符号加法
endmodule

module Func0 (
  input  [31:0] X,
  input  [31:0] Y,
  output [31:0] out
);

  Shifter #(.width(32)) shifter_1 (.in(X), .\dist (Y[4:0]), .out(out));
endmodule

module Func1 (
  input  [31:0] X,
  input  [31:0] Y,
  output [31:0] out
);

  Shifter #(.width(32), .shift("ar")) shifter_1 (.in(X), .\dist (Y[4:0]), .out(out));
endmodule

module Func2 (
  input  [31:0] X,
  input  [31:0] Y,
  output [31:0] out
);

  Shifter #(.width(32), .shift("lr")) shifter_1 (.in(X), .\dist (Y[4:0]), .out(out));
endmodule

module Func3 (
  input  [31:0] X,
  input  [31:0] Y,
  output [31:0] out,
  output [31:0] out_2
);

  Multiplier #(.width(32)) multiplier_1 (.a(X), .b(Y), .out(out), .cout(out_2));  // open: cin
endmodule

module Func4 (
  input  [31:0] X,
  input  [31:0] Y,
  output [31:0] out,
  output [31:0] out_2
);

  Divider #(.width(32)) divider_1 (.a(X), .b(Y), .out(out), .rem(out_2));  // open: upper
endmodule

module Func5 (
  input  [31:0] X,
  input  [31:0] Y,
  output out,
  output of,
  output [31:0] s
);

  \_32位可控加减法器  \u_32位可控加减法器_1  (.X(X), .Y(Y), .Sub(1'b0), .S(s), .Cout(out), .Overflow(of));
endmodule

module Func6 (
  input  [31:0] X,
  input  [31:0] Y,
  output out,
  output of,
  output [31:0] s
);

  wire \n32位可控加减法器_1_cout ;

  \_32位可控加减法器  \u_32位可控加减法器_1  (.X(X), .Y(Y), .Sub(1'b1), .S(s), .Cout(\n32位可控加减法器_1_cout ), .Overflow(of));
  not not_1 (out, \n32位可控加减法器_1_cout );
endmodule

module Func7 (
  input  [31:0] X,
  input  [31:0] Y,
  output [31:0] out
);

  assign out = X & Y;  // AND_Gate and_1, 32 bits wide
endmodule

module Func8 (
  input  [31:0] X,
  input  [31:0] Y,
  output [31:0] out
);

  assign out = X | Y;  // OR_Gate or_1, 32 bits wide
endmodule

module Func9 (
  input  [31:0] X,
  input  [31:0] Y,
  output [31:0] out
);

  assign out = X ^ Y;  // XOR_Gate xor_1, 32 bits wide
endmodule

module Func10 (
  input  [31:0] X,
  input  [31:0] Y,
  output [31:0] out
);

  assign out = ~(X | Y);  // NOR_Gate nor_1, 32 bits wide
endmodule

module Func11 (
  input  [31:0] X,
  input  [31:0] Y,
  output [31:0] out
);

  Comparator #(.width(32)) comparator_1 (.a(X), .b(Y), .lt(out[0]));  // open: gt, eq

  assign out[31:1] = {31{1'b0}};
endmodule

module Func12 (
  input  [31:0] X,
  input  [31:0] Y,
  output [31:0] out
);

  wire \n32位可控加减法器_1_cout ;

  \_32位可控加减法器  \u_32位可控加减法器_1  (.X(X), .Y(Y), .Sub(1'b1), .Cout(\n32位可控加减法器_1_cout ));  // open: S, Overflow
  not not_1 (out[0], \n32位可控加减法器_1_cout );

  assign out[31:1] = {31{1'b0}};
endmodule
