// Logisim project cpu-2.circ as structural Verilog: 8 circuits, main circuit cpu
module cpu (
);

  wire alu_1_equal, and_1_out, and_2_out, CLK, controller_1_alusrca, controller_1_beq, controller_1_bne,
       controller_1_iord, controller_1_irwrite, controller_1_memtoreg, controller_1_pcsrc,
       controller_1_pcwrite, controller_1_regdst, mips_ram_1_p3, mips_ram_1_p5, not_1_out, or_1_out, RST, WE3;
  wire [1:0] controller_1_alusrcb;
  wire [3:0] controller_1_alucontrol;
  wire [4:0] A1, A2, A3;
  wire [15:0] \总周期数 , \无条件分支指令数 , \有条件分支成功跳转 , \有条件分支指令数 ;
  wire [31:0] alu_1_result, bit_extender_1_out, mips_ram_1_p2, mips_ram_1_p6, multiplexer_1_out,
       multiplexer_3_out, multiplexer_4_out, multiplexer_5_out, multiplexer_6_out, PC_q, register_1_q,
       register_2_q, register_3_q, register_5_q, registerfile_1_p7, registerfile_1_p8, shifter_1_out,
       SyscallOut;

  Button \u_总复位  (.out(RST));
  Clock clock_1 (.out(CLK));
  Register #(.width(32)) PC (.D(multiplexer_6_out), .en(or_1_out), .Q(PC_q), .clk(CLK), .clr(RST));
  Hex_Digit_Display hex_digit_display_1 (.value(SyscallOut[31:28]));  // open: dp
  Hex_Digit_Display hex_digit_display_2 (.value(SyscallOut[27:24]));  // open: dp
  Multiplexer #(.width(32)) multiplexer_1 (
    .in0(PC_q), .in1(register_5_q), .out(multiplexer_1_out), .sel(controller_1_iord));  // open: en
  Hex_Digit_Display hex_digit_display_3 (.value(SyscallOut[19:16]));  // open: dp
  Hex_Digit_Display hex_digit_display_4 (.value(SyscallOut[23:20]));  // open: dp
  Hex_Digit_Display hex_digit_display_5 (.value(SyscallOut[15:12]));  // open: dp
  Hex_Digit_Display hex_digit_display_6 (.value(SyscallOut[11:8]));  // open: dp
  // MIPS_RAM mips_ram_1: pin names not known; wires that end beside it: multiplexer_1_out[21:2], mips_ram_1_p2, mips_ram_1_p3, CLK, mips_ram_1_p5, mips_ram_1_p6
  Hex_Digit_Display hex_digit_display_7 (.value(SyscallOut[7:4]));  // open: dp
  Hex_Digit_Display hex_digit_display_8 (.value(SyscallOut[3:0]));  // open: dp
  Register #(.width(32)) register_1 (
    .D(mips_ram_1_p6), .en(controller_1_irwrite), .Q({register_1_q[31:26], A1, A2, register_1_q[15:0]}),
    .clk(CLK), .clr(RST));
  Register #(.width(32)) register_2 (.D(mips_ram_1_p6), .Q(register_2_q), .clk(CLK), .clr(RST));  // open: en
  Multiplexer #(.width(5)) multiplexer_2 (
    .in0(A2), .in1(register_1_q[15:11]), .out(A3), .sel(controller_1_regdst));  // open: en
  // Probe on \总周期数 
  // Probe on \无条件分支指令数 
  // Probe on \有条件分支指令数 
  // Probe on \有条件分支成功跳转 
  controller controller_1 (
    .op(register_1_q[31:26]), .func(register_1_q[5:0]), .alucontrol(controller_1_alucontrol), .rst(RST),
    .clk(CLK), .IorD(controller_1_iord), .PcSrc(controller_1_pcsrc), .AluSrcA(controller_1_alusrca),
    .MemToReg(controller_1_memtoreg), .AluSrcB(controller_1_alusrcb), .RegDst(controller_1_regdst),
    .IrWrite(controller_1_irwrite), .PcWrite(controller_1_pcwrite), .RegWrite(WE3), .MemWrite(mips_ram_1_p3),
    .MemRead(mips_ram_1_p5), .BNE(controller_1_bne), .BEQ(controller_1_beq));
  Multiplexer #(.width(32)) multiplexer_3 (
    .in0(register_5_q), .in1(register_2_q), .out(multiplexer_3_out), .sel(controller_1_memtoreg));  // open: en
  assign bit_extender_1_out = {{16{register_1_q[15]}}, register_1_q[15:0]};  // Bit_Extender bit_extender_1
  // RegisterFile registerfile_1: pin names not known; wires that end beside it: multiplexer_3_out, CLK, WE3, A3, A1, A2, registerfile_1_p7, registerfile_1_p8
  Register #(.width(32)) register_3 (.D(registerfile_1_p7), .Q(register_3_q), .clk(CLK), .clr(RST));  // open: en
  Register #(.width(32)) register_4 (.D(registerfile_1_p8), .Q(mips_ram_1_p2), .clk(CLK), .clr(RST));  // open: en
  Multiplexer #(.width(32)) multiplexer_4 (
    .in0(PC_q), .in1(register_3_q), .out(multiplexer_4_out), .sel(controller_1_alusrca));  // open: en
  Shifter #(.width(32)) shifter_1 (.in(bit_extender_1_out), .\dist (5'b00010), .out(shifter_1_out));
  Multiplexer #(.select(2), .width(32)) multiplexer_5 (
    .in0(mips_ram_1_p2), .in1(32'h4), .in2(bit_extender_1_out), .in3(shifter_1_out), .out(multiplexer_5_out),
    .sel(controller_1_alusrcb));  // open: en
  ALU alu_1 (
    .AluOP(controller_1_alucontrol), .X(multiplexer_4_out), .Equal(alu_1_equal), .Result(alu_1_result),
    .Y(multiplexer_5_out));  // open: Signed_Overflow, Result_2, UnSigned_Overflow
  and and_1 (and_1_out, controller_1_bne, not_1_out);
  not not_1 (not_1_out, alu_1_equal);
  and and_2 (and_2_out, controller_1_beq, alu_1_equal);
  Register #(.width(32)) register_5 (.D(alu_1_result), .Q(register_5_q), .clk(CLK), .clr(RST));  // open: en
  or or_1 (or_1_out, controller_1_pcwrite, and_1_out, and_2_out);
  Multiplexer #(.width(32)) multiplexer_6 (
    .in0(alu_1_result), .in1(register_5_q), .out(multiplexer_6_out), .sel(controller_1_pcsrc));  // open: en

  // Notes on the sheet:
  //   数码管输出应该用寄存器锁存，否则显示数据只能一闪而过
  //   可以通过项目增加Logisim库的方式将前几次实验完成的电路作为子电路引入到本电路中使用
  //   指令存储器
  //   数码管输出
  //   总复位信号应将除ROM以外所有存储组件全部清零
  //   寄存器文件
endmodule

module pipline (
);

  wire IR1, IR2, IR3, RST, W1, W2, W3;
  wire [15:0] \load_use次数 , \总周期数 , \插入气泡数 , \无条件分支指令数 , \有条件分支成功跳转 ;
  wire [31:0] SyscallOut;

  Button \u_总复位  (.out(RST));
  Button _1 (.out(IR1));
  Button _2 (.out(IR2));
  Button _3 (.out(IR3));
  LED led_1 (.in(W1));
  LED led_2 (.in(W2));
  LED led_3 (.in(W3));
  Hex_Digit_Display hex_digit_display_1 (.value(SyscallOut[31:28]));  // open: dp
  Hex_Digit_Display hex_digit_display_2 (.value(SyscallOut[27:24]));  // open: dp
  Hex_Digit_Display hex_digit_display_3 (.value(SyscallOut[23:20]));  // open: dp
  Hex_Digit_Display hex_digit_display_4 (.value(SyscallOut[15:12]));  // open: dp
  Hex_Digit_Display hex_digit_display_5 (.value(SyscallOut[19:16]));  // open: dp
  Hex_Digit_Display hex_digit_display_6 (.value(SyscallOut[7:4]));  // open: dp
  Hex_Digit_Display hex_digit_display_7 (.value(SyscallOut[11:8]));  // open: dp
  Hex_Digit_Display hex_digit_display_8 (.value(SyscallOut[3:0]));  // open: dp
  // Probe on \总周期数 
  // Probe on \无条件分支指令数 
  // Probe on \有条件分支成功跳转 
  // Probe on \load_use次数 
  // Probe on \插入气泡数 

  // Notes on the sheet:
  //   中断源
  //   中断等待指示
  //   数码管输出
endmodule

module controller (
  input  [5:0] op,
  input  rst,
  input  [5:0] func,
  input  clk,
  output IorD,
  output PcSrc,
  output AluSrcA,
  output [1:0] AluSrcB,
  output MemToReg,
  output RegDst,
  output IrWrite,
  output PcWrite,
  output RegWrite,
  output MemWrite,
  output MemRead,
  output BEQ,
  output BNE,
  output [3:0] alucontrol
);

  wire opdecoder_1_addi, opdecoder_1_beq, opdecoder_1_bne, opdecoder_1_lw, opdecoder_1_r, opdecoder_1_sw,
       opdecoder_1_syscall;
  wire [1:0] AluOp;
  wire [3:0] hardweired_1_n0, register_1_q;

  Register #(.width(4)) register_1 (.D(hardweired_1_n0), .Q(register_1_q), .clk(clk), .clr(rst));  // open: en
  opdecoder opdecoder_1 (
    .op(op), .func(func), .R(opdecoder_1_r), .lw(opdecoder_1_lw), .sw(opdecoder_1_sw), .beq(opdecoder_1_beq),
    .bne(opdecoder_1_bne), .addi(opdecoder_1_addi), .syscall(opdecoder_1_syscall));
  hardweired hardweired_1 (
    .S3(register_1_q[3]), .S2(register_1_q[2]), .S1(register_1_q[1]), .S0(register_1_q[0]),
    .R(opdecoder_1_r), .LW(opdecoder_1_lw), .SW(opdecoder_1_sw), .BEQ(opdecoder_1_beq),
    .BNE(opdecoder_1_bne), .ADDI(opdecoder_1_addi), .SYSCALL(opdecoder_1_syscall), .N3(hardweired_1_n0[3]),
    .N2(hardweired_1_n0[2]), .N1(hardweired_1_n0[1]), .N0(hardweired_1_n0[0]));
  state1 state1_1 (
    .I3(register_1_q[3]), .I2(register_1_q[2]), .I1(register_1_q[1]), .I0(register_1_q[0]), .IorD(IorD),
    .PcSrc(PcSrc), .AluSrcA(AluSrcA), .AluSrcBh(AluSrcB[1]), .AluSrcBl(AluSrcB[0]), .MemToReg(MemToReg),
    .RegDst(RegDst), .IrWrite(IrWrite), .PcWrite(PcWrite), .RegWrite(RegWrite), .MemWrite(MemWrite),
    .MemRead(MemRead));
  state2 state2_1 (
    .I3(register_1_q[3]), .I2(register_1_q[2]), .I1(register_1_q[1]), .I0(register_1_q[0]), .BEQ(BEQ),
    .BNE(BNE), .AluOph(AluOp[1]), .AluOpl(AluOp[0]));
  aludecoder aludecoder_1 (.func(func), .aluop(AluOp), .alucontrol(alucontrol));
endmodule

module aludecoder (
  input  [5:0] func,
  input  [1:0] aluop,
  output [3:0] alucontrol
);

  wire and_1_out, comparator_1_eq, comparator_2_eq;

  Comparator #(.width(2)) comparator_1 (.a(aluop), .b(2'b10), .eq(comparator_1_eq));  // open: gt, lt
  Comparator #(.width(6)) comparator_2 (.a(func), .b(6'b101010), .eq(comparator_2_eq));  // open: gt, lt
  and and_1 (and_1_out, comparator_1_eq, comparator_2_eq);
  Multiplexer #(.width(4)) multiplexer_1 (.in0(4'b0101), .in1(4'b1011), .out(alucontrol), .sel(and_1_out));  // open: en
endmodule

module opdecoder (
  input  [5:0] op,
  input  [5:0] func,
  output R,
  output lw,
  output sw,
  output beq,
  output bne,
  output addi,
  output syscall
);

  wire and_1_out, and_2_out, comparator_1_eq, comparator_2_eq, comparator_3_eq, comparator_4_eq,
       comparator_10_eq, comparator_11_eq;

  Comparator #(.width(6)) comparator_1 (.a(op), .b({6{1'b0}}), .eq(comparator_1_eq));  // open: gt, lt
  Comparator #(.width(6)) comparator_2 (.a(func), .b(6'b100000), .eq(comparator_2_eq));  // open: gt, lt
  Comparator #(.width(6)) comparator_3 (.a(op), .b({6{1'b0}}), .eq(comparator_3_eq));  // open: gt, lt
  Comparator #(.width(6)) comparator_4 (.a(func), .b(6'b101010), .eq(comparator_4_eq));  // open: gt, lt
  Comparator #(.width(6)) comparator_5 (.a(op), .b(6'b100011), .eq(lw));  // open: gt, lt
  Comparator #(.width(6)) comparator_6 (.a(op), .b(6'b101011), .eq(sw));  // open: gt, lt
  Comparator #(.width(6)) comparator_7 (.a(op), .b(6'b000100), .eq(beq));  // open: gt, lt
  Comparator #(.width(6)) comparator_8 (.a(op), .b(6'b000101), .eq(bne));  // open: gt, lt
  Comparator #(.width(6)) comparator_9 (.a(op), .b(6'b001000), .eq(addi));  // open: gt, lt
  Comparator #(.width(6)) comparator_10 (.a(op), .b({6{1'b0}}), .eq(comparator_10_eq));  // open: gt, lt
  Comparator #(.width(6)) comparator_11 (.a(func), .b(6'b001100), .eq(comparator_11_eq));  // open: gt, lt
  and and_1 (and_1_out, comparator_1_eq, comparator_2_eq);
  and and_2 (and_2_out, comparator_3_eq, comparator_4_eq);
  and and_3 (syscall, comparator_10_eq, comparator_11_eq);
  or or_1 (R, and_1_out, and_2_out);
endmodule

module hardweired (
  input  S3,
  input  S2,
  input  S1,
  input  S0,
  input  R,
  input  LW,
  input  SW,
  input  BEQ,
  input  BNE,
  input  ADDI,
  input  SYSCALL,
  output N3,
  output N2,
  output N1,
  output N0
);

  wire and_1_out, and_2_out, and_3_out, and_4_out, and_5_out, and_6_out, and_7_out, and_8_out, and_9_out,
       and_10_out, and_11_out, and_12_out, and_13_out, and_14_out, and_15_out, and_16_out, and_17_out,
       and_18_out, and_19_out, and_20_out, and_21_out, and_22_out, and_23_out, and_24_out, and_25_out,
       and_26_out, and_27_out, and_28_out, not_1_out, not_2_out, not_3_out, not_4_out, not_5_out, not_6_out,
       not_7_out, not_8_out, not_9_out, not_10_out, not_11_out, not_12_out, not_13_out, not_14_out,
       not_15_out, not_16_out, not_17_out, not_18_out, not_19_out, not_20_out, not_21_out, not_22_out,
       not_23_out, not_24_out, not_25_out, not_26_out, not_27_out, not_28_out, not_29_out, not_30_out,
       not_31_out, not_32_out, not_33_out, not_34_out, not_35_out, not_36_out, not_37_out, not_38_out,
       not_39_out, not_40_out, not_41_out, not_42_out, not_43_out, not_44_out, not_45_out, not_46_out,
       not_47_out, not_48_out, not_49_out, not_50_out, not_51_out, not_52_out, not_53_out, not_54_out,
       not_55_out, not_56_out, not_57_out, not_58_out, not_59_out, not_60_out, not_61_out, not_62_out,
       not_63_out, not_64_out, not_65_out, not_66_out, not_67_out, not_68_out, not_69_out, not_70_out;

  not not_1 (not_1_out, S3);
  not not_2 (not_2_out, S2);
  not not_3 (not_3_out, S1);
  not not_4 (not_4_out, S3);
  not not_5 (not_5_out, S2);
  not not_6 (not_6_out, S1);
  not not_7 (not_7_out, S3);
  not not_8 (not_8_out, S2);
  not not_9 (not_9_out, S1);
  not not_10 (not_10_out, S3);
  not not_11 (not_11_out, S2);
  not not_12 (not_12_out, S1);
  not not_13 (not_13_out, S3);
  not not_14 (not_14_out, S2);
  not not_15 (not_15_out, S1);
  not not_16 (not_16_out, S3);
  not not_17 (not_17_out, S2);
  not not_18 (not_18_out, S1);
  not not_19 (not_19_out, S3);
  not not_20 (not_20_out, S2);
  not not_21 (not_21_out, S1);
  not not_22 (not_22_out, S3);
  not not_23 (not_23_out, S2);
  not not_24 (not_24_out, S1);
  not not_25 (not_25_out, S3);
  not not_26 (not_26_out, S2);
  not not_27 (not_27_out, S3);
  not not_28 (not_28_out, S1);
  not not_29 (not_29_out, S2);
  not not_30 (not_30_out, S1);
  not not_31 (not_31_out, S3);
  not not_32 (not_32_out, S2);
  not not_33 (not_33_out, S1);
  not not_34 (not_34_out, S3);
  not not_35 (not_35_out, S2);
  not not_36 (not_36_out, S1);
  not not_37 (not_37_out, S3);
  not not_38 (not_38_out, S2);
  not not_39 (not_39_out, S1);
  not not_40 (not_40_out, S3);
  not not_41 (not_41_out, S2);
  not not_42 (not_42_out, S1);
  not not_43 (not_43_out, S3);
  not not_44 (not_44_out, S2);
  not not_45 (not_45_out, S0);
  not not_46 (not_46_out, S3);
  not not_47 (not_47_out, S1);
  not not_48 (not_48_out, S3);
  not not_49 (not_49_out, S2);
  not not_50 (not_50_out, S1);
  not not_51 (not_51_out, S0);
  not not_52 (not_52_out, S3);
  not not_53 (not_53_out, S2);
  not not_54 (not_54_out, S1);
  not not_55 (not_55_out, S3);
  not not_56 (not_56_out, S2);
  not not_57 (not_57_out, S1);
  not not_58 (not_58_out, S3);
  not not_59 (not_59_out, S2);
  not not_60 (not_60_out, S1);
  not not_61 (not_61_out, S3);
  not not_62 (not_62_out, S2);
  not not_63 (not_63_out, S1);
  not not_64 (not_64_out, S3);
  not not_65 (not_65_out, S2);
  not not_66 (not_66_out, S1);
  not not_67 (not_67_out, S3);
  not not_68 (not_68_out, S2);
  not not_69 (not_69_out, S0);
  not not_70 (not_70_out, S1);
  and and_1 (and_1_out, not_1_out, not_2_out, not_3_out, S0, BEQ);
  and and_2 (and_2_out, not_4_out, not_5_out, not_6_out, S0, BNE);
  and and_3 (and_3_out, not_7_out, not_8_out, not_9_out, S0, SYSCALL);
  and and_4 (and_4_out, not_10_out, S2, S1, S0, R);
  and and_5 (and_5_out, S3, not_11_out, S1, S0, ADDI);
  and and_6 (and_6_out, S3, S2, not_12_out, S0, SYSCALL);
  and and_7 (and_7_out, not_13_out, not_14_out, not_15_out, S0, ADDI);
  and and_8 (and_8_out, not_16_out, not_17_out, not_18_out, S0, R);
  and and_9 (and_9_out, not_19_out, not_20_out, not_21_out, S0, SW);
  and and_10 (and_10_out, not_22_out, not_23_out, not_24_out, S0, SYSCALL);
  and and_11 (and_11_out, not_25_out, not_26_out, S1, S0, LW);
  and and_12 (and_12_out, not_27_out, S2, not_28_out, S0, SW);
  and and_13 (and_13_out, S3, not_29_out, S1, S0, ADDI);
  and and_14 (and_14_out, S3, S2, not_30_out, S0, SYSCALL);
  and and_15 (and_15_out, not_31_out, not_32_out, not_33_out, S0, R);
  and and_16 (and_16_out, not_34_out, not_35_out, not_36_out, S0, LW);
  and and_17 (and_17_out, not_37_out, not_38_out, not_39_out, S0, BNE);
  and and_18 (and_18_out, not_40_out, not_41_out, not_42_out, S0, ADDI);
  and and_19 (and_19_out, not_43_out, not_44_out, S1, not_45_out, LW);
  and and_20 (and_20_out, not_46_out, S2, not_47_out, S0, SW);
  and and_21 (and_21_out, not_48_out, not_49_out, not_50_out, not_51_out);
  and and_22 (and_22_out, not_52_out, not_53_out, not_54_out, S0, R);
  and and_23 (and_23_out, not_55_out, not_56_out, not_57_out, S0, SW);
  and and_24 (and_24_out, not_58_out, not_59_out, not_60_out, S0, BEQ);
  and and_25 (and_25_out, not_61_out, not_62_out, not_63_out, S0, SYSCALL);
  and and_26 (and_26_out, not_64_out, not_65_out, not_66_out, S0, ADDI);
  and and_27 (and_27_out, not_67_out, not_68_out, S1, not_69_out, LW);
  and and_28 (and_28_out, S3, S2, not_70_out, S0, SYSCALL);
  or or_1 (N3, and_1_out, and_2_out, and_3_out, and_4_out, and_5_out, and_6_out, and_7_out);
  or or_2 (N2, and_8_out, and_9_out, and_10_out, and_11_out, and_12_out, and_13_out, and_14_out);
  or or_3 (N1, and_15_out, and_16_out, and_17_out, and_18_out, and_19_out, and_20_out);
  or or_4 (N0, and_21_out, and_22_out, and_23_out, and_24_out, and_25_out, and_26_out, and_27_out, and_28_out);
endmodule

module state1 (
  input  I3,
  input  I2,
  input  I1,
  input  I0,
  output IorD,
  output PcSrc,
  output AluSrcA,
  output AluSrcBh,
  output AluSrcBl,
  output MemToReg,
  output RegDst,
  output IrWrite,
  output PcWrite,
  output RegWrite,
  output MemWrite,
  output MemRead
);

  wire and_1_out, and_2_out, and_3_out, and_4_out, and_5_out, and_6_out, and_7_out, and_8_out, and_9_out,
       and_10_out, and_11_out, and_12_out, and_13_out, and_14_out, and_15_out, and_16_out, and_21_out,
       and_22_out, and_23_out, and_25_out, and_26_out, not_1_out, not_2_out, not_3_out, not_4_out, not_5_out,
       not_6_out, not_7_out, not_8_out, not_9_out, not_10_out, not_11_out, not_12_out, not_13_out,
       not_14_out, not_15_out, not_16_out, not_17_out, not_18_out, not_19_out, not_20_out, not_21_out,
       not_22_out, not_23_out, not_24_out, not_25_out, not_26_out, not_27_out, not_28_out, not_29_out,
       not_30_out, not_31_out, not_32_out, not_33_out, not_34_out, not_35_out, not_36_out, not_37_out,
       not_38_out, not_39_out, not_40_out, not_41_out, not_42_out, not_43_out, not_44_out, not_45_out,
       not_46_out, not_47_out, not_48_out, not_49_out, not_50_out, not_51_out, not_52_out, not_53_out,
       not_54_out, not_55_out, not_56_out, not_57_out, not_58_out, not_59_out, not_60_out, not_61_out,
       not_62_out, not_63_out, not_64_out, not_65_out;

  not not_1 (not_1_out, I3);
  not not_2 (not_2_out, I2);
  not not_3 (not_3_out, I3);
  not not_4 (not_4_out, I0);
  not not_5 (not_5_out, I2);
  not not_6 (not_6_out, I1);
  not not_7 (not_7_out, I2);
  not not_8 (not_8_out, I0);
  not not_9 (not_9_out, I3);
  not not_10 (not_10_out, I2);
  not not_11 (not_11_out, I0);
  not not_12 (not_12_out, I3);
  not not_13 (not_13_out, I1);
  not not_14 (not_14_out, I3);
  not not_15 (not_15_out, I2);
  not not_16 (not_16_out, I1);
  not not_17 (not_17_out, I2);
  not not_18 (not_18_out, I0);
  not not_19 (not_19_out, I2);
  not not_20 (not_20_out, I3);
  not not_21 (not_21_out, I2);
  not not_22 (not_22_out, I1);
  not not_23 (not_23_out, I3);
  not not_24 (not_24_out, I2);
  not not_25 (not_25_out, I0);
  not not_26 (not_26_out, I3);
  not not_27 (not_27_out, I1);
  not not_28 (not_28_out, I2);
  not not_29 (not_29_out, I3);
  not not_30 (not_30_out, I2);
  not not_31 (not_31_out, I1);
  not not_32 (not_32_out, I0);
  not not_33 (not_33_out, I3);
  not not_34 (not_34_out, I2);
  not not_35 (not_35_out, I1);
  not not_36 (not_36_out, I3);
  not not_37 (not_37_out, I1);
  not not_38 (not_38_out, I0);
  not not_39 (not_39_out, I2);
  not not_40 (not_40_out, I1);
  not not_41 (not_41_out, I0);
  not not_42 (not_42_out, I3);
  not not_43 (not_43_out, I2);
  not not_44 (not_44_out, I1);
  not not_45 (not_45_out, I0);
  not not_46 (not_46_out, I3);
  not not_47 (not_47_out, I2);
  not not_48 (not_48_out, I1);
  not not_49 (not_49_out, I0);
  not not_50 (not_50_out, I3);
  not not_51 (not_51_out, I1);
  not not_52 (not_52_out, I0);
  not not_53 (not_53_out, I2);
  not not_54 (not_54_out, I1);
  not not_55 (not_55_out, I0);
  not not_56 (not_56_out, I1);
  not not_57 (not_57_out, I0);
  not not_58 (not_58_out, I3);
  not not_59 (not_59_out, I0);
  not not_60 (not_60_out, I3);
  not not_61 (not_61_out, I2);
  not not_62 (not_62_out, I1);
  not not_63 (not_63_out, I0);
  not not_64 (not_64_out, I3);
  not not_65 (not_65_out, I2);
  and and_1 (and_1_out, not_1_out, not_2_out, I1, I0);
  or or_1 (IorD, and_1_out, and_2_out);
  and and_2 (and_2_out, not_3_out, I2, I1, not_4_out);
  and and_3 (and_3_out, I3, not_5_out, not_6_out, I0);
  or or_2 (PcSrc, and_3_out, and_4_out);
  and and_4 (and_4_out, I3, not_7_out, I1, not_8_out);
  and and_5 (and_5_out, not_9_out, not_10_out, I1, not_11_out);
  and and_6 (and_6_out, not_12_out, I2, not_13_out, I0);
  and and_7 (and_7_out, not_14_out, I2, I1, I0);
  and and_8 (and_8_out, I3, not_15_out, not_16_out, I0);
  and and_9 (and_9_out, I3, not_17_out, I1, not_18_out);
  and and_10 (and_10_out, I3, not_19_out, I1, I0);
  and and_11 (and_11_out, not_20_out, not_21_out, not_22_out, I0);
  and and_12 (and_12_out, not_23_out, not_24_out, I1, not_25_out);
  and and_13 (and_13_out, not_26_out, I2, not_27_out, I0);
  and and_14 (and_14_out, I3, not_28_out, I1, I0);
  and and_15 (and_15_out, not_29_out, not_30_out, not_31_out, not_32_out);
  or or_3 (AluSrcBl, and_15_out, and_16_out);
  and and_16 (and_16_out, not_33_out, not_34_out, not_35_out, I0);
  and and_17 (MemToReg, not_36_out, I2, not_37_out, not_38_out);
  and and_18 (RegDst, I3, not_39_out, not_40_out, not_41_out);
  and and_19 (IrWrite, not_42_out, not_43_out, not_44_out, not_45_out);
  and and_20 (PcWrite, not_46_out, not_47_out, not_48_out, not_49_out);
  and and_21 (and_21_out, not_50_out, I2, not_51_out, not_52_out);
  or or_4 (RegWrite, and_21_out, and_22_out, and_23_out);
  and and_22 (and_22_out, I3, not_53_out, not_54_out, not_55_out);
  and and_23 (and_23_out, I3, I2, not_56_out, not_57_out);
  and and_24 (MemWrite, not_58_out, I2, I1, not_59_out);
  and and_25 (and_25_out, not_60_out, not_61_out, not_62_out, not_63_out);
  or or_5 (MemRead, and_25_out, and_26_out);
  and and_26 (and_26_out, not_64_out, not_65_out, I1, I0);
  or or_6 (AluSrcA, and_5_out, and_6_out, and_7_out, and_8_out, and_9_out, and_10_out);
  or or_7 (AluSrcBh, and_11_out, and_12_out, and_13_out, and_14_out);
endmodule

module state2 (
  input  I3,
  input  I2,
  input  I1,
  input  I0,
  output BEQ,
  output BNE,
  output AluOph,
  output AluOpl
);

  wire and_4_out, and_5_out, not_1_out, not_2_out, not_3_out, not_4_out, not_5_out, not_6_out, not_7_out,
       not_8_out, not_9_out;

  not not_1 (not_1_out, I2);
  not not_2 (not_2_out, I1);
  not not_3 (not_3_out, I2);
  not not_4 (not_4_out, I0);
  not not_5 (not_5_out, I3);
  not not_6 (not_6_out, I2);
  not not_7 (not_7_out, I1);
  not not_8 (not_8_out, I2);
  not not_9 (not_9_out, I0);
  and and_1 (BEQ, I3, not_1_out, not_2_out, I0);
  and and_2 (BNE, I3, not_3_out, I1, not_4_out);
  and and_3 (AluOph, not_5_out, I2, I1, I0);
  and and_4 (and_4_out, I3, not_6_out, not_7_out, I0);
  or or_1 (AluOpl, and_4_out, and_5_out);
  and and_5 (and_5_out, I3, not_8_out, I1, not_9_out);
endmodule
