// Logisim project cpu.circ as structural Verilog: 6 circuits, main circuit cpu
module cpu (
);

  wire alu_1_equal, and_1_out, and_2_out, CLK, controller_1_alusrca, controller_1_beq, controller_1_bne,
       controller_1_irwrite, controller_1_lord, controller_1_memtoreg, controller_1_pcsrc,
       controller_1_pcwrite, controller_1_regdst, mips_ram_1_p3, mips_ram_1_p5, not_1_out, or_1_out, RST, WE3;
  wire [1:0] controller_1_alusrcb;
  wire [3:0] controller_1_alucontrol;
  wire [4:0] A1, A2, A3;
  wire [15:0] \总周期数 , \无条件分支指令数 , \有条件分支成功跳转 , \有条件分支指令数 ;
  wire [31:0] alu_1_result, bit_extender_1_out, mips_ram_1_p2, mips_ram_1_p6, multiplexer_1_out,
       multiplexer_3_out, multiplexer_4_out, multiplexer_5_out, multiplexer_6_out, PC_q, register_1_q,
       register_2_q, register_3_q, register_5_q, registerfile_1_p7, registerfile_1_p8, shifter_1_out,
       SyscallOut;

  Button \u_总复位  (.out(RST));
  Clock clock_1 (.out(CLK));
  Register #(.width(32)) PC (.D(multiplexer_6_out), .en(or_1_out), .Q(PC_q), .clk(CLK), .clr(RST));
  Hex_Digit_Display hex_digit_display_1 (.value(SyscallOut[31:28]));  // open: dp
  Hex_Digit_Display hex_digit_display_2 (.value(SyscallOut[27:24]));  // open: dp
  Multiplexer #(.width(32)) multiplexer_1 (
    .in0(PC_q), .in1(register_5_q), .out(multiplexer_1_out), .sel(controller_1_lord));  // open: en
  Hex_Digit_Display hex_digit_display_3 (.value(SyscallOut[23:20]));  // open: dp
  Hex_Digit_Display hex_digit_display_4 (.value(SyscallOut[19:16]));  // open: dp
  Hex_Digit_Display hex_digit_display_5 (.value(SyscallOut[15:12]));  // open: dp
  Hex_Digit_Display hex_digit_display_6 (.value(SyscallOut[11:8]));  // open: dp
  // MIPS_RAM mips_ram_1: pin names not known; wires that end beside it: multiplexer_1_out[21:2], mips_ram_1_p2, mips_ram_1_p3, CLK, mips_ram_1_p5, mips_ram_1_p6
  Hex_Digit_Display hex_digit_display_7 (.value(SyscallOut[3:0]));  // open: dp
  Hex_Digit_Display hex_digit_display_8 (.value(SyscallOut[7:4]));  // open: dp
  Register #(.width(32)) register_1 (
    .D(mips_ram_1_p6), .en(controller_1_irwrite), .Q({register_1_q[31:26], A1, A2, register_1_q[15:0]}),
    .clk(CLK), .clr(RST));
  Register #(.width(32)) register_2 (.D(mips_ram_1_p6), .Q(register_2_q), .clk(CLK), .clr(RST));  // open: en
  Multiplexer #(.width(5)) multiplexer_2 (
    .in0(A2), .in1(register_1_q[15:11]), .out(A3), .sel(controller_1_regdst));  // open: en
  // Probe on \总周期数 
  // Probe on \无条件分支指令数 
  // Probe on \有条件分支指令数 
  // Probe on \有条件分支成功跳转 
  controller controller_1 (
    .op(register_1_q[31:26]), .func(register_1_q[5:0]), .lorD(controller_1_lord), .PcSrc(controller_1_pcsrc),
    .AluSrcA(controller_1_alusrca), .AluSrcB(controller_1_alusrcb), .MemToReg(controller_1_memtoreg),
    .RegDst(controller_1_regdst), .IrWrite(controller_1_irwrite), .PcWrite(controller_1_pcwrite),
    .RegWrite(WE3), .MemWrite(mips_ram_1_p3), .MemRead(mips_ram_1_p5), .Beq(controller_1_beq),
    .Bne(controller_1_bne), .alucontrol(controller_1_alucontrol), .rst(RST), .clk(CLK));
  Multiplexer #(.width(32)) multiplexer_3 (
    .in0(register_5_q), .in1(register_2_q), .out(multiplexer_3_out), .sel(controller_1_memtoreg));  // open: en
  assign bit_extender_1_out = {{16{register_1_q[15]}}, register_1_q[15:0]};  // Bit_Extender bit_extender_1
  // RegisterFile registerfile_1: pin names not known; wires that end beside it: multiplexer_3_out, CLK, WE3, A3, A1, A2, registerfile_1_p7, registerfile_1_p8
  Register #(.width(32)) register_3 (.D(registerfile_1_p7), .Q(register_3_q), .clk(CLK), .clr(RST));  // open: en
  Register #(.width(32)) register_4 (.D(registerfile_1_p8), .Q(mips_ram_1_p2), .clk(CLK), .clr(RST));  // open: en
  Multiplexer #(.width(32)) multiplexer_4 (
    .in0(PC_q), .in1(register_3_q), .out(multiplexer_4_out), .sel(controller_1_alusrca));  // open: en
  Shifter #(.width(32)) shifter_1 (.in(bit_extender_1_out), .\dist (5'b00010), .out(shifter_1_out));
  Multiplexer #(.select(2), .width(32)) multiplexer_5 (
    .in0(mips_ram_1_p2), .in1(32'h4), .in2(bit_extender_1_out), .in3(shifter_1_out), .out(multiplexer_5_out),
    .sel(controller_1_alusrcb));  // open: en
  ALU alu_1 (
    .AluOP(controller_1_alucontrol), .X(multiplexer_4_out), .Equal(alu_1_equal), .Result(alu_1_result),
    .Y(multiplexer_5_out));  // open: Signed_Overflow, Result_2, UnSigned_Overflow
  and and_1 (and_1_out, controller_1_bne, not_1_out);
  not not_1 (not_1_out, alu_1_equal);
  and and_2 (and_2_out, controller_1_beq, alu_1_equal);
  Register #(.width(32)) register_5 (.D(alu_1_result), .Q(register_5_q), .clk(CLK), .clr(RST));  // open: en
  or or_1 (or_1_out, controller_1_pcwrite, and_1_out, and_2_out);
  Multiplexer #(.width(32)) multiplexer_6 (
    .in0(alu_1_result), .in1(register_5_q), .out(multiplexer_6_out), .sel(controller_1_pcsrc));  // open: en

  // Notes on the sheet:
  //   数码管输出应该用寄存器锁存，否则显示数据只能一闪而过
  //   可以通过项目增加Logisim库的方式将前几次实验完成的电路作为子电路引入到本电路中使用
  //   指令存储器
  //   数码管输出
  //   总复位信号应将除ROM以外所有存储组件全部清零
  //   寄存器文件
endmodule

module pipline (
);

  wire IR1, IR2, IR3, RST, W1, W2, W3;
  wire [15:0] \load_use次数 , \总周期数 , \插入气泡数 , \无条件分支指令数 , \有条件分支成功跳转 ;
  wire [31:0] SyscallOut;

  Button \u_总复位  (.out(RST));
  Button _1 (.out(IR1));
  Button _2 (.out(IR2));
  Button _3 (.out(IR3));
  LED led_1 (.in(W1));
  LED led_2 (.in(W2));
  LED led_3 (.in(W3));
  Hex_Digit_Display hex_digit_display_1 (.value(SyscallOut[31:28]));  // open: dp
  Hex_Digit_Display hex_digit_display_2 (.value(SyscallOut[27:24]));  // open: dp
  Hex_Digit_Display hex_digit_display_3 (.value(SyscallOut[23:20]));  // open: dp
  Hex_Digit_Display hex_digit_display_4 (.value(SyscallOut[15:12]));  // open: dp
  Hex_Digit_Display hex_digit_display_5 (.value(SyscallOut[19:16]));  // open: dp
  Hex_Digit_Display hex_digit_display_6 (.value(SyscallOut[7:4]));  // open: dp
  Hex_Digit_Display hex_digit_display_7 (.value(SyscallOut[11:8]));  // open: dp
  Hex_Digit_Display hex_digit_display_8 (.value(SyscallOut[3:0]));  // open: dp
  // Probe on \总周期数 
  // Probe on \无条件分支指令数 
  // Probe on \有条件分支成功跳转 
  // Probe on \load_use次数 
  // Probe on \插入气泡数 

  // Notes on the sheet:
  //   中断源
  //   中断等待指示
  //   数码管输出
endmodule

module controller (
  input  [5:0] op,
  input  rst,
  input  [5:0] func,
  input  clk,
  output [3:0] alucontrol,
  output lorD,
  output PcSrc,
  output Bne,
  output AluSrcA,
  output [1:0] AluSrcB,
  output Beq,
  output MemToReg,
  output MemRead,
  output RegDst,
  output MemWrite,
  output IrWrite,
  output RegWrite,
  output PcWrite
);

  wire [1:0] AluOp;
  wire [3:0] addrdecoder_1_addr, multiplexer_1_out, register_1_q, rom_1_data;
  wire [4:4] rom_1_data_2;

  addrdecoder addrdecoder_1 (.op(op), .func(func), .addr(addrdecoder_1_addr));
  Multiplexer #(.width(4)) multiplexer_1 (
    .in0(addrdecoder_1_addr), .in1(rom_1_data), .out(multiplexer_1_out), .sel(rom_1_data_2[4]));  // open: en
  aludecoder aludecoder_1 (.func(func), .aluop(AluOp), .alucontrol(alucontrol));
  Register #(.width(4)) register_1 (.D(multiplexer_1_out), .Q(register_1_q), .clk(clk), .clr(rst));  // open: en
  ROM #(.addrWidth(4), .dataWidth(21)) rom_1 (
    .addr(register_1_q),
    .data({lorD, PcSrc, AluSrcA, AluSrcB, MemToReg, RegDst, IrWrite, PcWrite, RegWrite, MemWrite, MemRead, Beq, Bne, AluOp, rom_1_data_2[4], rom_1_data}));  // open: sel

  // Notes on the sheet:
  //   contents of rom_1 (hex, n*v repeats v):
  //   13211 30000 60013 100214 8810 60016 100410 40058 4810 c0130 c00b0 6001c 810 1d
endmodule

module addrdecoder (
  input  [5:0] op,
  input  [5:0] func,
  output [3:0] addr
);

  wire add, addi, beq, bne, comparator_6_eq, comparator_7_eq, comparator_8_eq, comparator_9_eq,
       comparator_10_eq, comparator_11_eq, lw, or_1_out, slt, sw, syscall;

  Comparator #(.width(6)) comparator_1 (.a(op), .b(6'b100011), .eq(lw));  // open: gt, lt
  Comparator #(.width(6)) comparator_2 (.a(op), .b(6'b101011), .eq(sw));  // open: gt, lt
  Comparator #(.width(6)) comparator_3 (.a(op), .b(6'b000101), .eq(bne));  // open: gt, lt
  Comparator #(.width(6)) comparator_4 (.a(op), .b(6'b000100), .eq(beq));  // open: gt, lt
  Comparator #(.width(6)) comparator_5 (.a(op), .b(6'b001000), .eq(addi));  // open: gt, lt
  Multiplexer #(.width(4)) multiplexer_1 (.in0(4'b0010), .out(addr), .sel(1'b0), .en(lw));  // open: in1
  Multiplexer #(.width(4)) multiplexer_2 (.in0(4'b1001), .out(addr), .sel(1'b0), .en(beq));  // open: in1
  Multiplexer #(.width(4)) multiplexer_3 (.in0(4'b0101), .out(addr), .sel(1'b0), .en(sw));  // open: in1
  Multiplexer #(.width(4)) multiplexer_4 (.in0(4'b1010), .out(addr), .sel(1'b0), .en(bne));  // open: in1
  Comparator #(.width(6)) comparator_6 (.a(op), .b({6{1'b0}}), .eq(comparator_6_eq));  // open: gt, lt
  Comparator #(.width(6)) comparator_7 (.a(func), .b(6'b001100), .eq(comparator_7_eq));  // open: gt, lt
  Comparator #(.width(6)) comparator_8 (.a(op), .b({6{1'b0}}), .eq(comparator_8_eq));  // open: gt, lt
  Comparator #(.width(6)) comparator_9 (.a(func), .b(6'b100000), .eq(comparator_9_eq));  // open: gt, lt
  Comparator #(.width(6)) comparator_10 (.a(op), .b({6{1'b0}}), .eq(comparator_10_eq));  // open: gt, lt
  Comparator #(.width(6)) comparator_11 (.a(func), .b(6'b101010), .eq(comparator_11_eq));  // open: gt, lt
  and and_1 (syscall, comparator_6_eq, comparator_7_eq);
  and and_2 (add, comparator_8_eq, comparator_9_eq);
  and and_3 (slt, comparator_10_eq, comparator_11_eq);
  Multiplexer #(.width(4)) multiplexer_5 (.in0(4'b0111), .out(addr), .sel(1'b0), .en(or_1_out));  // open: in1
  or or_1 (or_1_out, add, slt);
  Multiplexer #(.width(4)) multiplexer_6 (.in0(4'b1011), .out(addr), .sel(1'b0), .en(addi));  // open: in1
  Multiplexer #(.width(4)) multiplexer_7 (.in0(4'b1101), .out(addr), .sel(1'b0), .en(syscall));  // open: in1
endmodule

module aludecoder (
  input  [5:0] func,
  input  [1:0] aluop,
  output [3:0] alucontrol
);

  wire add, aluop0, aluop1, aluop2, and_1_out, and_2_out, slt;

  Comparator #(.width(2)) comparator_1 (.a(2'b00), .b(aluop), .eq(aluop0));  // open: gt, lt
  Comparator #(.width(2)) comparator_2 (.a(2'b01), .b(aluop), .eq(aluop1));  // open: gt, lt
  Comparator #(.width(2)) comparator_3 (.a(2'b10), .b(aluop), .eq(aluop2));  // open: gt, lt
  Comparator #(.width(6)) comparator_4 (.a(func), .b(6'b100000), .eq(add));  // open: gt, lt
  Comparator #(.width(6)) comparator_5 (.a(func), .b(6'b101010), .eq(slt));  // open: gt, lt
  Multiplexer #(.width(4)) multiplexer_1 (.in0(4'b0101), .out(alucontrol), .sel(1'b0), .en(aluop0));  // open: in1
  Multiplexer #(.width(4)) multiplexer_2 (.in0(4'b0101), .out(alucontrol), .sel(1'b0), .en(and_1_out));  // open: in1
  and and_1 (and_1_out, aluop2, add);
  Multiplexer #(.width(4)) multiplexer_3 (.in0(4'b0101), .out(alucontrol), .sel(1'b0), .en(aluop1));  // open: in1
  Multiplexer #(.width(4)) multiplexer_4 (.in0(4'b1011), .out(alucontrol), .sel(1'b0), .en(and_2_out));  // open: in1
  and and_2 (and_2_out, aluop2, slt);
endmodule

module regfile (
);

  // RegisterFile registerfile_1: pin names not known
endmodule
