// Logisim project 三路选择器.circ as structural Verilog: 2 circuits, main circuit main
module main (
  input  I0,
  input  I1,
  input  I2,
  input  S1,
  input  S2,
  output Out
);

  wire mux_2_1_out;

  MUX_2 mux_2_1 (.I0(I0), .I1(I1), .S(S2), .Out(mux_2_1_out));
  MUX_2 mux_2_2 (.I0(mux_2_1_out), .I1(I2), .S(S1), .Out(Out));
endmodule

module MUX_2 (
  input  I0,
  input  I1,
  input  S,
  output Out
);

  wire and_1_out, and_2_out, not_1_out;

  not not_1 (not_1_out, S);
  and and_1 (and_1_out, I1, S);
  and and_2 (and_2_out, I0, not_1_out);
  or or_1 (Out, and_1_out, and_2_out);
endmodule
