// Logisim project 不可重叠1001检测器-Mealy.circ as structural Verilog: 1 circuit, main circuit main
module main (
  input  in_1
);

  wire and_1_out, and_2_out, and_3_out, and_4_out, clock_1_out, j_k_ff_1_q, j_k_ff_1_qn, j_k_ff_2_q,
       j_k_ff_2_qn, not_1_out, not_2_out, or_1_out;

  Clock clock_1 (.out(clock_1_out));
  and and_1 (and_1_out, in_1, j_k_ff_2_qn);
  not not_1 (not_1_out, in_1);
  and and_2 (and_2_out, not_1_out, j_k_ff_2_q);
  not not_2 (not_2_out, in_1);
  or or_1 (or_1_out, j_k_ff_1_qn, in_1);
  J_K_Flip_Flop #(.trigger("falling")) j_k_ff_1 (
    .J(and_1_out), .clk(clock_1_out), .K(and_2_out), .Q(j_k_ff_1_q), .Qn(j_k_ff_1_qn));  // open: preset, en, reset
  J_K_Flip_Flop #(.trigger("falling")) j_k_ff_2 (
    .J(and_3_out), .clk(clock_1_out), .K(or_1_out), .Q(j_k_ff_2_q), .Qn(j_k_ff_2_qn));  // open: preset, en, reset
  and and_3 (and_3_out, j_k_ff_1_q, not_2_out);
  LED led_1 (.in(and_4_out));
  and and_4 (and_4_out, j_k_ff_1_qn, in_1, j_k_ff_2_q);
endmodule
