// Logisim project 不可重叠1001检测器-Moore.circ as structural Verilog: 1 circuit, main circuit main
module main (
  input  in_1
);

  wire and_1_out, and_2_out, and_3_out, and_4_out, and_5_out, and_6_out, and_7_out, and_8_out, clock_1_out,
       j_k_ff_1_q, j_k_ff_1_qn, j_k_ff_2_q, j_k_ff_2_qn, j_k_ff_3_q, j_k_ff_3_qn, not_1_out, not_2_out,
       not_3_out, or_1_out, or_2_out;

  not not_1 (not_1_out, in_1);
  and and_1 (and_1_out, not_1_out, j_k_ff_2_q);
  and and_2 (and_2_out, in_1, j_k_ff_2_qn);
  and and_3 (and_3_out, in_1, j_k_ff_3_q);
  not not_2 (not_2_out, in_1);
  and and_4 (and_4_out, in_1, j_k_ff_1_q, j_k_ff_3_qn);
  and and_5 (and_5_out, j_k_ff_1_q, not_3_out);
  or or_1 (or_1_out, and_2_out, and_3_out);
  not not_3 (not_3_out, in_1);
  and and_6 (and_6_out, not_2_out, j_k_ff_1_qn, j_k_ff_3_qn);
  Clock clock_1 (.out(clock_1_out));
  or or_2 (or_2_out, and_6_out, and_4_out, j_k_ff_3_q);
  and and_7 (and_7_out, j_k_ff_2_q, j_k_ff_1_qn, in_1);
  J_K_Flip_Flop #(.trigger("falling")) j_k_ff_1 (
    .J(or_1_out), .clk(clock_1_out), .K(and_1_out), .Q(j_k_ff_1_q), .Qn(j_k_ff_1_qn));  // open: preset, en, reset
  J_K_Flip_Flop #(.trigger("falling")) j_k_ff_2 (
    .J(and_5_out), .clk(clock_1_out), .K(or_2_out), .Q(j_k_ff_2_q), .Qn(j_k_ff_2_qn));  // open: preset, en, reset
  J_K_Flip_Flop #(.trigger("falling")) j_k_ff_3 (
    .J(and_7_out), .clk(clock_1_out), .K(1'b1), .Q(j_k_ff_3_q), .Qn(j_k_ff_3_qn));  // open: preset, en, reset
  and and_8 (and_8_out, j_k_ff_1_qn, j_k_ff_2_q, j_k_ff_3_q);
  LED led_1 (.in(and_8_out));
endmodule
