// Logisim project 二-十译码器.circ as structural Verilog: 1 circuit, main circuit main
module main (
  input  X1,
  input  X2,
  input  X3,
  input  X4,
  output Y9,
  output Y8,
  output Y7,
  output Y6,
  output Y5,
  output Y4,
  output Y3,
  output Y2,
  output Y1,
  output Y0
);

  wire and_4_out, and_5_out, not_1_out, not_2_out, not_3_out, not_4_out, not_5_out, not_6_out, not_7_out,
       not_8_out, not_9_out, not_10_out, not_11_out, not_12_out, not_13_out, not_14_out, not_15_out,
       not_16_out, not_17_out, not_18_out, not_19_out, not_20_out, not_21_out, not_22_out, not_23_out,
       not_24_out, not_25_out, not_26_out, not_27_out;

  not not_1 (not_1_out, X2);
  not not_2 (not_2_out, X3);
  not not_3 (not_3_out, X2);
  not not_4 (not_4_out, X3);
  not not_5 (not_5_out, X4);
  not not_6 (not_6_out, X1);
  not not_7 (not_7_out, X1);
  not not_8 (not_8_out, X4);
  not not_9 (not_9_out, X2);
  not not_10 (not_10_out, X3);
  not not_11 (not_11_out, X1);
  not not_12 (not_12_out, X3);
  not not_13 (not_13_out, X1);
  not not_14 (not_14_out, X3);
  not not_15 (not_15_out, X4);
  not not_16 (not_16_out, X1);
  not not_17 (not_17_out, X2);
  not not_18 (not_18_out, X1);
  not not_19 (not_19_out, X2);
  not not_20 (not_20_out, X4);
  not not_21 (not_21_out, X1);
  not not_22 (not_22_out, X2);
  not not_23 (not_23_out, X3);
  not not_24 (not_24_out, X1);
  not not_25 (not_25_out, X2);
  not not_26 (not_26_out, X3);
  not not_27 (not_27_out, X4);
  and and_1 (Y9, X1, not_1_out, not_2_out, X4);
  and and_2 (Y8, X1, not_3_out, not_4_out, not_5_out);
  and and_3 (Y7, not_6_out, X2, X3, X4);
  and and_4 (and_4_out, not_7_out, X2, X3, not_8_out);
  or or_1 (Y6, and_4_out, and_5_out);
  and and_5 (and_5_out, X1, not_9_out, not_10_out, X4);
  and and_6 (Y5, not_11_out, X2, not_12_out, X4);
  and and_7 (Y4, not_13_out, X2, not_14_out, not_15_out);
  and and_8 (Y3, not_16_out, not_17_out, X3, X4);
  and and_9 (Y2, not_18_out, not_19_out, X3, not_20_out);
  and and_10 (Y1, not_21_out, not_22_out, not_23_out, X4);
  and and_11 (Y0, not_24_out, not_25_out, not_26_out, not_27_out);
endmodule
