// Logisim project 二进制译码器.circ as structural Verilog: 1 circuit, main circuit main
module main (
  input  A1,
  input  A0,
  output Y0,
  output Y1,
  output Y2,
  output Y3
);

  wire not_1_out, not_2_out, not_3_out, not_4_out;

  not not_1 (not_1_out, A1);
  not not_2 (not_2_out, A0);
  not not_3 (not_3_out, A1);
  not not_4 (not_4_out, A0);
  and and_1 (Y3, A1, A0);
  and and_2 (Y0, not_1_out, not_2_out);
  and and_3 (Y1, not_3_out, A0);
  and and_4 (Y2, A1, not_4_out);
endmodule
