// Logisim project 代码检查电路-Mealy.circ as structural Verilog: 1 circuit, main circuit main
module main (
  input  in_1
);

  wire and_1_out, and_2_out, and_3_out, clock_1_out, j_k_ff_1_q, j_k_ff_2_q, not_1_out, not_2_out, or_1_out,
       or_2_out;

  not not_1 (not_1_out, in_1);
  or or_1 (or_1_out, not_1_out, j_k_ff_2_q);
  and and_1 (and_1_out, in_1, j_k_ff_1_q);
  Clock clock_1 (.out(clock_1_out));
  J_K_Flip_Flop #(.trigger("falling")) j_k_ff_1 (
    .J(in_1), .clk(clock_1_out), .K(or_1_out), .Q(j_k_ff_1_q));  // open: Qn, preset, en, reset
  J_K_Flip_Flop #(.trigger("falling")) j_k_ff_2 (
    .J(and_1_out), .clk(clock_1_out), .K(1'b1), .Q(j_k_ff_2_q));  // open: Qn, preset, en, reset
  and and_2 (and_2_out, j_k_ff_1_q, in_1, j_k_ff_2_q);
  and and_3 (and_3_out, j_k_ff_1_q, j_k_ff_2_q, not_2_out);
  not not_2 (not_2_out, in_1);
  or or_2 (or_2_out, and_2_out, and_3_out);
  LED led_1 (.in(or_2_out));
endmodule
