// Logisim project 代码检查电路-Moore.circ as structural Verilog: 1 circuit, main circuit main
module main (
  input  in_1
);

  wire and_1_out, and_2_out, clock_1_out, j_k_ff_1_q, j_k_ff_1_qn, j_k_ff_2_q, not_1_out, not_2_out, or_1_out;

  not not_1 (not_1_out, in_1);
  or or_1 (or_1_out, not_1_out, j_k_ff_2_q);
  and and_1 (and_1_out, j_k_ff_1_q, in_1);
  Clock clock_1 (.out(clock_1_out));
  J_K_Flip_Flop j_k_ff_1 (
    .J(in_1), .clk(clock_1_out), .K(or_1_out), .Q(j_k_ff_1_q), .Qn(j_k_ff_1_qn));  // open: preset, en, reset
  J_K_Flip_Flop j_k_ff_2 (
    .J(and_1_out), .clk(clock_1_out), .K(j_k_ff_1_qn), .Q(j_k_ff_2_q));  // open: Qn, preset, en, reset
  not not_2 (not_2_out, j_k_ff_1_q);
  and and_2 (and_2_out, not_2_out, j_k_ff_2_q);
  LED led_1 (.in(and_2_out));
endmodule
