// Logisim project 优先编码器.circ as structural Verilog: 1 circuit, main circuit main
module main (
  input  I0,
  input  I1,
  input  I2,
  input  I3,
  input  I4,
  input  I5,
  input  I6,
  input  I7,
  output Y2,
  output Y1,
  output Y0
);

  wire and_1_out, and_2_out, and_3_out, and_4_out, and_5_out, not_1_out, not_2_out, not_3_out, not_4_out,
       not_5_out, not_6_out, not_7_out, not_8_out, not_9_out, not_10_out;

  or or_1 (Y2, I7, I6, I5, I4);
  not not_1 (not_1_out, I5);
  and and_1 (and_1_out, not_1_out, not_2_out, I3);
  not not_2 (not_2_out, I4);
  not not_3 (not_3_out, I5);
  not not_4 (not_4_out, I4);
  and and_2 (and_2_out, not_3_out, not_4_out, I2);
  not not_5 (not_5_out, I6);
  not not_6 (not_6_out, I6);
  not not_7 (not_7_out, I4);
  not not_8 (not_8_out, I6);
  not not_9 (not_9_out, I4);
  not not_10 (not_10_out, I2);
  or or_2 (Y1, I7, I6, and_1_out, and_2_out);
  and and_3 (and_3_out, not_5_out, I5);
  and and_4 (and_4_out, not_6_out, not_7_out, I3);
  and and_5 (and_5_out, not_8_out, not_9_out, not_10_out, I1);
  or or_3 (Y0, I7, and_3_out, and_4_out, and_5_out);
endmodule
