// Logisim project 偶校验编码解码器.circ as structural Verilog: 3 circuits, main circuit main
module main (
  input  in_1,
  input  in_2,
  input  in_3,
  input  in_4,
  input  in_5,
  input  in_6,
  input  in_7,
  input  in_8,
  input  in_9
);

  wire encode_1_a0, encode_1_a1_2, encode_1_a2_2, encode_1_a3_2, encode_1_a4_2, test_1_out, test_2_out;

  Encode encode_1 (
    .A4(in_1), .A3(in_2), .A2(in_3), .A1(in_4), .A4_2(encode_1_a4_2), .A3_2(encode_1_a3_2),
    .A2_2(encode_1_a2_2), .A1_2(encode_1_a1_2), .A0(encode_1_a0));
  Test test_1 (.A4(in_5), .A3(in_6), .A2(in_7), .A1(in_8), .A0(in_9), .Out(test_1_out));
  Test test_2 (
    .A4(encode_1_a4_2), .A3(encode_1_a3_2), .A2(encode_1_a2_2), .A1(encode_1_a1_2), .A0(encode_1_a0),
    .Out(test_2_out));
  LED led_1 (.in(test_2_out));
  LED led_2 (.in(test_1_out));
endmodule

module Encode (
  input  A4,
  input  A3,
  input  A2,
  input  A1,
  output A4_2,
  output A3_2,
  output A2_2,
  output A1_2,
  output A0
);

  wire and_1_out, and_2_out, and_3_out, and_4_out, and_5_out, and_6_out, and_7_out, and_8_out, not_1_out,
       not_2_out, not_3_out, not_4_out, not_5_out, not_6_out, not_7_out, not_8_out, not_9_out, not_10_out,
       not_11_out, not_12_out, not_13_out, not_14_out, not_15_out, not_16_out;

  not not_1 (not_1_out, A4);
  not not_2 (not_2_out, A3);
  not not_3 (not_3_out, A2);
  not not_4 (not_4_out, A4);
  not not_5 (not_5_out, A3);
  not not_6 (not_6_out, A1);
  not not_7 (not_7_out, A4);
  not not_8 (not_8_out, A2);
  not not_9 (not_9_out, A1);
  not not_10 (not_10_out, A4);
  not not_11 (not_11_out, A3);
  not not_12 (not_12_out, A2);
  not not_13 (not_13_out, A1);
  not not_14 (not_14_out, A3);
  not not_15 (not_15_out, A2);
  not not_16 (not_16_out, A1);
  and and_1 (and_1_out, not_1_out, not_2_out, not_3_out, A1);
  and and_2 (and_2_out, not_4_out, not_5_out, A2, not_6_out);
  and and_3 (and_3_out, not_7_out, A3, not_8_out, not_9_out);
  and and_4 (and_4_out, not_10_out, A3, A2, A1);
  and and_5 (and_5_out, A4, not_11_out, not_12_out, not_13_out);
  and and_6 (and_6_out, A4, not_14_out, A2, A1);
  and and_7 (and_7_out, A4, A3, not_15_out, A1);
  and and_8 (and_8_out, A4, A3, A2, not_16_out);
  or or_1 (A0, and_1_out, and_2_out, and_3_out, and_4_out, and_5_out, and_6_out, and_7_out, and_8_out);

  assign A1_2 = A1;
  assign A2_2 = A2;
  assign A3_2 = A3;
  assign A4_2 = A4;
endmodule

module Test (
  input  A4,
  input  A3,
  input  A2,
  input  A1,
  input  A0,
  output Out
);

  wire and_1_out, and_2_out, and_3_out, and_4_out, and_5_out, and_6_out, and_7_out, and_8_out, and_9_out,
       and_10_out, and_11_out, and_12_out, and_13_out, and_14_out, and_15_out, and_16_out, and_17_out,
       and_18_out, and_19_out, and_20_out, and_21_out, and_22_out, and_23_out, and_24_out, and_25_out,
       and_26_out, and_27_out, and_28_out, and_29_out, and_30_out, and_31_out, and_32_out, and_33_out,
       and_34_out, and_35_out, and_36_out, and_37_out, and_38_out, and_39_out, and_40_out, and_41_out,
       and_42_out, and_43_out, and_44_out, and_45_out, and_46_out, and_47_out, and_48_out, and_49_out,
       and_50_out, and_51_out, and_52_out, and_53_out, and_54_out, and_55_out, and_56_out, and_57_out,
       and_58_out, and_59_out, and_60_out, and_61_out, and_62_out, and_63_out, and_64_out, not_1_out,
       not_2_out, not_3_out, not_4_out, not_5_out, not_6_out, not_7_out, not_8_out, not_9_out, not_10_out,
       not_11_out, not_12_out, not_13_out, not_14_out, not_15_out, not_16_out, not_17_out, not_18_out,
       not_19_out, not_20_out, not_21_out, not_22_out, not_23_out, not_24_out, not_25_out, not_26_out,
       not_27_out, not_28_out, not_29_out, not_30_out, not_31_out, not_32_out, not_33_out, not_34_out,
       not_35_out, not_36_out, not_37_out, not_38_out, not_39_out, not_40_out, or_1_out, or_2_out, or_3_out,
       or_4_out, or_5_out, or_6_out, or_7_out, or_8_out, or_9_out, or_10_out, or_11_out, or_12_out,
       or_13_out, or_14_out;

  not not_1 (not_1_out, A4);
  not not_2 (not_2_out, A3);
  not not_3 (not_3_out, A4);
  not not_4 (not_4_out, A3);
  not not_5 (not_5_out, A4);
  not not_6 (not_6_out, A3);
  not not_7 (not_7_out, A4);
  not not_8 (not_8_out, A3);
  not not_9 (not_9_out, A4);
  not not_10 (not_10_out, A4);
  not not_11 (not_11_out, A4);
  not not_12 (not_12_out, A4);
  not not_13 (not_13_out, A3);
  not not_14 (not_14_out, A3);
  not not_15 (not_15_out, A3);
  not not_16 (not_16_out, A3);
  and and_1 (and_1_out, not_1_out, not_2_out);
  not not_17 (not_17_out, A2);
  not not_18 (not_18_out, A1);
  and and_2 (and_2_out, not_3_out, not_4_out);
  not not_19 (not_19_out, A2);
  not not_20 (not_20_out, A0);
  and and_3 (and_3_out, not_5_out, not_6_out);
  not not_21 (not_21_out, A1);
  not not_22 (not_22_out, A0);
  and and_4 (and_4_out, not_7_out, not_8_out);
  and and_5 (and_5_out, not_9_out, A3);
  not not_23 (not_23_out, A2);
  not not_24 (not_24_out, A1);
  not not_25 (not_25_out, A0);
  and and_6 (and_6_out, not_10_out, A3);
  not not_26 (not_26_out, A2);
  and and_7 (and_7_out, not_11_out, A3);
  not not_27 (not_27_out, A1);
  and and_8 (and_8_out, not_12_out, A3);
  not not_28 (not_28_out, A0);
  and and_9 (and_9_out, A4, not_13_out);
  not not_29 (not_29_out, A2);
  not not_30 (not_30_out, A1);
  not not_31 (not_31_out, A0);
  and and_10 (and_10_out, A4, not_14_out);
  not not_32 (not_32_out, A2);
  and and_11 (and_11_out, A4, not_15_out);
  not not_33 (not_33_out, A1);
  and and_12 (and_12_out, A4, not_16_out);
  not not_34 (not_34_out, A0);
  and and_13 (and_13_out, A4, A3);
  not not_35 (not_35_out, A2);
  not not_36 (not_36_out, A1);
  and and_14 (and_14_out, A4, A3);
  not not_37 (not_37_out, A2);
  not not_38 (not_38_out, A0);
  and and_15 (and_15_out, A4, A3);
  not not_39 (not_39_out, A1);
  not not_40 (not_40_out, A0);
  and and_16 (and_16_out, A4, A3);
  and and_17 (and_17_out, and_1_out, not_17_out);
  and and_18 (and_18_out, and_17_out, and_19_out);
  and and_19 (and_19_out, not_18_out, A0);
  and and_20 (and_20_out, and_2_out, not_19_out);
  and and_21 (and_21_out, and_20_out, and_22_out);
  and and_22 (and_22_out, A1, not_20_out);
  and and_23 (and_23_out, and_3_out, A2);
  and and_24 (and_24_out, and_23_out, and_25_out);
  and and_25 (and_25_out, not_21_out, not_22_out);
  and and_26 (and_26_out, and_4_out, A2);
  and and_27 (and_27_out, and_26_out, and_28_out);
  and and_28 (and_28_out, A1, A0);
  and and_29 (and_29_out, and_5_out, not_23_out);
  and and_30 (and_30_out, and_29_out, and_31_out);
  and and_31 (and_31_out, not_24_out, not_25_out);
  and and_32 (and_32_out, and_6_out, not_26_out);
  and and_33 (and_33_out, and_32_out, and_34_out);
  and and_34 (and_34_out, A1, A0);
  and and_35 (and_35_out, and_7_out, A2);
  and and_36 (and_36_out, and_35_out, and_37_out);
  and and_37 (and_37_out, not_27_out, A0);
  and and_38 (and_38_out, and_8_out, A2);
  and and_39 (and_39_out, and_38_out, and_40_out);
  and and_40 (and_40_out, A1, not_28_out);
  and and_41 (and_41_out, and_9_out, not_29_out);
  and and_42 (and_42_out, and_41_out, and_43_out);
  and and_43 (and_43_out, not_30_out, not_31_out);
  and and_44 (and_44_out, and_10_out, not_32_out);
  and and_45 (and_45_out, and_44_out, and_46_out);
  and and_46 (and_46_out, A1, A0);
  and and_47 (and_47_out, and_11_out, A2);
  and and_48 (and_48_out, and_47_out, and_49_out);
  and and_49 (and_49_out, not_33_out, A0);
  and and_50 (and_50_out, and_12_out, A2);
  and and_51 (and_51_out, and_50_out, and_52_out);
  and and_52 (and_52_out, A1, not_34_out);
  and and_53 (and_53_out, and_13_out, not_35_out);
  and and_54 (and_54_out, and_53_out, and_55_out);
  and and_55 (and_55_out, not_36_out, A0);
  and and_56 (and_56_out, and_14_out, not_37_out);
  and and_57 (and_57_out, and_56_out, and_58_out);
  and and_58 (and_58_out, A1, not_38_out);
  and and_59 (and_59_out, and_15_out, A2);
  and and_60 (and_60_out, and_59_out, and_61_out);
  and and_61 (and_61_out, not_39_out, not_40_out);
  and and_62 (and_62_out, and_16_out, A2);
  and and_63 (and_63_out, and_62_out, and_64_out);
  and and_64 (and_64_out, A1, A0);
  or or_1 (or_1_out, and_18_out, and_21_out);
  or or_2 (or_2_out, and_24_out, and_27_out);
  or or_3 (or_3_out, and_30_out, and_33_out);
  or or_4 (or_4_out, and_36_out, and_39_out);
  or or_5 (or_5_out, and_42_out, and_45_out);
  or or_6 (or_6_out, and_48_out, and_51_out);
  or or_7 (or_7_out, and_54_out, and_57_out);
  or or_8 (or_8_out, and_60_out, and_63_out);
  or or_9 (or_9_out, or_1_out, or_2_out);
  or or_10 (or_10_out, or_3_out, or_4_out);
  or or_11 (or_11_out, or_5_out, or_6_out);
  or or_12 (or_12_out, or_7_out, or_8_out);
  or or_13 (or_13_out, or_9_out, or_10_out);
  or or_14 (or_14_out, or_11_out, or_12_out);
  or or_15 (Out, or_13_out, or_14_out);
endmodule
