// Logisim project 可重叠1001检测器-Mealy.circ as structural Verilog: 1 circuit, main circuit main
module main (
  input  in_1
);

  wire and_1_out, and_2_out, and_3_out, clock_1_out, j_k_ff_1_q, j_k_ff_1_qn, j_k_ff_2_q, not_1_out,
       not_2_out, or_1_out;

  Clock clock_1 (.out(clock_1_out));
  not not_1 (not_1_out, in_1);
  and and_1 (and_1_out, not_1_out, j_k_ff_2_q);
  not not_2 (not_2_out, in_1);
  or or_1 (or_1_out, j_k_ff_1_qn, in_1);
  J_K_Flip_Flop #(.trigger("falling")) j_k_ff_1 (
    .J(in_1), .clk(clock_1_out), .K(and_1_out), .Q(j_k_ff_1_q), .Qn(j_k_ff_1_qn));  // open: preset, en, reset
  and and_2 (and_2_out, j_k_ff_1_q, not_2_out);
  J_K_Flip_Flop #(.trigger("falling")) j_k_ff_2 (
    .J(and_2_out), .clk(clock_1_out), .K(or_1_out), .Q(j_k_ff_2_q));  // open: Qn, preset, en, reset
  LED led_1 (.in(and_3_out));
  and and_3 (and_3_out, j_k_ff_1_qn, in_1, j_k_ff_2_q);
endmodule
