// Logisim project 四位二进制加法器.circ as structural Verilog: 3 circuits, main circuit main
module main (
  input  A1,
  input  A1_2,
  input  A2,
  input  A2_2,
  input  A3,
  input  A3_2,
  input  A4,
  input  A4_2,
  input  B1,
  input  B1_2,
  input  B2,
  input  B2_2,
  input  B3,
  input  B3_2,
  input  B4,
  input  B4_2,
  input  Cin,
  input  Cin_2,
  output Cout,
  output S1,
  output Cout_2,
  output S2,
  output S1_2,
  output S2_2,
  output S3,
  output S3_2,
  output S4,
  output S4_2
);

  wire adder_1_cout, adder_2_1_cout, adder_2_cout, adder_3_cout;

  Adder adder_1 (.A(A3_2), .B(B3_2), .Cin(adder_2_cout), .S(S3), .Cout(adder_1_cout));
  Adder adder_2 (.A(A4_2), .B(B4_2), .Cin(Cin_2), .S(S4_2), .Cout(adder_2_cout));
  Hex_Digit_Display hex_digit_display_1 (.value({3'b000, Cout}));  // open: dp
  Adder adder_3 (.A(A2_2), .B(B2_2), .Cin(adder_1_cout), .S(S2), .Cout(adder_3_cout));
  Hex_Digit_Display hex_digit_display_2 (.value({S1, S2, S3, S4_2}));  // open: dp
  Adder adder_4 (.A(A1_2), .B(B1_2), .Cin(adder_3_cout), .S(S1), .Cout(Cout));
  Hex_Digit_Display hex_digit_display_3 (.value({3'b000, Cout_2}));  // open: dp
  Hex_Digit_Display hex_digit_display_4 (.value({S1_2, S2_2, S3_2, S4}));  // open: dp
  Adder_2 adder_2_1 (.A1(A3), .A2(A4), .B1(B3), .B2(B4), .Cin(Cin), .Cout(adder_2_1_cout), .S1(S3_2), .S2(S4));
  Adder_2 adder_2_2 (.A1(A1), .A2(A2), .B1(B1), .B2(B2), .Cin(adder_2_1_cout), .Cout(Cout_2), .S1(S1_2), .S2(S2_2));
endmodule

module Adder (
  input  A,
  input  B,
  input  Cin,
  output S,
  output Cout
);

  wire and_1_out, and_2_out, and_3_out, and_4_out, and_5_out, and_6_out, and_7_out, and_8_out, and_9_out,
       and_10_out, and_11_out, not_1_out, not_2_out, not_3_out, not_4_out, not_5_out, not_6_out, or_1_out,
       or_3_out, or_4_out;

  not not_1 (not_1_out, A);
  not not_2 (not_2_out, B);
  not not_3 (not_3_out, A);
  not not_4 (not_4_out, B);
  and and_1 (and_1_out, B, Cin);
  and and_2 (and_2_out, A, Cin);
  and and_3 (and_3_out, not_1_out, not_2_out);
  and and_4 (and_4_out, not_3_out, B);
  not not_5 (not_5_out, Cin);
  and and_5 (and_5_out, A, not_4_out);
  not not_6 (not_6_out, Cin);
  and and_6 (and_6_out, A, B);
  or or_1 (or_1_out, and_1_out, and_2_out);
  and and_7 (and_7_out, A, B);
  and and_8 (and_8_out, and_3_out, Cin);
  and and_9 (and_9_out, and_4_out, not_5_out);
  and and_10 (and_10_out, and_5_out, not_6_out);
  and and_11 (and_11_out, and_6_out, Cin);
  or or_2 (Cout, or_1_out, and_7_out);
  or or_3 (or_3_out, and_8_out, and_9_out);
  or or_4 (or_4_out, and_10_out, and_11_out);
  or or_5 (S, or_3_out, or_4_out);
endmodule

module Adder_2 (
  input  A1,
  input  A2,
  input  B1,
  input  B2,
  input  Cin,
  output Cout,
  output S1,
  output S2
);

  wire adder_2_cout;

  Adder adder_1 (.A(A1), .B(B1), .Cin(adder_2_cout), .S(S1), .Cout(Cout));
  Adder adder_2 (.A(A2), .B(B2), .Cin(Cin), .S(S2), .Cout(adder_2_cout));
endmodule
