// Logisim project 带使能端的2-4线译码器.circ as structural Verilog: 1 circuit, main circuit main
module main (
  input  S,
  input  A1,
  input  A0,
  output Y0,
  output Y1,
  output Y2,
  output Y3
);

  wire and_1_out, and_2_out, and_3_out, and_4_out, not_1_out, not_2_out, not_3_out, not_4_out, not_5_out,
       not_6_out, not_7_out, not_8_out;

  not not_1 (not_1_out, S);
  not not_2 (not_2_out, A1);
  not not_3 (not_3_out, S);
  not not_4 (not_4_out, A1);
  not not_5 (not_5_out, S);
  not not_6 (not_6_out, S);
  and and_1 (and_1_out, not_1_out, not_2_out);
  not not_7 (not_7_out, A0);
  and and_2 (and_2_out, not_3_out, not_4_out);
  and and_3 (and_3_out, not_5_out, A1);
  not not_8 (not_8_out, A0);
  and and_4 (and_4_out, not_6_out, A1);
  and and_5 (Y0, and_1_out, not_7_out);
  and and_6 (Y1, and_2_out, A0);
  and and_7 (Y2, and_3_out, not_8_out);
  and and_8 (Y3, and_4_out, A0);
endmodule
