// Logisim project 普通的二进制编码选择器.circ as structural Verilog: 1 circuit, main circuit main
module main (
  input  I0,
  input  I1,
  input  I2,
  input  I3,
  input  I4,
  input  I5,
  input  I6,
  input  I7,
  output Y2,
  output Y1,
  output Y0
);

  wire or_1_out, or_2_out, or_3_out, or_4_out, or_5_out, or_6_out;

  or or_1 (or_1_out, I4, I5);
  or or_2 (or_2_out, I6, I7);
  or or_3 (or_3_out, I2, I3);
  or or_4 (or_4_out, I6, I7);
  or or_5 (or_5_out, I1, I3);
  or or_6 (or_6_out, I5, I7);
  or or_7 (Y2, or_1_out, or_2_out);
  or or_8 (Y1, or_3_out, or_4_out);
  or or_9 (Y0, or_5_out, or_6_out);
endmodule
