// Logisim project 模6计数器.circ as structural Verilog: 1 circuit, main circuit main
module main (
  input  in_1
);

  wire and_1_out, and_2_out, and_3_out, and_4_out, clock_1_out, j_k_ff_1_q, j_k_ff_1_qn, j_k_ff_2_q,
       j_k_ff_2_qn, j_k_ff_3_q, j_k_ff_3_qn, not_1_out, or_1_out, or_2_out, xor_1_out, xor_2_out, xor_3_out;

  xor xor_1 (xor_1_out, in_1, j_k_ff_2_q);
  xor xor_2 (xor_2_out, in_1, j_k_ff_1_q);
  xor xor_3 (xor_3_out, in_1, j_k_ff_3_q);
  or or_1 (or_1_out, j_k_ff_2_qn, xor_3_out);
  or or_2 (or_2_out, xor_1_out, j_k_ff_3_q);
  and and_1 (and_1_out, xor_3_out, j_k_ff_1_q);
  and and_2 (and_2_out, xor_1_out, j_k_ff_1_qn);
  Clock clock_1 (.out(clock_1_out));
  J_K_Flip_Flop #(.trigger("falling")) j_k_ff_1 (
    .J(or_1_out), .clk(clock_1_out), .K(or_2_out), .Q(j_k_ff_1_q), .Qn(j_k_ff_1_qn));  // open: preset, en, reset
  J_K_Flip_Flop #(.trigger("falling")) j_k_ff_2 (
    .J(xor_2_out), .clk(clock_1_out), .K(and_1_out), .Q(j_k_ff_2_q), .Qn(j_k_ff_2_qn));  // open: preset, en, reset
  J_K_Flip_Flop #(.trigger("falling")) j_k_ff_3 (
    .J(and_2_out), .clk(clock_1_out), .K(xor_2_out), .Q(j_k_ff_3_q), .Qn(j_k_ff_3_qn));  // open: preset, en, reset
  not not_1 (not_1_out, in_1);
  LED led_1 (.in(and_3_out));
  and and_3 (and_3_out, in_1, j_k_ff_1_qn, j_k_ff_2_qn, j_k_ff_3_qn);
  and and_4 (and_4_out, not_1_out, j_k_ff_1_q, j_k_ff_2_q, j_k_ff_3_q);
  LED led_2 (.in(and_4_out));
endmodule
