// Logisim project 第三次实验.circ as structural Verilog: 4 circuits, main circuit main
module main (
);

  wire CLR_out, CPd_out, CPu_out, d_ff_1_q, d_ff_2_q, d_ff_3_q, d_ff_4_q, \n4位二进制加法器_1_y1 , \n4位二进制加法器_1_y2 ,
       \n4位二进制加法器_1_y3 , \n4位二进制加法器_1_y4 , \n4位二进制加法器_1_z , \n4位二进制转8421码_1_y0 , \n4位二进制转8421码_1_y1 ,
       \n4位二进制转8421码_1_y2 , \n4位二进制转8421码_1_y3 , \n4位二进制转8421码_1_y4 , \n4位二进制转8421码_1_y5 ,
       \n4位二进制转8421码_1_y6 , \n4位二进制转8421码_1_y7 , \n7段译码器_1_a_2 , \n7段译码器_1_b_2 , \n7段译码器_1_c_2 ,
       \n7段译码器_1_d_2 , \n7段译码器_1_e , \n7段译码器_1_f , \n7段译码器_1_g , \n7段译码器_2_a_2 , \n7段译码器_2_b_2 ,
       \n7段译码器_2_c_2 , \n7段译码器_2_d_2 , \n7段译码器_2_e , \n7段译码器_2_f , \n7段译码器_2_g , nor_1_out;

  Button CLR (.out(CLR_out));
  Clock CPu (.out(CPu_out));
  Clock CPd (.out(CPd_out));
  \_4位二进制加法器  \u_4位二进制加法器_1  (
    .CPu(CPu_out), .CPd(CPd_out), .X4(d_ff_1_q), .X3(d_ff_2_q), .X2(d_ff_3_q), .X1(d_ff_4_q),
    .Y4(\n4位二进制加法器_1_y4 ), .Y3(\n4位二进制加法器_1_y3 ), .Y2(\n4位二进制加法器_1_y2 ), .Y1(\n4位二进制加法器_1_y1 ),
    .Z(\n4位二进制加法器_1_z ));
  nor nor_1 (nor_1_out, CPu_out, CPd_out);
  D_Flip_Flop d_ff_1 (.clk(nor_1_out), .D(\n4位二进制加法器_1_y4 ), .Q(d_ff_1_q), .reset(CLR_out));  // open: Qn, preset, en
  D_Flip_Flop d_ff_2 (.clk(nor_1_out), .D(\n4位二进制加法器_1_y3 ), .Q(d_ff_2_q), .reset(CLR_out));  // open: Qn, preset, en
  D_Flip_Flop d_ff_3 (.clk(nor_1_out), .D(\n4位二进制加法器_1_y2 ), .Q(d_ff_3_q), .reset(CLR_out));  // open: Qn, preset, en
  D_Flip_Flop d_ff_4 (.clk(nor_1_out), .D(\n4位二进制加法器_1_y1 ), .Q(d_ff_4_q), .reset(CLR_out));  // open: Qn, preset, en
  \_4位二进制转8421码  \u_4位二进制转8421码_1  (
    .X3(d_ff_1_q), .X2(d_ff_2_q), .X1(d_ff_3_q), .X0(d_ff_4_q), .Y7(\n4位二进制转8421码_1_y7 ),
    .Y6(\n4位二进制转8421码_1_y6 ), .Y5(\n4位二进制转8421码_1_y5 ), .Y4(\n4位二进制转8421码_1_y4 ), .Y3(\n4位二进制转8421码_1_y3 ),
    .Y2(\n4位二进制转8421码_1_y2 ), .Y1(\n4位二进制转8421码_1_y1 ), .Y0(\n4位二进制转8421码_1_y0 ));
  LED led_1 (.in(\n4位二进制加法器_1_z ));
  \_7段译码器  \u_7段译码器_1  (
    .D(\n4位二进制转8421码_1_y7 ), .C(\n4位二进制转8421码_1_y6 ), .B(\n4位二进制转8421码_1_y5 ), .A(\n4位二进制转8421码_1_y4 ),
    .a_2(\n7段译码器_1_a_2 ), .b_2(\n7段译码器_1_b_2 ), .c_2(\n7段译码器_1_c_2 ), .d_2(\n7段译码器_1_d_2 ), .e(\n7段译码器_1_e ),
    .f(\n7段译码器_1_f ), .g(\n7段译码器_1_g ));
  \_7段译码器  \u_7段译码器_2  (
    .D(\n4位二进制转8421码_1_y3 ), .C(\n4位二进制转8421码_1_y2 ), .B(\n4位二进制转8421码_1_y1 ), .A(\n4位二进制转8421码_1_y0 ),
    .a_2(\n7段译码器_2_a_2 ), .b_2(\n7段译码器_2_b_2 ), .c_2(\n7段译码器_2_c_2 ), .d_2(\n7段译码器_2_d_2 ), .e(\n7段译码器_2_e ),
    .f(\n7段译码器_2_f ), .g(\n7段译码器_2_g ));
  _7_Segment_Display u_7_segment_display_1 (
    .g(\n7段译码器_1_g ), .f(\n7段译码器_1_f ), .a(\n7段译码器_1_a_2 ), .b(\n7段译码器_1_b_2 ), .e(\n7段译码器_1_e ),
    .d(\n7段译码器_1_d_2 ), .c(\n7段译码器_1_c_2 ));  // open: dp
  _7_Segment_Display u_7_segment_display_2 (
    .g(\n7段译码器_2_g ), .f(\n7段译码器_2_f ), .a(\n7段译码器_2_a_2 ), .b(\n7段译码器_2_b_2 ), .e(\n7段译码器_2_e ),
    .d(\n7段译码器_2_d_2 ), .c(\n7段译码器_2_c_2 ));  // open: dp
endmodule

module \_4位二进制加法器  (
  input  CPu,
  input  CPd,
  input  X4,
  input  X3,
  input  X2,
  input  X1,
  output Y4,
  output Y3,
  output Y2,
  output Y1,
  output Z
);

  wire and_1_out, and_2_out, and_3_out, and_4_out, and_5_out, and_6_out, and_7_out, and_8_out, and_9_out,
       and_10_out, and_11_out, and_12_out, and_13_out, and_14_out, and_15_out, and_16_out, and_17_out,
       and_18_out, and_19_out, and_20_out, and_21_out, and_22_out, and_23_out, and_24_out, and_25_out,
       and_26_out, not_1_out, not_2_out, not_3_out, not_4_out, not_5_out, not_6_out, not_7_out, not_8_out,
       not_9_out, not_10_out, not_11_out, not_12_out, not_13_out, not_14_out, not_15_out, not_16_out,
       not_17_out, not_18_out, not_19_out, not_20_out, not_21_out, not_22_out, not_23_out, not_24_out,
       not_25_out, not_26_out, not_27_out, not_28_out;

  not not_1 (not_1_out, CPd);
  not not_2 (not_2_out, CPd);
  not not_3 (not_3_out, X1);
  not not_4 (not_4_out, CPu);
  not not_5 (not_5_out, X3);
  not not_6 (not_6_out, X2);
  not not_7 (not_7_out, X1);
  not not_8 (not_8_out, X3);
  not not_9 (not_9_out, X2);
  not not_10 (not_10_out, CPd);
  not not_11 (not_11_out, X1);
  not not_12 (not_12_out, CPu);
  not not_13 (not_13_out, CPd);
  not not_14 (not_14_out, X2);
  not not_15 (not_15_out, X1);
  not not_16 (not_16_out, X2);
  not not_17 (not_17_out, X1);
  not not_18 (not_18_out, X2);
  not not_19 (not_19_out, CPu);
  not not_20 (not_20_out, CPd);
  not not_21 (not_21_out, X1);
  not not_22 (not_22_out, X1);
  not not_23 (not_23_out, X1);
  not not_24 (not_24_out, X1);
  not not_25 (not_25_out, X4);
  not not_26 (not_26_out, X3);
  not not_27 (not_27_out, X2);
  not not_28 (not_28_out, X1);
  and and_1 (and_1_out, not_1_out, X4);
  and and_2 (and_2_out, X4, X1);
  and and_3 (and_3_out, X4, X2);
  and and_4 (and_4_out, X4, X3);
  and and_5 (and_5_out, CPu, X3, X2, X1);
  and and_6 (and_6_out, not_2_out, X3, not_3_out);
  and and_7 (and_7_out, not_4_out, X3, X1);
  and and_8 (and_8_out, X4, X3, X2);
  and and_9 (and_9_out, CPd, X3, X2);
  and and_10 (and_10_out, CPd, X4, not_5_out, not_6_out, not_7_out);
  and and_11 (and_11_out, CPu, not_8_out, X2, X1);
  and and_12 (and_12_out, CPu, X3, not_9_out);
  and and_13 (and_13_out, not_10_out, X2, not_11_out);
  and and_14 (and_14_out, not_12_out, X2, X1);
  and and_15 (and_15_out, not_13_out, X4, X3, X2);
  and and_16 (and_16_out, CPd, X3, not_14_out, not_15_out);
  and and_17 (and_17_out, CPd, X4, not_16_out, not_17_out);
  and and_18 (and_18_out, CPu, not_18_out, X1);
  and and_19 (and_19_out, not_19_out, not_20_out, X1);
  and and_20 (and_20_out, CPd, X2, not_21_out);
  and and_21 (and_21_out, CPd, X3, not_22_out);
  and and_22 (and_22_out, CPd, X4, not_23_out);
  and and_23 (and_23_out, CPu, not_24_out);
  and and_24 (and_24_out, CPu, X4, X3, X2);
  and and_25 (and_25_out, CPd, not_25_out, not_26_out, not_27_out, not_28_out);
  and and_26 (and_26_out, CPu, X4, X3, X2, X1);
  or or_1 (Y4, and_1_out, and_2_out, and_3_out, and_4_out, and_5_out);
  or or_2 (Y3, and_6_out, and_7_out, and_8_out, and_9_out, and_10_out, and_11_out, and_12_out);
  or or_3 (Y2, and_13_out, and_14_out, and_15_out, and_16_out, and_17_out, and_18_out);
  or or_4 (Y1, and_19_out, and_20_out, and_21_out, and_22_out, and_23_out, and_24_out);
  or or_5 (Z, and_25_out, and_26_out);
endmodule

module \_4位二进制转8421码  (
  input  X3,
  input  X2,
  input  X1,
  input  X0,
  output Y7,
  output Y6,
  output Y5,
  output Y4,
  output Y3,
  output Y2,
  output Y1,
  output Y0
);

  wire and_1_out, and_2_out, and_4_out, and_5_out, and_6_out, and_7_out, not_1_out, not_2_out, not_3_out,
       not_4_out, not_5_out;

  and and_1 (and_1_out, X3, X1);
  and and_2 (and_2_out, X3, X2);
  not not_1 (not_1_out, X2);
  and and_3 (Y3, X3, not_1_out, not_2_out);
  not not_2 (not_2_out, X1);
  not not_3 (not_3_out, X3);
  and and_4 (and_4_out, not_3_out, X2);
  and and_5 (and_5_out, X2, X1);
  not not_4 (not_4_out, X3);
  and and_6 (and_6_out, not_4_out, X1);
  and and_7 (and_7_out, X3, X2, not_5_out);
  not not_5 (not_5_out, X1);
  or or_1 (Y4, and_1_out, and_2_out);
  or or_2 (Y2, and_4_out, and_5_out);
  or or_3 (Y1, and_6_out, and_7_out);

  assign Y0 = X0;
  assign Y5 = 1'b0;
  assign Y6 = 1'b0;
  assign Y7 = 1'b0;
endmodule

module \_7段译码器  (
  input  D,
  input  C,
  input  B,
  input  A,
  output a_2,
  output b_2,
  output c_2,
  output d_2,
  output e,
  output f,
  output g
);

  wire and_1_out, and_2_out, and_3_out, and_4_out, and_5_out, and_6_out, and_7_out, and_8_out, and_9_out,
       and_10_out, and_11_out, and_12_out, and_13_out, and_14_out, and_15_out, and_16_out, not_1_out,
       not_2_out, not_3_out, not_4_out, not_5_out, not_6_out, not_7_out, not_8_out, not_9_out, not_10_out,
       not_11_out, not_12_out, not_13_out, not_14_out, not_15_out, not_16_out, not_17_out, not_18_out,
       not_19_out, not_20_out, not_21_out;

  not not_1 (not_1_out, C);
  and and_1 (and_1_out, not_1_out, not_2_out);
  not not_2 (not_2_out, A);
  and and_2 (and_2_out, C, A);
  not not_3 (not_3_out, C);
  not not_4 (not_4_out, B);
  and and_3 (and_3_out, not_4_out, not_5_out);
  not not_5 (not_5_out, A);
  and and_4 (and_4_out, B, A);
  not not_6 (not_6_out, B);
  or or_1 (c_2, not_6_out, A, C);
  not not_7 (not_7_out, C);
  and and_5 (and_5_out, not_7_out, not_8_out);
  not not_8 (not_8_out, A);
  not not_9 (not_9_out, C);
  and and_6 (and_6_out, not_9_out, B);
  and and_7 (and_7_out, B, not_10_out);
  not not_10 (not_10_out, A);
  and and_8 (and_8_out, C, not_11_out, A);
  not not_11 (not_11_out, B);
  not not_12 (not_12_out, C);
  and and_9 (and_9_out, not_12_out, not_13_out);
  not not_13 (not_13_out, A);
  and and_10 (and_10_out, B, not_14_out);
  not not_14 (not_14_out, A);
  not not_15 (not_15_out, B);
  and and_11 (and_11_out, not_15_out, not_16_out);
  not not_16 (not_16_out, A);
  and and_12 (and_12_out, C, not_17_out);
  not not_17 (not_17_out, B);
  and and_13 (and_13_out, C, not_18_out);
  not not_18 (not_18_out, A);
  not not_19 (not_19_out, C);
  and and_14 (and_14_out, not_19_out, B);
  and and_15 (and_15_out, B, not_20_out);
  not not_20 (not_20_out, A);
  and and_16 (and_16_out, C, not_21_out);
  not not_21 (not_21_out, B);
  or or_2 (a_2, and_1_out, B, and_2_out, D);
  or or_3 (b_2, not_3_out, and_3_out, and_4_out);
  or or_4 (d_2, and_5_out, and_6_out, and_7_out, and_8_out, D);
  or or_5 (e, and_9_out, and_10_out);
  or or_6 (f, and_11_out, and_12_out, and_13_out, D);
  or or_7 (g, and_14_out, and_15_out, and_16_out, D);
endmodule
